// Logisim project cpu21-riscv-基于RISC-V32的简易迷宫游戏.circ as structural Verilog: 28 circuits, main circuit ◇单周期RISC-V
module \单周期RISC_V  (
  input  IR1,
  input  IR2,
  input  IR3,
  output RegWrite,
  output MemWrite,
  output [31:0] PC,
  output [31:0] IR,
  output [31:0] RDin,
  output [31:0] MDin,
  output [31:0] LedData
);

  wire alu_1_equal, alu_1_out_4, and_2_out, and_3_out, and_4_out, and_5_out, Beq, Bgeu, Bne, \B型 , CLK,
       clock_1_out, comparator_1_eq, comparator_2_eq, comparator_2_lt, d_ff_2_q, ecall, Go, halt, IR1_t,
       IR2_t, IR3_t, IRA, IRB, IRC, JAL, JALR, LBU, MemToReg, nand_1_out, not_1_out, not_2_out, or_5_out,
       RST, URET, W1, W2, W3, \单周期硬布线控制器_1_alu_src , \单周期硬布线控制器_1_s_type ;
  wire [1:0] priority_encoder_1_out, priority_encoder_2_out;
  wire [3:0] \单周期硬布线控制器_1_alu_op ;
  wire [4:0] multiplexer_2_out, multiplexer_3_out;
  wire [7:0] multiplexer_6_out;
  wire [11:0] multiplexer_4_out;
  wire [12:0] CNT_num;
  wire [15:0] \总周期数 ;
  wire [31:0] adder_1_out, adder_2_out, adder_3_out, ALU_result, and_1_out, bit_extender_1_out,
       bit_extender_2_out, bit_extender_3_out, bit_extender_4_out, multiplexer_1_out, multiplexer_5_out, R1,
       ram_1_data, shifter_1_out, shifter_2_out;

  Button \u_继续运行  (.out(Go));
  Button _1 (.out(IRA));
  Button _2 (.out(IRB));
  Button _3 (.out(IRC));
  LED #(.active("true")) led_1 (.in(W1));
  LED #(.active("true")) led_2 (.in(W2));
  LED #(.active("true")) led_3 (.in(W3));
  Priority_Encoder #(.select(2), .disabled("Z")) priority_encoder_1 (
    .in0(1'b1), .in1(\B型 ), .in2(JAL), .in3(JALR), .out(priority_encoder_1_out));  // open: gs, en_out, en_in
  Multiplexer #(.select(2), .width(32), .disabled("Z"), .enable("false")) multiplexer_1 (
    .in0(adder_1_out), .in1(adder_2_out), .in2(adder_3_out), .in3(and_1_out), .out(multiplexer_1_out),
    .sel(priority_encoder_1_out));
  assign and_1_out = 32'hfffffffe & ALU_result;  // AND_Gate and_1, 32 bits wide
  Hex_Digit_Display hex_digit_display_1 (.value(LedData[31:28]));  // open: dp
  Register #(.width(32), .trigger("rising"), .Select("low")) u_PC (
    .D(multiplexer_1_out), .en(not_1_out), .Q(PC), .clk(CLK), .clr(RST));
  not not_1 (not_1_out, halt);
  not not_2 (not_2_out, halt);
  Hex_Digit_Display hex_digit_display_2 (.value(LedData[27:24]));  // open: dp
  Hex_Digit_Display hex_digit_display_3 (.value(LedData[23:20]));  // open: dp
  Counter #(.width(16), .max('hffff), .ongoal("wrap"), .trigger("rising"), .behavior("new")) counter_1 (
    .count(not_2_out), .Q(\总周期数 ), .clk(CLK));  // open: load, D, carry, clr, preset, down
  Comparator #(.width(32), .mode("unsigned")) comparator_1 (.a(R1), .b(32'ha), .eq(comparator_1_eq));  // open: gt, lt
  Hex_Digit_Display hex_digit_display_4 (.value(LedData[15:12]));  // open: dp
  Hex_Digit_Display hex_digit_display_5 (.value(LedData[19:16]));  // open: dp
  // RiscV_Probe riscv_probe_1: pin names not known; wires that end beside it: IR
  and and_2 (and_2_out, ~comparator_1_eq, ecall);  // AND_Gate
  Hex_Digit_Display hex_digit_display_6 (.value(LedData[11:8]));  // open: dp
  Hex_Digit_Display hex_digit_display_7 (.value(LedData[7:4]));  // open: dp
  // Probe on \总周期数 
  ROM #(.addrWidth(10), .dataWidth(32), .Select("high")) rom_1 (.addr(PC[11:2]), .data(IR));
  D_Flip_Flop #(.trigger("rising"), .Pre_Clr_Positions("ABOVE_BELOW"), .NegatePresetClear("false"), .enable("true"), .NewFFLayout("true")) d_ff_1 (
    .clk(comparator_1_eq), .D(1'b1), .Q(halt), .en(ecall), .reset(Go));  // open: Qn, preset
  Register #(.width(32), .trigger("rising"), .Select("low")) register_1 (
    .D(MDin), .en(and_2_out), .Q(LedData), .clk(CLK));  // open: clr
  Hex_Digit_Display hex_digit_display_8 (.value(LedData[3:0]));  // open: dp
  \单周期硬布线控制器  \u_单周期硬布线控制器_1  (
    .Funct({IR[30], IR[25], IR[14:12]}), .OP(IR[6:2]), .ALU_OP(\单周期硬布线控制器_1_alu_op ), .MemToReg(MemToReg),
    .MemWrite(MemWrite), .ALU_SRC(\单周期硬布线控制器_1_alu_src ), .RegWrite(RegWrite), .ecall(ecall),
    .S_type(\单周期硬布线控制器_1_s_type ), .Jalr(JALR), .Beq(Beq), .JAL(JAL), .Bne(Bne), .in_3(IR[21]), .uret(URET),
    .LBU(LBU), .BGEU(Bgeu));  // open: CSRRSI, CSEECI, rs1_use, rs2_use
  Multiplexer #(.select(1), .width(5), .disabled("Z"), .enable("false")) multiplexer_2 (
    .in0(IR[19:15]), .in1(5'b10001), .out(multiplexer_2_out), .sel(ecall));
  Multiplexer #(.select(1), .width(5), .disabled("Z"), .enable("false")) multiplexer_3 (
    .in0(IR[24:20]), .in1(5'b01010), .out(multiplexer_3_out), .sel(ecall));
  assign bit_extender_1_out = {{20{IR[31]}}, {IR[31], IR[7], IR[30:25], IR[11:8]}};  // Bit_Extender bit_extender_1
  assign bit_extender_2_out = {{12{IR[31]}}, {IR[31], IR[19:12], IR[20], IR[30:21]}};  // Bit_Extender bit_extender_2
  or or_1 (IR1_t, IR1, IRA);
  Multiplexer #(.select(1), .width(12), .disabled("Z"), .enable("false")) multiplexer_4 (
    .in0(IR[31:20]), .in1({IR[31:25], IR[11:7]}), .out(multiplexer_4_out), .sel(\单周期硬布线控制器_1_s_type ));
  assign bit_extender_3_out = {{20{multiplexer_4_out[11]}}, multiplexer_4_out};  // Bit_Extender bit_extender_3
  Shifter #(.width(32), .shift("ll")) shifter_1 (.in(bit_extender_1_out), .\dist (5'b00001), .out(shifter_1_out));
  Shifter #(.width(32), .shift("ll")) shifter_2 (.in(bit_extender_2_out), .\dist (5'b00001), .out(shifter_2_out));
  // Probe on bit_extender_2_out
  or or_2 (IR2_t, IR2, IRB);
  Regifile regifile_1 (
    .Din(RDin), .Clk(CLK), .R1(R1), .R2(MDin), .WE(RegWrite), .W_num(IR[11:7]), .R1_num(multiplexer_2_out),
    .R2_num(multiplexer_3_out));
  Adder #(.width(32)) adder_1 (.a(PC), .b(32'h4), .out(adder_1_out));  // open: cin, cout
  Adder #(.width(32)) adder_2 (.a(shifter_1_out), .b(PC), .out(adder_2_out));  // open: cin, cout
  Adder #(.width(32)) adder_3 (.a(shifter_2_out), .b(PC), .out(adder_3_out));  // open: cin, cout
  Multiplexer #(.select(1), .width(32), .disabled("Z"), .enable("false")) multiplexer_5 (
    .in0(MDin), .in1(bit_extender_3_out), .out(multiplexer_5_out), .sel(\单周期硬布线控制器_1_alu_src ));
  // Probe on adder_3_out
  or or_3 (IR3_t, IR3, IRC);
  and and_3 (and_3_out, Beq, alu_1_equal);
  and and_4 (and_4_out, Bne, ~alu_1_equal);  // AND_Gate
  and and_5 (and_5_out, Bgeu, alu_1_out_4);
  ALU alu_1 (
    .X(R1), .Y(multiplexer_5_out), .AluOP(\单周期硬布线控制器_1_alu_op ), .Equal(alu_1_equal), .Result(ALU_result),
    .out_4(alu_1_out_4));  // open: Result_2, out_6
  or or_4 (\B型 , and_3_out, and_4_out, and_5_out);
  RAM #(.addrWidth(10), .dataWidth(32), .bus("separate"), .Select("high")) ram_1 (
    .addr(ALU_result[11:2]), .din(MDin), .data(ram_1_data), .str(MemWrite), .sel(1'b1), .clk(CLK), .ld(1'b1),
    .clr(RST));
  Multiplexer #(.select(2), .width(8), .disabled("Z"), .enable("false")) multiplexer_6 (
    .in0(ram_1_data[7:0]), .in1(ram_1_data[15:8]), .in2(ram_1_data[23:16]), .in3(ram_1_data[31:24]),
    .out(multiplexer_6_out), .sel(ALU_result[1:0]));
  assign bit_extender_4_out = {{24{1'b0}}, multiplexer_6_out};  // Bit_Extender bit_extender_4
  or or_5 (or_5_out, JAL, JALR);
  Priority_Encoder #(.select(2), .disabled("Z")) priority_encoder_2 (
    .in0(1'b1), .in1(MemToReg), .in2(LBU), .in3(or_5_out), .out(priority_encoder_2_out));  // open: gs, en_out, en_in
  Multiplexer #(.select(2), .width(32), .disabled("Z"), .enable("false")) multiplexer_7 (
    .in0(ALU_result), .in1(ram_1_data), .in2(bit_extender_4_out), .in3(adder_1_out), .out(RDin),
    .sel(priority_encoder_2_out));
  D_Flip_Flop #(.trigger("high"), .Pre_Clr_Positions("LEGACY"), .NegatePresetClear("false"), .enable("true"), .NewFFLayout("false")) d_ff_2 (.Q(d_ff_2_q));  // open: clk, D, Qn, preset, en, reset
  // Probe on 13'h609
  Comparator #(.width(13), .mode("twosComplement")) comparator_2 (
    .a(CNT_num), .b(13'h609), .eq(comparator_2_eq), .lt(comparator_2_lt));  // open: gt
  Clock #(.highDuration(1), .lowDuration(1)) clock_1 (.out(clock_1_out));
  Counter #(.width(13), .max('h1fff), .ongoal("stay"), .trigger("rising"), .behavior("old")) counter_2 (
    .count(comparator_2_lt), .Q(CNT_num), .clk(clock_1_out));  // open: load, D, carry, clr, preset
  nand nand_1 (nand_1_out, d_ff_2_q, comparator_2_eq);
  assign CLK = nand_1_out ? clock_1_out : 1'bz;  // Controlled_Buffer controlled_buffer_1
  Pull_Resistor #(.pull(1)) pull_resistor_1 (.node(CLK));

  // Notes on the sheet:
  //   中断源
  //   中断等待指示
  //   数码管输出应该用寄存器锁存，否则显示数据只能一闪而过
  //   这里设置为10是为了过头歌
  //   和任务书中的要求确实有出入
  //   数码管输出
  //   指令探针
  //   指令存储器
  //   指令字
  //   contents of rom_1 (hex, n*v repeats v):
  //   100493 100006f 100493 200913 300993 100006f 100493 200913 300993 100006f 100493 200913 300993
  //   100006f 100493 200913 300993 3d8000ef 100413 100493 1f49493 900533 2200893 73 24d493 48463 fedff06f
  //   900533 2200893 73 100493 249493 900533 2200893 73 48463 fedff06f 100493 1f49493 900533 2200893 73
  //   4034d493 900533 2200893 73 4044d493 900533 2200893 73 4044d493 900533 2200893 73 4044d493 900533
  //   2200893 73 4044d493 900533 2200893 73 4044d493 900533 2200893 73 4044d493 900533 2200893 73 4044d493
  //   900533 2200893 73 100413 1f41993 41f9d993 433 c00913 300b13 140413 f47413 800293 100313 499993
  //   89e9b3 1300533 2200893 73 406282b3 fe0294e3 140413 f00f93 1f47433 1c41413 800293 100313 49d993
  //   89e9b3 1300533 2200893 73 406282b3 fe0294e3 1c45413 406b0b33 b0463 f95ff06f 2b3 fff2c293 829293
  //   ff2e293 500533 2200893 73 fff00413 493 84a023 140413 448493 84a023 140413 448493 84a023 140413
  //   448493 84a023 140413 448493 84a023 140413 448493 84a023 140413 448493 84a023 140413 448493 84a023
  //   140413 448493 84a023 140413 448493 84a023 140413 448493 84a023 140413 448493 84a023 140413 448493
  //   84a023 140413 448493 84a023 140413 448493 84a023 140413 448493 84a023 140413 448493 140413 433
  //   3c00493 42983 4aa03 149a2b3 28663 134a023 1442023 ffc48493 fe9412e3 800533 2200893 73 440413 3c00493
  //   fc9416e3 a00893 73 100293 300313 800493 849493 7648493 900533 2200893 73 800e13 5494b3 6494b3 900533
  //   2200893 73 fffe0e13 fe0e14e3 a00893 73 100293 300313 800493 849493 7648493 1449493 900533 2200893 73
  //   800e13 4054d4b3 4064d4b3 900533 2200893 73 fffe0e13 fe0e14e3 a00893 73 313 1000e13 8400493 849493
  //   8348493 400913 891913 490913 849493 8248493 849493 8148493 891913 490913 891913 490913 932023
  //   12484b3 430313 fffe0e13 fe0e18e3 2000e13 313 34483 900533 2200893 73 130313 fffe0e13 fe0e14e3 a00893
  //   73 f00493 100913 409909b3 900533 2200893 73 fff48493 ff29f6e3 a00893 73 413 140413 800533 2200893 73
  //   240413 800533 2200893 73 340413 800533 2200893 73 440413 800533 2200893 73 540413 800533 2200893 73
  //   640413 800533 2200893 73 740413 800533 2200893 73 840413 800533 2200893 2200893 73 8067
  //   JAL
  //   JALR
  //   URET
  //   LBU
  //   $a7
  //   $a0
  //   I型（上）/sw（下）
  //   B型指令立即数
  //   J型指令立即数
  //   注意JALR是I型指令
  //   Beq
  //   Bgeu
  //   Bne
  //   MemToReg
  //   MemWrite
  //   AluOP
  //   AluSrcB
  //   RegWrite
  //   S_Type
  //   AluSrcB为1代表是lw/sw/立即数指令
  //   只有sw指令会往存储器存数据
  //   数据存储器
  //   为方便自动评测，需要输出PC，IR，寄存器堆写如数据RDin
  //   RAM写使能MemWrite、RAM写入数据MDin等信号
  //   LBU无符号加载字节指令
  //   控制位
  //   暂停节拍，不能为0
  //   戳工具置1进入计数暂停模式，ctrl+k时钟自动运行到对应节拍暂停
  //   ctrl+k关闭时钟连续运行，将控制位置零，进入单步调试模式调试
  //   用这个时钟源需要去掉电路中的其他时钟源
  //   可计数暂停的时钟源
endmodule

// 单周期硬布线控制器
module \单周期硬布线控制器  (
  input  [4:0] OP,
  input  [4:0] Funct,
  input  in_3,
  output [3:0] ALU_OP,
  output uret,
  output MemToReg,
  output ecall,
  output MemWrite,
  output rs1_use,
  output rs2_use,
  output ALU_SRC,
  output RegWrite,
  output S_type,
  output Beq,
  output Bne,
  output Jalr,
  output JAL,
  output LBU,
  output BGEU,
  output CSRRSI,
  output CSEECI
);

  wire \控制信号自动生成_1_ecall ;

  \运算控制器自动生成  \u_运算控制器自动生成_1  (
    .OP2(OP[0]), .OP3(OP[1]), .OP4(OP[2]), .OP5(OP[3]), .OP6(OP[4]), .F12(Funct[0]), .F13(Funct[1]),
    .F14(Funct[2]), .F25(Funct[3]), .F30(Funct[4]), .S0(ALU_OP[0]), .S1(ALU_OP[1]), .S2(ALU_OP[2]),
    .S3(ALU_OP[3]));
  \控制信号自动生成  \u_控制信号自动生成_1  (
    .OP2(OP[0]), .OP3(OP[1]), .OP4(OP[2]), .OP5(OP[3]), .MemToReg(MemToReg), .OP6(OP[4]), .F12(Funct[0]),
    .F13(Funct[1]), .F14(Funct[2]), .F25(Funct[3]), .F30(Funct[4]), .MemWrite(MemWrite), .rs1_use(rs1_use),
    .rs2_use(rs2_use), .ALU_SRC(ALU_SRC), .RegWrite(RegWrite), .ecall(\控制信号自动生成_1_ecall ), .S_Type(S_type),
    .BEQ(Beq), .BNE(Bne), .JALR(Jalr), .JAL(JAL), .LBU(LBU), .BGEU(BGEU), .CSRRSI(CSRRSI), .CSEECI(CSEECI));
  and and_1 (uret, in_3, \控制信号自动生成_1_ecall );
  and and_2 (ecall, ~in_3, \控制信号自动生成_1_ecall );  // AND_Gate

  // Other names for the same wires on the sheet: IR21 = in_3; OP_CODE[4:0] = OP

  // Notes on the sheet:
  //   运算器控制器，根据指令生成运算器功能选择信号
endmodule

// 运算器控制器
module \运算控制器自动生成  (
  input  OP2,
  input  OP3,
  input  OP4,
  input  OP5,
  input  OP6,
  input  F12,
  input  F13,
  input  F14,
  input  F25,
  input  F30,
  output S0,
  output S1,
  output S2,
  output S3
);

  wire and_1_out, and_2_out, and_3_out, and_4_out, and_5_out, and_6_out, and_7_out, and_8_out, and_9_out,
       and_10_out, and_11_out, and_12_out, and_13_out, and_14_out, and_15_out, and_16_out, and_17_out,
       and_18_out, and_19_out, and_20_out, and_21_out, and_22_out, and_23_out, and_24_out, and_25_out,
       and_26_out, and_27_out, and_28_out, and_29_out, and_30_out, and_31_out, and_32_out, and_33_out,
       and_34_out, and_35_out, not_1_out, not_2_out, not_3_out, not_4_out, not_5_out, not_6_out, not_7_out,
       not_8_out, not_9_out, not_10_out, not_11_out, not_12_out, not_13_out, not_14_out, not_15_out,
       not_16_out, not_17_out, not_18_out, not_19_out, not_20_out, not_21_out, not_22_out, not_23_out,
       not_24_out, not_25_out, not_26_out, not_27_out, not_28_out, not_29_out, not_30_out, not_31_out,
       not_32_out, not_33_out, not_34_out, not_35_out, not_36_out, not_37_out, not_38_out, not_39_out,
       not_40_out, not_41_out, not_42_out, not_43_out, not_44_out, not_45_out, not_46_out, not_47_out,
       not_48_out, not_49_out, not_50_out, not_51_out, not_52_out, not_53_out, not_54_out, not_55_out,
       not_56_out, not_57_out, not_58_out, not_59_out, not_60_out, not_61_out, not_62_out, not_63_out,
       not_64_out, not_65_out, not_66_out, not_67_out, not_68_out, not_69_out, not_70_out, not_71_out,
       not_72_out, not_73_out, not_74_out, not_75_out, not_76_out, not_77_out, not_78_out, not_79_out,
       not_80_out, not_81_out, not_82_out, not_83_out, not_84_out, not_85_out, not_86_out, not_87_out,
       not_88_out, not_89_out, not_90_out, not_91_out, not_92_out, not_93_out, not_94_out, not_95_out,
       not_96_out, not_97_out, not_98_out, not_99_out, not_100_out, not_101_out, not_102_out, not_103_out,
       not_104_out, not_105_out, not_106_out, not_107_out, not_108_out, not_109_out, not_110_out,
       not_111_out, not_112_out, not_113_out, not_114_out, not_115_out, not_116_out, not_117_out,
       not_118_out, not_119_out, not_120_out, not_121_out, not_122_out, not_123_out, not_124_out,
       not_125_out, not_126_out, not_127_out, not_128_out, not_129_out, not_130_out, not_131_out,
       not_132_out, not_133_out, not_134_out, not_135_out, not_136_out, not_137_out, not_138_out,
       not_139_out, not_140_out, not_141_out, not_142_out, not_143_out, not_144_out, not_145_out,
       not_146_out, not_147_out, not_148_out, not_149_out, not_150_out, not_151_out, not_152_out,
       not_153_out, not_154_out, not_155_out, not_156_out, not_157_out, not_158_out, not_159_out,
       not_160_out, not_161_out, not_162_out, not_163_out, not_164_out, not_165_out, not_166_out,
       not_167_out, not_168_out, not_169_out, not_170_out, not_171_out, not_172_out, not_173_out,
       not_174_out, not_175_out, not_176_out, not_177_out, not_178_out, not_179_out, not_180_out,
       not_181_out, not_182_out, not_183_out, not_184_out, not_185_out, not_186_out, not_187_out,
       not_188_out, not_189_out, not_190_out, not_191_out, not_192_out, not_193_out, not_194_out,
       not_195_out, not_196_out, not_197_out, not_198_out, not_199_out, not_200_out, not_201_out,
       not_202_out, not_203_out, not_204_out, not_205_out, not_206_out, not_207_out, not_208_out, not_209_out;

  not not_1 (not_1_out, F30);
  not not_2 (not_2_out, F25);
  not not_3 (not_3_out, F14);
  not not_4 (not_4_out, F13);
  not not_5 (not_5_out, F12);
  not not_6 (not_6_out, OP6);
  not not_7 (not_7_out, OP3);
  not not_8 (not_8_out, OP2);
  not not_9 (not_9_out, F30);
  not not_10 (not_10_out, F25);
  not not_11 (not_11_out, OP6);
  not not_12 (not_12_out, OP3);
  not not_13 (not_13_out, OP2);
  not not_14 (not_14_out, F30);
  not not_15 (not_15_out, F25);
  not not_16 (not_16_out, F14);
  not not_17 (not_17_out, F12);
  not not_18 (not_18_out, OP6);
  not not_19 (not_19_out, OP3);
  not not_20 (not_20_out, OP2);
  not not_21 (not_21_out, F14);
  not not_22 (not_22_out, F13);
  not not_23 (not_23_out, F12);
  not not_24 (not_24_out, OP6);
  not not_25 (not_25_out, OP5);
  not not_26 (not_26_out, OP3);
  not not_27 (not_27_out, OP2);
  not not_28 (not_28_out, OP6);
  not not_29 (not_29_out, OP5);
  not not_30 (not_30_out, OP3);
  not not_31 (not_31_out, OP2);
  not not_32 (not_32_out, F13);
  not not_33 (not_33_out, F12);
  not not_34 (not_34_out, OP6);
  not not_35 (not_35_out, OP5);
  not not_36 (not_36_out, OP3);
  not not_37 (not_37_out, OP2);
  not not_38 (not_38_out, F14);
  not not_39 (not_39_out, F12);
  not not_40 (not_40_out, OP6);
  not not_41 (not_41_out, OP5);
  not not_42 (not_42_out, OP3);
  not not_43 (not_43_out, OP2);
  not not_44 (not_44_out, F25);
  not not_45 (not_45_out, F13);
  not not_46 (not_46_out, OP6);
  not not_47 (not_47_out, OP5);
  not not_48 (not_48_out, OP3);
  not not_49 (not_49_out, OP2);
  not not_50 (not_50_out, F14);
  not not_51 (not_51_out, F12);
  not not_52 (not_52_out, OP6);
  not not_53 (not_53_out, OP5);
  not not_54 (not_54_out, OP4);
  not not_55 (not_55_out, OP3);
  not not_56 (not_56_out, OP2);
  not not_57 (not_57_out, F14);
  not not_58 (not_58_out, F12);
  not not_59 (not_59_out, OP6);
  not not_60 (not_60_out, OP4);
  not not_61 (not_61_out, OP3);
  not not_62 (not_62_out, OP2);
  not not_63 (not_63_out, F25);
  not not_64 (not_64_out, F13);
  not not_65 (not_65_out, OP6);
  not not_66 (not_66_out, OP3);
  not not_67 (not_67_out, OP2);
  not not_68 (not_68_out, F13);
  not not_69 (not_69_out, F12);
  not not_70 (not_70_out, OP6);
  not not_71 (not_71_out, OP5);
  not not_72 (not_72_out, OP4);
  not not_73 (not_73_out, OP3);
  not not_74 (not_74_out, OP2);
  not not_75 (not_75_out, F25);
  not not_76 (not_76_out, F14);
  not not_77 (not_77_out, F13);
  not not_78 (not_78_out, F12);
  not not_79 (not_79_out, OP6);
  not not_80 (not_80_out, OP3);
  not not_81 (not_81_out, OP2);
  not not_82 (not_82_out, F30);
  not not_83 (not_83_out, F25);
  not not_84 (not_84_out, OP6);
  not not_85 (not_85_out, OP3);
  not not_86 (not_86_out, OP2);
  not not_87 (not_87_out, F30);
  not not_88 (not_88_out, F25);
  not not_89 (not_89_out, F14);
  not not_90 (not_90_out, F12);
  not not_91 (not_91_out, OP6);
  not not_92 (not_92_out, OP3);
  not not_93 (not_93_out, OP2);
  not not_94 (not_94_out, OP6);
  not not_95 (not_95_out, OP5);
  not not_96 (not_96_out, OP3);
  not not_97 (not_97_out, OP2);
  not not_98 (not_98_out, F14);
  not not_99 (not_99_out, F12);
  not not_100 (not_100_out, OP6);
  not not_101 (not_101_out, OP5);
  not not_102 (not_102_out, OP3);
  not not_103 (not_103_out, OP2);
  not not_104 (not_104_out, F30);
  not not_105 (not_105_out, F25);
  not not_106 (not_106_out, F13);
  not not_107 (not_107_out, OP6);
  not not_108 (not_108_out, OP5);
  not not_109 (not_109_out, OP3);
  not not_110 (not_110_out, OP2);
  not not_111 (not_111_out, F30);
  not not_112 (not_112_out, F25);
  not not_113 (not_113_out, F14);
  not not_114 (not_114_out, F13);
  not not_115 (not_115_out, F12);
  not not_116 (not_116_out, OP6);
  not not_117 (not_117_out, OP3);
  not not_118 (not_118_out, OP2);
  not not_119 (not_119_out, F25);
  not not_120 (not_120_out, F14);
  not not_121 (not_121_out, F13);
  not not_122 (not_122_out, F12);
  not not_123 (not_123_out, OP6);
  not not_124 (not_124_out, OP3);
  not not_125 (not_125_out, OP2);
  not not_126 (not_126_out, F30);
  not not_127 (not_127_out, F25);
  not not_128 (not_128_out, OP6);
  not not_129 (not_129_out, OP3);
  not not_130 (not_130_out, OP2);
  not not_131 (not_131_out, F30);
  not not_132 (not_132_out, F25);
  not not_133 (not_133_out, F14);
  not not_134 (not_134_out, OP6);
  not not_135 (not_135_out, OP3);
  not not_136 (not_136_out, OP2);
  not not_137 (not_137_out, F14);
  not not_138 (not_138_out, F13);
  not not_139 (not_139_out, F12);
  not not_140 (not_140_out, OP6);
  not not_141 (not_141_out, OP5);
  not not_142 (not_142_out, OP3);
  not not_143 (not_143_out, OP2);
  not not_144 (not_144_out, OP6);
  not not_145 (not_145_out, OP5);
  not not_146 (not_146_out, OP3);
  not not_147 (not_147_out, OP2);
  not not_148 (not_148_out, F14);
  not not_149 (not_149_out, F12);
  not not_150 (not_150_out, OP6);
  not not_151 (not_151_out, OP5);
  not not_152 (not_152_out, OP4);
  not not_153 (not_153_out, OP3);
  not not_154 (not_154_out, OP2);
  not not_155 (not_155_out, F14);
  not not_156 (not_156_out, F12);
  not not_157 (not_157_out, OP6);
  not not_158 (not_158_out, OP4);
  not not_159 (not_159_out, OP3);
  not not_160 (not_160_out, OP2);
  not not_161 (not_161_out, F13);
  not not_162 (not_162_out, F12);
  not not_163 (not_163_out, OP6);
  not not_164 (not_164_out, OP5);
  not not_165 (not_165_out, OP4);
  not not_166 (not_166_out, OP3);
  not not_167 (not_167_out, OP2);
  not not_168 (not_168_out, OP4);
  not not_169 (not_169_out, OP3);
  not not_170 (not_170_out, OP2);
  not not_171 (not_171_out, F30);
  not not_172 (not_172_out, F25);
  not not_173 (not_173_out, F12);
  not not_174 (not_174_out, OP6);
  not not_175 (not_175_out, OP3);
  not not_176 (not_176_out, OP2);
  not not_177 (not_177_out, F30);
  not not_178 (not_178_out, F25);
  not not_179 (not_179_out, F14);
  not not_180 (not_180_out, F12);
  not not_181 (not_181_out, OP6);
  not not_182 (not_182_out, OP3);
  not not_183 (not_183_out, OP2);
  not not_184 (not_184_out, F30);
  not not_185 (not_185_out, F25);
  not not_186 (not_186_out, F14);
  not not_187 (not_187_out, OP6);
  not not_188 (not_188_out, OP3);
  not not_189 (not_189_out, OP2);
  not not_190 (not_190_out, F12);
  not not_191 (not_191_out, OP6);
  not not_192 (not_192_out, OP5);
  not not_193 (not_193_out, OP3);
  not not_194 (not_194_out, OP2);
  not not_195 (not_195_out, F13);
  not not_196 (not_196_out, F12);
  not not_197 (not_197_out, OP6);
  not not_198 (not_198_out, OP5);
  not not_199 (not_199_out, OP3);
  not not_200 (not_200_out, OP2);
  not not_201 (not_201_out, F14);
  not not_202 (not_202_out, F12);
  not not_203 (not_203_out, OP6);
  not not_204 (not_204_out, OP5);
  not not_205 (not_205_out, OP3);
  not not_206 (not_206_out, OP2);
  not not_207 (not_207_out, OP4);
  not not_208 (not_208_out, OP3);
  not not_209 (not_209_out, OP2);
  and and_1 (and_1_out, not_1_out, not_2_out, not_3_out, not_4_out, not_5_out, not_6_out, OP5, OP4, not_7_out, not_8_out);
  and and_2 (and_2_out, not_9_out, not_10_out, F14, F13, F12, not_11_out, OP5, OP4, not_12_out, not_13_out);
  and and_3 (and_3_out, not_14_out, not_15_out, not_16_out, F13, not_17_out, not_18_out, OP5, OP4, not_19_out, not_20_out);
  and and_4 (and_4_out, not_21_out, not_22_out, not_23_out, not_24_out, not_25_out, OP4, not_26_out, not_27_out);
  and and_5 (and_5_out, F14, F13, F12, not_28_out, not_29_out, OP4, not_30_out, not_31_out);
  and and_6 (and_6_out, F14, not_32_out, not_33_out, not_34_out, not_35_out, OP4, not_36_out, not_37_out);
  and and_7 (and_7_out, not_38_out, F13, not_39_out, not_40_out, not_41_out, OP4, not_42_out, not_43_out);
  and and_8 (and_8_out, F30, not_44_out, F14, not_45_out, F12, not_46_out, not_47_out, OP4, not_48_out, not_49_out);
  and and_9 (and_9_out, not_50_out, F13, not_51_out, not_52_out, not_53_out, not_54_out, not_55_out, not_56_out);
  and and_10 (and_10_out, not_57_out, F13, not_58_out, not_59_out, OP5, not_60_out, not_61_out, not_62_out);
  and and_11 (and_11_out, F30, not_63_out, F14, not_64_out, F12, not_65_out, OP5, OP4, not_66_out, not_67_out);
  and and_12 (and_12_out, F14, not_68_out, not_69_out, not_70_out, not_71_out, not_72_out, not_73_out, not_74_out);
  and and_13 (and_13_out, F30, not_75_out, not_76_out, not_77_out, not_78_out, not_79_out, OP5, OP4, not_80_out, not_81_out);
  and and_14 (and_14_out, not_82_out, not_83_out, F14, F13, F12, not_84_out, OP5, OP4, not_85_out, not_86_out);
  and and_15 (and_15_out, not_87_out, not_88_out, not_89_out, F13, not_90_out, not_91_out, OP5, OP4, not_92_out, not_93_out);
  and and_16 (and_16_out, F14, F13, F12, not_94_out, not_95_out, OP4, not_96_out, not_97_out);
  and and_17 (and_17_out, not_98_out, F13, not_99_out, not_100_out, not_101_out, OP4, not_102_out, not_103_out);
  and and_18 (and_18_out, not_104_out, not_105_out, F14, not_106_out, F12, not_107_out, not_108_out, OP4, not_109_out, not_110_out);
  and and_19 (and_19_out, not_111_out, not_112_out, not_113_out, not_114_out, not_115_out, not_116_out, OP5, OP4, not_117_out, not_118_out);
  and and_20 (and_20_out, F30, not_119_out, not_120_out, not_121_out, not_122_out, not_123_out, OP5, OP4, not_124_out, not_125_out);
  and and_21 (and_21_out, not_126_out, not_127_out, F14, F13, F12, not_128_out, OP5, OP4, not_129_out, not_130_out);
  and and_22 (and_22_out, not_131_out, not_132_out, not_133_out, F13, F12, not_134_out, OP5, OP4, not_135_out, not_136_out);
  and and_23 (and_23_out, not_137_out, not_138_out, not_139_out, not_140_out, not_141_out, OP4, not_142_out, not_143_out);
  and and_24 (and_24_out, F14, F13, F12, not_144_out, not_145_out, OP4, not_146_out, not_147_out);
  and and_25 (and_25_out, not_148_out, F13, not_149_out, not_150_out, not_151_out, not_152_out, not_153_out, not_154_out);
  and and_26 (and_26_out, not_155_out, F13, not_156_out, not_157_out, OP5, not_158_out, not_159_out, not_160_out);
  and and_27 (and_27_out, F14, not_161_out, not_162_out, not_163_out, not_164_out, not_165_out, not_166_out, not_167_out);
  and and_28 (and_28_out, F14, F13, F12, OP6, OP5, not_168_out, not_169_out, not_170_out);
  and and_29 (and_29_out, not_171_out, not_172_out, F14, F13, not_173_out, not_174_out, OP5, OP4, not_175_out, not_176_out);
  and and_30 (and_30_out, not_177_out, not_178_out, not_179_out, F13, not_180_out, not_181_out, OP5, OP4, not_182_out, not_183_out);
  and and_31 (and_31_out, not_184_out, not_185_out, not_186_out, F13, F12, not_187_out, OP5, OP4, not_188_out, not_189_out);
  and and_32 (and_32_out, F14, F13, not_190_out, not_191_out, not_192_out, OP4, not_193_out, not_194_out);
  and and_33 (and_33_out, F14, not_195_out, not_196_out, not_197_out, not_198_out, OP4, not_199_out, not_200_out);
  and and_34 (and_34_out, not_201_out, F13, not_202_out, not_203_out, not_204_out, OP4, not_205_out, not_206_out);
  and and_35 (and_35_out, F14, F13, F12, OP6, OP5, not_207_out, not_208_out, not_209_out);
  or or_1 (S0, and_1_out, and_2_out, and_3_out, and_4_out, and_5_out, and_6_out, and_7_out, and_8_out, and_9_out, and_10_out, and_11_out, and_12_out);
  or or_2 (S1, and_13_out, and_14_out, and_15_out, and_16_out, and_17_out, and_18_out);
  or or_3 (S2, and_19_out, and_20_out, and_21_out, and_22_out, and_23_out, and_24_out, and_25_out, and_26_out, and_27_out, and_28_out);
  or or_4 (S3, and_29_out, and_30_out, and_31_out, and_32_out, and_33_out, and_34_out, and_35_out);
endmodule

// 控制信号生成
module \控制信号自动生成  (
  input  OP2,
  input  OP3,
  input  OP4,
  input  OP5,
  input  OP6,
  input  F12,
  input  F13,
  input  F14,
  input  F25,
  input  F30,
  output MemToReg,
  output MemWrite,
  output rs1_use,
  output rs2_use,
  output ALU_SRC,
  output RegWrite,
  output ecall,
  output S_Type,
  output BEQ,
  output BNE,
  output JALR,
  output JAL,
  output LBU,
  output BGEU,
  output CSRRSI,
  output CSEECI
);

  wire and_1_out, and_2_out, and_4_out, and_5_out, and_6_out, and_7_out, and_8_out, and_9_out, and_10_out,
       and_11_out, and_12_out, and_13_out, and_14_out, and_15_out, and_16_out, and_17_out, and_18_out,
       and_19_out, and_20_out, and_21_out, and_22_out, and_23_out, and_24_out, and_25_out, and_26_out,
       and_27_out, and_28_out, and_29_out, and_30_out, and_31_out, and_32_out, and_33_out, and_34_out,
       and_35_out, and_36_out, and_37_out, and_38_out, and_39_out, and_40_out, and_41_out, and_42_out,
       and_43_out, and_44_out, and_45_out, and_46_out, and_47_out, and_48_out, and_49_out, and_50_out,
       and_51_out, and_52_out, and_53_out, and_54_out, and_55_out, and_56_out, and_57_out, and_58_out,
       and_59_out, and_60_out, and_61_out, and_62_out, and_63_out, and_64_out, and_65_out, and_66_out,
       and_67_out, and_68_out, and_69_out, and_70_out, not_1_out, not_2_out, not_3_out, not_4_out, not_5_out,
       not_6_out, not_7_out, not_8_out, not_9_out, not_10_out, not_11_out, not_12_out, not_13_out,
       not_14_out, not_15_out, not_16_out, not_17_out, not_18_out, not_19_out, not_20_out, not_21_out,
       not_22_out, not_23_out, not_24_out, not_25_out, not_26_out, not_27_out, not_28_out, not_29_out,
       not_30_out, not_31_out, not_32_out, not_33_out, not_34_out, not_35_out, not_36_out, not_37_out,
       not_38_out, not_39_out, not_40_out, not_41_out, not_42_out, not_43_out, not_44_out, not_45_out,
       not_46_out, not_47_out, not_48_out, not_49_out, not_50_out, not_51_out, not_52_out, not_53_out,
       not_54_out, not_55_out, not_56_out, not_57_out, not_58_out, not_59_out, not_60_out, not_61_out,
       not_62_out, not_63_out, not_64_out, not_65_out, not_66_out, not_67_out, not_68_out, not_69_out,
       not_70_out, not_71_out, not_72_out, not_73_out, not_74_out, not_75_out, not_76_out, not_77_out,
       not_78_out, not_79_out, not_80_out, not_81_out, not_82_out, not_83_out, not_84_out, not_85_out,
       not_86_out, not_87_out, not_88_out, not_89_out, not_90_out, not_91_out, not_92_out, not_93_out,
       not_94_out, not_95_out, not_96_out, not_97_out, not_98_out, not_99_out, not_100_out, not_101_out,
       not_102_out, not_103_out, not_104_out, not_105_out, not_106_out, not_107_out, not_108_out,
       not_109_out, not_110_out, not_111_out, not_112_out, not_113_out, not_114_out, not_115_out,
       not_116_out, not_117_out, not_118_out, not_119_out, not_120_out, not_121_out, not_122_out,
       not_123_out, not_124_out, not_125_out, not_126_out, not_127_out, not_128_out, not_129_out,
       not_130_out, not_131_out, not_132_out, not_133_out, not_134_out, not_135_out, not_136_out,
       not_137_out, not_138_out, not_139_out, not_140_out, not_141_out, not_142_out, not_143_out,
       not_144_out, not_145_out, not_146_out, not_147_out, not_148_out, not_149_out, not_150_out,
       not_151_out, not_152_out, not_153_out, not_154_out, not_155_out, not_156_out, not_157_out,
       not_158_out, not_159_out, not_160_out, not_161_out, not_162_out, not_163_out, not_164_out,
       not_165_out, not_166_out, not_167_out, not_168_out, not_169_out, not_170_out, not_171_out,
       not_172_out, not_173_out, not_174_out, not_175_out, not_176_out, not_177_out, not_178_out,
       not_179_out, not_180_out, not_181_out, not_182_out, not_183_out, not_184_out, not_185_out,
       not_186_out, not_187_out, not_188_out, not_189_out, not_190_out, not_191_out, not_192_out,
       not_193_out, not_194_out, not_195_out, not_196_out, not_197_out, not_198_out, not_199_out,
       not_200_out, not_201_out, not_202_out, not_203_out, not_204_out, not_205_out, not_206_out,
       not_207_out, not_208_out, not_209_out, not_210_out, not_211_out, not_212_out, not_213_out,
       not_214_out, not_215_out, not_216_out, not_217_out, not_218_out, not_219_out, not_220_out,
       not_221_out, not_222_out, not_223_out, not_224_out, not_225_out, not_226_out, not_227_out,
       not_228_out, not_229_out, not_230_out, not_231_out, not_232_out, not_233_out, not_234_out,
       not_235_out, not_236_out, not_237_out, not_238_out, not_239_out, not_240_out, not_241_out,
       not_242_out, not_243_out, not_244_out, not_245_out, not_246_out, not_247_out, not_248_out,
       not_249_out, not_250_out, not_251_out, not_252_out, not_253_out, not_254_out, not_255_out,
       not_256_out, not_257_out, not_258_out, not_259_out, not_260_out, not_261_out, not_262_out,
       not_263_out, not_264_out, not_265_out, not_266_out, not_267_out, not_268_out, not_269_out,
       not_270_out, not_271_out, not_272_out, not_273_out, not_274_out, not_275_out, not_276_out,
       not_277_out, not_278_out, not_279_out, not_280_out, not_281_out, not_282_out, not_283_out,
       not_284_out, not_285_out, not_286_out, not_287_out, not_288_out, not_289_out, not_290_out,
       not_291_out, not_292_out, not_293_out, not_294_out, not_295_out, not_296_out, not_297_out,
       not_298_out, not_299_out, not_300_out, not_301_out, not_302_out, not_303_out, not_304_out,
       not_305_out, not_306_out, not_307_out, not_308_out, not_309_out, not_310_out, not_311_out,
       not_312_out, not_313_out, not_314_out, not_315_out, not_316_out, not_317_out, not_318_out,
       not_319_out, not_320_out, not_321_out, not_322_out, not_323_out, not_324_out, not_325_out,
       not_326_out, not_327_out, not_328_out, not_329_out, not_330_out, not_331_out, not_332_out,
       not_333_out, not_334_out, not_335_out, not_336_out, not_337_out, not_338_out, not_339_out,
       not_340_out, not_341_out, not_342_out, not_343_out, not_344_out, not_345_out, not_346_out,
       not_347_out, not_348_out, not_349_out, not_350_out, not_351_out, not_352_out, not_353_out,
       not_354_out, not_355_out, not_356_out, not_357_out, not_358_out, not_359_out, not_360_out,
       not_361_out, not_362_out, not_363_out, not_364_out, not_365_out, not_366_out, not_367_out,
       not_368_out, not_369_out, not_370_out, not_371_out, not_372_out, not_373_out, not_374_out,
       not_375_out, not_376_out, not_377_out, not_378_out, not_379_out, not_380_out, not_381_out,
       not_382_out, not_383_out, not_384_out, not_385_out, not_386_out, not_387_out, not_388_out,
       not_389_out, not_390_out, not_391_out, not_392_out, not_393_out, not_394_out, not_395_out,
       not_396_out, not_397_out, not_398_out, not_399_out, not_400_out, not_401_out, not_402_out,
       not_403_out, not_404_out, not_405_out, not_406_out, not_407_out, not_408_out, not_409_out,
       not_410_out, not_411_out, not_412_out, not_413_out, not_414_out, not_415_out, not_416_out,
       not_417_out, not_418_out, not_419_out, not_420_out, not_421_out, not_422_out, not_423_out,
       not_424_out, not_425_out, not_426_out, not_427_out, not_428_out, not_429_out, not_430_out,
       not_431_out, not_432_out, not_433_out, not_434_out, not_435_out, not_436_out, not_437_out,
       not_438_out, not_439_out, not_440_out, not_441_out, not_442_out, not_443_out, not_444_out,
       not_445_out, not_446_out, not_447_out, not_448_out, not_449_out, not_450_out, not_451_out,
       not_452_out, not_453_out, not_454_out, not_455_out, not_456_out, not_457_out, not_458_out,
       not_459_out, not_460_out, not_461_out, not_462_out, not_463_out, not_464_out, not_465_out,
       not_466_out, not_467_out, not_468_out, not_469_out;

  not not_1 (not_1_out, F14);
  not not_2 (not_2_out, F12);
  not not_3 (not_3_out, OP6);
  not not_4 (not_4_out, OP5);
  not not_5 (not_5_out, OP4);
  not not_6 (not_6_out, OP3);
  not not_7 (not_7_out, OP2);
  not not_8 (not_8_out, F13);
  not not_9 (not_9_out, F12);
  not not_10 (not_10_out, OP6);
  not not_11 (not_11_out, OP5);
  not not_12 (not_12_out, OP4);
  not not_13 (not_13_out, OP3);
  not not_14 (not_14_out, OP2);
  not not_15 (not_15_out, F14);
  not not_16 (not_16_out, F12);
  not not_17 (not_17_out, OP6);
  not not_18 (not_18_out, OP4);
  not not_19 (not_19_out, OP3);
  not not_20 (not_20_out, OP2);
  not not_21 (not_21_out, F30);
  not not_22 (not_22_out, F25);
  not not_23 (not_23_out, F14);
  not not_24 (not_24_out, F13);
  not not_25 (not_25_out, F12);
  not not_26 (not_26_out, OP6);
  not not_27 (not_27_out, OP3);
  not not_28 (not_28_out, OP2);
  not not_29 (not_29_out, F25);
  not not_30 (not_30_out, F14);
  not not_31 (not_31_out, F13);
  not not_32 (not_32_out, F12);
  not not_33 (not_33_out, OP6);
  not not_34 (not_34_out, OP3);
  not not_35 (not_35_out, OP2);
  not not_36 (not_36_out, F30);
  not not_37 (not_37_out, F25);
  not not_38 (not_38_out, OP6);
  not not_39 (not_39_out, OP3);
  not not_40 (not_40_out, OP2);
  not not_41 (not_41_out, F30);
  not not_42 (not_42_out, F25);
  not not_43 (not_43_out, F12);
  not not_44 (not_44_out, OP6);
  not not_45 (not_45_out, OP3);
  not not_46 (not_46_out, OP2);
  not not_47 (not_47_out, F30);
  not not_48 (not_48_out, F25);
  not not_49 (not_49_out, F14);
  not not_50 (not_50_out, F12);
  not not_51 (not_51_out, OP6);
  not not_52 (not_52_out, OP3);
  not not_53 (not_53_out, OP2);
  not not_54 (not_54_out, F30);
  not not_55 (not_55_out, F25);
  not not_56 (not_56_out, F14);
  not not_57 (not_57_out, OP6);
  not not_58 (not_58_out, OP3);
  not not_59 (not_59_out, OP2);
  not not_60 (not_60_out, F14);
  not not_61 (not_61_out, F13);
  not not_62 (not_62_out, F12);
  not not_63 (not_63_out, OP6);
  not not_64 (not_64_out, OP5);
  not not_65 (not_65_out, OP3);
  not not_66 (not_66_out, OP2);
  not not_67 (not_67_out, OP6);
  not not_68 (not_68_out, OP5);
  not not_69 (not_69_out, OP3);
  not not_70 (not_70_out, OP2);
  not not_71 (not_71_out, F12);
  not not_72 (not_72_out, OP6);
  not not_73 (not_73_out, OP5);
  not not_74 (not_74_out, OP3);
  not not_75 (not_75_out, OP2);
  not not_76 (not_76_out, F13);
  not not_77 (not_77_out, F12);
  not not_78 (not_78_out, OP6);
  not not_79 (not_79_out, OP5);
  not not_80 (not_80_out, OP3);
  not not_81 (not_81_out, OP2);
  not not_82 (not_82_out, F14);
  not not_83 (not_83_out, F12);
  not not_84 (not_84_out, OP6);
  not not_85 (not_85_out, OP5);
  not not_86 (not_86_out, OP3);
  not not_87 (not_87_out, OP2);
  not not_88 (not_88_out, F30);
  not not_89 (not_89_out, F25);
  not not_90 (not_90_out, F14);
  not not_91 (not_91_out, F13);
  not not_92 (not_92_out, OP6);
  not not_93 (not_93_out, OP5);
  not not_94 (not_94_out, OP3);
  not not_95 (not_95_out, OP2);
  not not_96 (not_96_out, F30);
  not not_97 (not_97_out, F25);
  not not_98 (not_98_out, F13);
  not not_99 (not_99_out, OP6);
  not not_100 (not_100_out, OP5);
  not not_101 (not_101_out, OP3);
  not not_102 (not_102_out, OP2);
  not not_103 (not_103_out, F25);
  not not_104 (not_104_out, F13);
  not not_105 (not_105_out, OP6);
  not not_106 (not_106_out, OP5);
  not not_107 (not_107_out, OP3);
  not not_108 (not_108_out, OP2);
  not not_109 (not_109_out, F14);
  not not_110 (not_110_out, F12);
  not not_111 (not_111_out, OP6);
  not not_112 (not_112_out, OP5);
  not not_113 (not_113_out, OP4);
  not not_114 (not_114_out, OP3);
  not not_115 (not_115_out, OP2);
  not not_116 (not_116_out, F14);
  not not_117 (not_117_out, F12);
  not not_118 (not_118_out, OP6);
  not not_119 (not_119_out, OP4);
  not not_120 (not_120_out, OP3);
  not not_121 (not_121_out, OP2);
  not not_122 (not_122_out, F14);
  not not_123 (not_123_out, F13);
  not not_124 (not_124_out, F12);
  not not_125 (not_125_out, OP4);
  not not_126 (not_126_out, OP3);
  not not_127 (not_127_out, OP2);
  not not_128 (not_128_out, F14);
  not not_129 (not_129_out, F13);
  not not_130 (not_130_out, OP4);
  not not_131 (not_131_out, OP3);
  not not_132 (not_132_out, OP2);
  not not_133 (not_133_out, F14);
  not not_134 (not_134_out, F13);
  not not_135 (not_135_out, F12);
  not not_136 (not_136_out, OP4);
  not not_137 (not_137_out, OP3);
  not not_138 (not_138_out, F30);
  not not_139 (not_139_out, F25);
  not not_140 (not_140_out, F14);
  not not_141 (not_141_out, F13);
  not not_142 (not_142_out, OP6);
  not not_143 (not_143_out, OP3);
  not not_144 (not_144_out, OP2);
  not not_145 (not_145_out, F25);
  not not_146 (not_146_out, F13);
  not not_147 (not_147_out, OP6);
  not not_148 (not_148_out, OP3);
  not not_149 (not_149_out, OP2);
  not not_150 (not_150_out, F13);
  not not_151 (not_151_out, F12);
  not not_152 (not_152_out, OP6);
  not not_153 (not_153_out, OP5);
  not not_154 (not_154_out, OP4);
  not not_155 (not_155_out, OP3);
  not not_156 (not_156_out, OP2);
  not not_157 (not_157_out, OP4);
  not not_158 (not_158_out, OP3);
  not not_159 (not_159_out, OP2);
  not not_160 (not_160_out, F30);
  not not_161 (not_161_out, F25);
  not not_162 (not_162_out, F14);
  not not_163 (not_163_out, F13);
  not not_164 (not_164_out, F12);
  not not_165 (not_165_out, OP6);
  not not_166 (not_166_out, OP3);
  not not_167 (not_167_out, OP2);
  not not_168 (not_168_out, F25);
  not not_169 (not_169_out, F14);
  not not_170 (not_170_out, F13);
  not not_171 (not_171_out, F12);
  not not_172 (not_172_out, OP6);
  not not_173 (not_173_out, OP3);
  not not_174 (not_174_out, OP2);
  not not_175 (not_175_out, F30);
  not not_176 (not_176_out, F25);
  not not_177 (not_177_out, OP6);
  not not_178 (not_178_out, OP3);
  not not_179 (not_179_out, OP2);
  not not_180 (not_180_out, F30);
  not not_181 (not_181_out, F25);
  not not_182 (not_182_out, F12);
  not not_183 (not_183_out, OP6);
  not not_184 (not_184_out, OP3);
  not not_185 (not_185_out, OP2);
  not not_186 (not_186_out, F30);
  not not_187 (not_187_out, F25);
  not not_188 (not_188_out, F14);
  not not_189 (not_189_out, F12);
  not not_190 (not_190_out, OP6);
  not not_191 (not_191_out, OP3);
  not not_192 (not_192_out, OP2);
  not not_193 (not_193_out, F30);
  not not_194 (not_194_out, F25);
  not not_195 (not_195_out, F14);
  not not_196 (not_196_out, OP6);
  not not_197 (not_197_out, OP3);
  not not_198 (not_198_out, OP2);
  not not_199 (not_199_out, F14);
  not not_200 (not_200_out, F12);
  not not_201 (not_201_out, OP6);
  not not_202 (not_202_out, OP4);
  not not_203 (not_203_out, OP3);
  not not_204 (not_204_out, OP2);
  not not_205 (not_205_out, F14);
  not not_206 (not_206_out, F13);
  not not_207 (not_207_out, F12);
  not not_208 (not_208_out, OP4);
  not not_209 (not_209_out, OP3);
  not not_210 (not_210_out, OP2);
  not not_211 (not_211_out, F14);
  not not_212 (not_212_out, F13);
  not not_213 (not_213_out, OP4);
  not not_214 (not_214_out, OP3);
  not not_215 (not_215_out, OP2);
  not not_216 (not_216_out, F30);
  not not_217 (not_217_out, F25);
  not not_218 (not_218_out, F14);
  not not_219 (not_219_out, F13);
  not not_220 (not_220_out, OP6);
  not not_221 (not_221_out, OP3);
  not not_222 (not_222_out, OP2);
  not not_223 (not_223_out, F25);
  not not_224 (not_224_out, F13);
  not not_225 (not_225_out, OP6);
  not not_226 (not_226_out, OP3);
  not not_227 (not_227_out, OP2);
  not not_228 (not_228_out, OP4);
  not not_229 (not_229_out, OP3);
  not not_230 (not_230_out, OP2);
  not not_231 (not_231_out, F14);
  not not_232 (not_232_out, F13);
  not not_233 (not_233_out, F12);
  not not_234 (not_234_out, OP6);
  not not_235 (not_235_out, OP5);
  not not_236 (not_236_out, OP3);
  not not_237 (not_237_out, OP2);
  not not_238 (not_238_out, OP6);
  not not_239 (not_239_out, OP5);
  not not_240 (not_240_out, OP3);
  not not_241 (not_241_out, OP2);
  not not_242 (not_242_out, F12);
  not not_243 (not_243_out, OP6);
  not not_244 (not_244_out, OP5);
  not not_245 (not_245_out, OP3);
  not not_246 (not_246_out, OP2);
  not not_247 (not_247_out, F13);
  not not_248 (not_248_out, F12);
  not not_249 (not_249_out, OP6);
  not not_250 (not_250_out, OP5);
  not not_251 (not_251_out, OP3);
  not not_252 (not_252_out, OP2);
  not not_253 (not_253_out, F14);
  not not_254 (not_254_out, F12);
  not not_255 (not_255_out, OP6);
  not not_256 (not_256_out, OP5);
  not not_257 (not_257_out, OP3);
  not not_258 (not_258_out, OP2);
  not not_259 (not_259_out, F30);
  not not_260 (not_260_out, F25);
  not not_261 (not_261_out, F14);
  not not_262 (not_262_out, F13);
  not not_263 (not_263_out, OP6);
  not not_264 (not_264_out, OP5);
  not not_265 (not_265_out, OP3);
  not not_266 (not_266_out, OP2);
  not not_267 (not_267_out, F30);
  not not_268 (not_268_out, F25);
  not not_269 (not_269_out, F13);
  not not_270 (not_270_out, OP6);
  not not_271 (not_271_out, OP5);
  not not_272 (not_272_out, OP3);
  not not_273 (not_273_out, OP2);
  not not_274 (not_274_out, F25);
  not not_275 (not_275_out, F13);
  not not_276 (not_276_out, OP6);
  not not_277 (not_277_out, OP5);
  not not_278 (not_278_out, OP3);
  not not_279 (not_279_out, OP2);
  not not_280 (not_280_out, F14);
  not not_281 (not_281_out, F12);
  not not_282 (not_282_out, OP6);
  not not_283 (not_283_out, OP5);
  not not_284 (not_284_out, OP4);
  not not_285 (not_285_out, OP3);
  not not_286 (not_286_out, OP2);
  not not_287 (not_287_out, F14);
  not not_288 (not_288_out, F12);
  not not_289 (not_289_out, OP6);
  not not_290 (not_290_out, OP4);
  not not_291 (not_291_out, OP3);
  not not_292 (not_292_out, OP2);
  not not_293 (not_293_out, F14);
  not not_294 (not_294_out, F13);
  not not_295 (not_295_out, F12);
  not not_296 (not_296_out, OP4);
  not not_297 (not_297_out, OP3);
  not not_298 (not_298_out, F13);
  not not_299 (not_299_out, F12);
  not not_300 (not_300_out, OP6);
  not not_301 (not_301_out, OP5);
  not not_302 (not_302_out, OP4);
  not not_303 (not_303_out, OP3);
  not not_304 (not_304_out, OP2);
  not not_305 (not_305_out, F30);
  not not_306 (not_306_out, F25);
  not not_307 (not_307_out, F14);
  not not_308 (not_308_out, F13);
  not not_309 (not_309_out, F12);
  not not_310 (not_310_out, OP6);
  not not_311 (not_311_out, OP3);
  not not_312 (not_312_out, OP2);
  not not_313 (not_313_out, F25);
  not not_314 (not_314_out, F14);
  not not_315 (not_315_out, F13);
  not not_316 (not_316_out, F12);
  not not_317 (not_317_out, OP6);
  not not_318 (not_318_out, OP3);
  not not_319 (not_319_out, OP2);
  not not_320 (not_320_out, F30);
  not not_321 (not_321_out, F25);
  not not_322 (not_322_out, OP6);
  not not_323 (not_323_out, OP3);
  not not_324 (not_324_out, OP2);
  not not_325 (not_325_out, F30);
  not not_326 (not_326_out, F25);
  not not_327 (not_327_out, F12);
  not not_328 (not_328_out, OP6);
  not not_329 (not_329_out, OP3);
  not not_330 (not_330_out, OP2);
  not not_331 (not_331_out, F30);
  not not_332 (not_332_out, F25);
  not not_333 (not_333_out, F14);
  not not_334 (not_334_out, F12);
  not not_335 (not_335_out, OP6);
  not not_336 (not_336_out, OP3);
  not not_337 (not_337_out, OP2);
  not not_338 (not_338_out, F30);
  not not_339 (not_339_out, F25);
  not not_340 (not_340_out, F14);
  not not_341 (not_341_out, OP6);
  not not_342 (not_342_out, OP3);
  not not_343 (not_343_out, OP2);
  not not_344 (not_344_out, F14);
  not not_345 (not_345_out, F13);
  not not_346 (not_346_out, F12);
  not not_347 (not_347_out, OP6);
  not not_348 (not_348_out, OP5);
  not not_349 (not_349_out, OP3);
  not not_350 (not_350_out, OP2);
  not not_351 (not_351_out, OP6);
  not not_352 (not_352_out, OP5);
  not not_353 (not_353_out, OP3);
  not not_354 (not_354_out, OP2);
  not not_355 (not_355_out, F12);
  not not_356 (not_356_out, OP6);
  not not_357 (not_357_out, OP5);
  not not_358 (not_358_out, OP3);
  not not_359 (not_359_out, OP2);
  not not_360 (not_360_out, F13);
  not not_361 (not_361_out, F12);
  not not_362 (not_362_out, OP6);
  not not_363 (not_363_out, OP5);
  not not_364 (not_364_out, OP3);
  not not_365 (not_365_out, OP2);
  not not_366 (not_366_out, F14);
  not not_367 (not_367_out, F12);
  not not_368 (not_368_out, OP6);
  not not_369 (not_369_out, OP5);
  not not_370 (not_370_out, OP3);
  not not_371 (not_371_out, OP2);
  not not_372 (not_372_out, F30);
  not not_373 (not_373_out, F25);
  not not_374 (not_374_out, F14);
  not not_375 (not_375_out, F13);
  not not_376 (not_376_out, OP6);
  not not_377 (not_377_out, OP5);
  not not_378 (not_378_out, OP3);
  not not_379 (not_379_out, OP2);
  not not_380 (not_380_out, F30);
  not not_381 (not_381_out, F25);
  not not_382 (not_382_out, F13);
  not not_383 (not_383_out, OP6);
  not not_384 (not_384_out, OP5);
  not not_385 (not_385_out, OP3);
  not not_386 (not_386_out, OP2);
  not not_387 (not_387_out, F25);
  not not_388 (not_388_out, F13);
  not not_389 (not_389_out, OP6);
  not not_390 (not_390_out, OP5);
  not not_391 (not_391_out, OP3);
  not not_392 (not_392_out, OP2);
  not not_393 (not_393_out, F14);
  not not_394 (not_394_out, F12);
  not not_395 (not_395_out, OP6);
  not not_396 (not_396_out, OP5);
  not not_397 (not_397_out, OP4);
  not not_398 (not_398_out, OP3);
  not not_399 (not_399_out, OP2);
  not not_400 (not_400_out, OP4);
  not not_401 (not_401_out, F14);
  not not_402 (not_402_out, F13);
  not not_403 (not_403_out, F12);
  not not_404 (not_404_out, OP4);
  not not_405 (not_405_out, OP3);
  not not_406 (not_406_out, F30);
  not not_407 (not_407_out, F25);
  not not_408 (not_408_out, F14);
  not not_409 (not_409_out, F13);
  not not_410 (not_410_out, OP6);
  not not_411 (not_411_out, OP3);
  not not_412 (not_412_out, OP2);
  not not_413 (not_413_out, F25);
  not not_414 (not_414_out, F13);
  not not_415 (not_415_out, OP6);
  not not_416 (not_416_out, OP3);
  not not_417 (not_417_out, OP2);
  not not_418 (not_418_out, F13);
  not not_419 (not_419_out, F12);
  not not_420 (not_420_out, OP6);
  not not_421 (not_421_out, OP5);
  not not_422 (not_422_out, OP4);
  not not_423 (not_423_out, OP3);
  not not_424 (not_424_out, OP2);
  not not_425 (not_425_out, F30);
  not not_426 (not_426_out, F25);
  not not_427 (not_427_out, F14);
  not not_428 (not_428_out, F13);
  not not_429 (not_429_out, F12);
  not not_430 (not_430_out, OP3);
  not not_431 (not_431_out, OP2);
  not not_432 (not_432_out, F14);
  not not_433 (not_433_out, F12);
  not not_434 (not_434_out, OP6);
  not not_435 (not_435_out, OP4);
  not not_436 (not_436_out, OP3);
  not not_437 (not_437_out, OP2);
  not not_438 (not_438_out, F14);
  not not_439 (not_439_out, F13);
  not not_440 (not_440_out, F12);
  not not_441 (not_441_out, OP4);
  not not_442 (not_442_out, OP3);
  not not_443 (not_443_out, OP2);
  not not_444 (not_444_out, F14);
  not not_445 (not_445_out, F13);
  not not_446 (not_446_out, OP4);
  not not_447 (not_447_out, OP3);
  not not_448 (not_448_out, OP2);
  not not_449 (not_449_out, F14);
  not not_450 (not_450_out, F13);
  not not_451 (not_451_out, F12);
  not not_452 (not_452_out, OP4);
  not not_453 (not_453_out, OP3);
  not not_454 (not_454_out, OP4);
  not not_455 (not_455_out, F13);
  not not_456 (not_456_out, F12);
  not not_457 (not_457_out, OP6);
  not not_458 (not_458_out, OP5);
  not not_459 (not_459_out, OP4);
  not not_460 (not_460_out, OP3);
  not not_461 (not_461_out, OP2);
  not not_462 (not_462_out, OP4);
  not not_463 (not_463_out, OP3);
  not not_464 (not_464_out, OP2);
  not not_465 (not_465_out, F12);
  not not_466 (not_466_out, OP3);
  not not_467 (not_467_out, OP2);
  not not_468 (not_468_out, OP3);
  not not_469 (not_469_out, OP2);
  and and_1 (and_1_out, not_1_out, F13, not_2_out, not_3_out, not_4_out, not_5_out, not_6_out, not_7_out);
  and and_2 (and_2_out, F14, not_8_out, not_9_out, not_10_out, not_11_out, not_12_out, not_13_out, not_14_out);
  and and_3 (MemWrite, not_15_out, F13, not_16_out, not_17_out, OP5, not_18_out, not_19_out, not_20_out);
  and and_4 (and_4_out, not_21_out, not_22_out, not_23_out, not_24_out, not_25_out, not_26_out, OP5, OP4, not_27_out, not_28_out);
  and and_5 (and_5_out, F30, not_29_out, not_30_out, not_31_out, not_32_out, not_33_out, OP5, OP4, not_34_out, not_35_out);
  and and_6 (and_6_out, not_36_out, not_37_out, F14, F13, F12, not_38_out, OP5, OP4, not_39_out, not_40_out);
  and and_7 (and_7_out, not_41_out, not_42_out, F14, F13, not_43_out, not_44_out, OP5, OP4, not_45_out, not_46_out);
  and and_8 (and_8_out, not_47_out, not_48_out, not_49_out, F13, not_50_out, not_51_out, OP5, OP4, not_52_out, not_53_out);
  and and_9 (and_9_out, not_54_out, not_55_out, not_56_out, F13, F12, not_57_out, OP5, OP4, not_58_out, not_59_out);
  and and_10 (and_10_out, not_60_out, not_61_out, not_62_out, not_63_out, not_64_out, OP4, not_65_out, not_66_out);
  and and_11 (and_11_out, F14, F13, F12, not_67_out, not_68_out, OP4, not_69_out, not_70_out);
  and and_12 (and_12_out, F14, F13, not_71_out, not_72_out, not_73_out, OP4, not_74_out, not_75_out);
  and and_13 (and_13_out, F14, not_76_out, not_77_out, not_78_out, not_79_out, OP4, not_80_out, not_81_out);
  and and_14 (and_14_out, not_82_out, F13, not_83_out, not_84_out, not_85_out, OP4, not_86_out, not_87_out);
  and and_15 (and_15_out, not_88_out, not_89_out, not_90_out, not_91_out, F12, not_92_out, not_93_out, OP4, not_94_out, not_95_out);
  and and_16 (and_16_out, not_96_out, not_97_out, F14, not_98_out, F12, not_99_out, not_100_out, OP4, not_101_out, not_102_out);
  and and_17 (and_17_out, F30, not_103_out, F14, not_104_out, F12, not_105_out, not_106_out, OP4, not_107_out, not_108_out);
  and and_18 (and_18_out, not_109_out, F13, not_110_out, not_111_out, not_112_out, not_113_out, not_114_out, not_115_out);
  and and_19 (and_19_out, not_116_out, F13, not_117_out, not_118_out, OP5, not_119_out, not_120_out, not_121_out);
  and and_20 (and_20_out, not_122_out, not_123_out, not_124_out, OP6, OP5, not_125_out, not_126_out, not_127_out);
  and and_21 (and_21_out, not_128_out, not_129_out, F12, OP6, OP5, not_130_out, not_131_out, not_132_out);
  and and_22 (and_22_out, not_133_out, not_134_out, not_135_out, OP6, OP5, not_136_out, not_137_out, OP2);
  and and_23 (and_23_out, not_138_out, not_139_out, not_140_out, not_141_out, F12, not_142_out, OP5, OP4, not_143_out, not_144_out);
  and and_24 (and_24_out, F30, not_145_out, F14, not_146_out, F12, not_147_out, OP5, OP4, not_148_out, not_149_out);
  and and_25 (and_25_out, F14, not_150_out, not_151_out, not_152_out, not_153_out, not_154_out, not_155_out, not_156_out);
  and and_26 (and_26_out, F14, F13, F12, OP6, OP5, not_157_out, not_158_out, not_159_out);
  and and_27 (and_27_out, not_160_out, not_161_out, not_162_out, not_163_out, not_164_out, not_165_out, OP5, OP4, not_166_out, not_167_out);
  and and_28 (and_28_out, F30, not_168_out, not_169_out, not_170_out, not_171_out, not_172_out, OP5, OP4, not_173_out, not_174_out);
  and and_29 (and_29_out, not_175_out, not_176_out, F14, F13, F12, not_177_out, OP5, OP4, not_178_out, not_179_out);
  and and_30 (and_30_out, not_180_out, not_181_out, F14, F13, not_182_out, not_183_out, OP5, OP4, not_184_out, not_185_out);
  and and_31 (and_31_out, not_186_out, not_187_out, not_188_out, F13, not_189_out, not_190_out, OP5, OP4, not_191_out, not_192_out);
  and and_32 (and_32_out, not_193_out, not_194_out, not_195_out, F13, F12, not_196_out, OP5, OP4, not_197_out, not_198_out);
  and and_33 (and_33_out, not_199_out, F13, not_200_out, not_201_out, OP5, not_202_out, not_203_out, not_204_out);
  and and_34 (and_34_out, not_205_out, not_206_out, not_207_out, OP6, OP5, not_208_out, not_209_out, not_210_out);
  and and_35 (and_35_out, not_211_out, not_212_out, F12, OP6, OP5, not_213_out, not_214_out, not_215_out);
  and and_36 (and_36_out, not_216_out, not_217_out, not_218_out, not_219_out, F12, not_220_out, OP5, OP4, not_221_out, not_222_out);
  and and_37 (and_37_out, F30, not_223_out, F14, not_224_out, F12, not_225_out, OP5, OP4, not_226_out, not_227_out);
  and and_38 (and_38_out, F14, F13, F12, OP6, OP5, not_228_out, not_229_out, not_230_out);
  and and_39 (and_39_out, not_231_out, not_232_out, not_233_out, not_234_out, not_235_out, OP4, not_236_out, not_237_out);
  and and_40 (and_40_out, F14, F13, F12, not_238_out, not_239_out, OP4, not_240_out, not_241_out);
  and and_41 (and_41_out, F14, F13, not_242_out, not_243_out, not_244_out, OP4, not_245_out, not_246_out);
  and and_42 (and_42_out, F14, not_247_out, not_248_out, not_249_out, not_250_out, OP4, not_251_out, not_252_out);
  and and_43 (and_43_out, not_253_out, F13, not_254_out, not_255_out, not_256_out, OP4, not_257_out, not_258_out);
  and and_44 (and_44_out, not_259_out, not_260_out, not_261_out, not_262_out, F12, not_263_out, not_264_out, OP4, not_265_out, not_266_out);
  and and_45 (and_45_out, not_267_out, not_268_out, F14, not_269_out, F12, not_270_out, not_271_out, OP4, not_272_out, not_273_out);
  and and_46 (and_46_out, F30, not_274_out, F14, not_275_out, F12, not_276_out, not_277_out, OP4, not_278_out, not_279_out);
  and and_47 (and_47_out, not_280_out, F13, not_281_out, not_282_out, not_283_out, not_284_out, not_285_out, not_286_out);
  and and_48 (and_48_out, not_287_out, F13, not_288_out, not_289_out, OP5, not_290_out, not_291_out, not_292_out);
  and and_49 (and_49_out, not_293_out, not_294_out, not_295_out, OP6, OP5, not_296_out, not_297_out, OP2);
  and and_50 (and_50_out, F14, not_298_out, not_299_out, not_300_out, not_301_out, not_302_out, not_303_out, not_304_out);
  and and_51 (and_51_out, not_305_out, not_306_out, not_307_out, not_308_out, not_309_out, not_310_out, OP5, OP4, not_311_out, not_312_out);
  and and_52 (and_52_out, F30, not_313_out, not_314_out, not_315_out, not_316_out, not_317_out, OP5, OP4, not_318_out, not_319_out);
  and and_53 (and_53_out, not_320_out, not_321_out, F14, F13, F12, not_322_out, OP5, OP4, not_323_out, not_324_out);
  and and_54 (and_54_out, not_325_out, not_326_out, F14, F13, not_327_out, not_328_out, OP5, OP4, not_329_out, not_330_out);
  and and_55 (and_55_out, not_331_out, not_332_out, not_333_out, F13, not_334_out, not_335_out, OP5, OP4, not_336_out, not_337_out);
  and and_56 (and_56_out, not_338_out, not_339_out, not_340_out, F13, F12, not_341_out, OP5, OP4, not_342_out, not_343_out);
  and and_57 (and_57_out, not_344_out, not_345_out, not_346_out, not_347_out, not_348_out, OP4, not_349_out, not_350_out);
  and and_58 (and_58_out, F14, F13, F12, not_351_out, not_352_out, OP4, not_353_out, not_354_out);
  and and_59 (and_59_out, F14, F13, not_355_out, not_356_out, not_357_out, OP4, not_358_out, not_359_out);
  and and_60 (and_60_out, F14, not_360_out, not_361_out, not_362_out, not_363_out, OP4, not_364_out, not_365_out);
  and and_61 (and_61_out, not_366_out, F13, not_367_out, not_368_out, not_369_out, OP4, not_370_out, not_371_out);
  and and_62 (and_62_out, not_372_out, not_373_out, not_374_out, not_375_out, F12, not_376_out, not_377_out, OP4, not_378_out, not_379_out);
  and and_63 (and_63_out, not_380_out, not_381_out, F14, not_382_out, F12, not_383_out, not_384_out, OP4, not_385_out, not_386_out);
  and and_64 (and_64_out, F30, not_387_out, F14, not_388_out, F12, not_389_out, not_390_out, OP4, not_391_out, not_392_out);
  and and_65 (and_65_out, not_393_out, F13, not_394_out, not_395_out, not_396_out, not_397_out, not_398_out, not_399_out);
  and and_66 (and_66_out, OP6, OP5, not_400_out, OP3, OP2);
  and and_67 (and_67_out, not_401_out, not_402_out, not_403_out, OP6, OP5, not_404_out, not_405_out, OP2);
  and and_68 (and_68_out, not_406_out, not_407_out, not_408_out, not_409_out, F12, not_410_out, OP5, OP4, not_411_out, not_412_out);
  and and_69 (and_69_out, F30, not_413_out, F14, not_414_out, F12, not_415_out, OP5, OP4, not_416_out, not_417_out);
  and and_70 (and_70_out, F14, not_418_out, not_419_out, not_420_out, not_421_out, not_422_out, not_423_out, not_424_out);
  and and_71 (ecall, not_425_out, not_426_out, not_427_out, not_428_out, not_429_out, OP6, OP5, OP4, not_430_out, not_431_out);
  and and_72 (S_Type, not_432_out, F13, not_433_out, not_434_out, OP5, not_435_out, not_436_out, not_437_out);
  and and_73 (BEQ, not_438_out, not_439_out, not_440_out, OP6, OP5, not_441_out, not_442_out, not_443_out);
  and and_74 (BNE, not_444_out, not_445_out, F12, OP6, OP5, not_446_out, not_447_out, not_448_out);
  and and_75 (JALR, not_449_out, not_450_out, not_451_out, OP6, OP5, not_452_out, not_453_out, OP2);
  and and_76 (JAL, OP6, OP5, not_454_out, OP3, OP2);
  and and_77 (LBU, F14, not_455_out, not_456_out, not_457_out, not_458_out, not_459_out, not_460_out, not_461_out);
  and and_78 (BGEU, F14, F13, F12, OP6, OP5, not_462_out, not_463_out, not_464_out);
  and and_79 (CSRRSI, F14, F13, not_465_out, OP6, OP5, OP4, not_466_out, not_467_out);
  and and_80 (CSEECI, F14, F13, F12, OP6, OP5, OP4, not_468_out, not_469_out);
  or or_1 (MemToReg, and_1_out, and_2_out);
  or or_2 (rs2_use, and_27_out, and_28_out, and_29_out, and_30_out, and_31_out, and_32_out, and_33_out, and_34_out, and_35_out, and_36_out, and_37_out, and_38_out);
  or or_3 (ALU_SRC, and_39_out, and_40_out, and_41_out, and_42_out, and_43_out, and_44_out, and_45_out, and_46_out, and_47_out, and_48_out, and_49_out, and_50_out);
  or or_4 (RegWrite, and_51_out, and_52_out, and_53_out, and_54_out, and_55_out, and_56_out, and_57_out, and_58_out, and_59_out, and_60_out, and_61_out, and_62_out, and_63_out, and_64_out, and_65_out, and_66_out, and_67_out, and_68_out, and_69_out, and_70_out);
  or or_5 (rs1_use, and_4_out, and_5_out, and_6_out, and_7_out, and_8_out, and_9_out, and_10_out, and_11_out, and_12_out, and_13_out, and_14_out, and_15_out, and_16_out, and_17_out, and_18_out, and_19_out, and_20_out, and_21_out, and_22_out, and_23_out, and_24_out, and_25_out, and_26_out);
endmodule

// ALU
module ALU (
  input  [31:0] X,
  input  [31:0] Y,
  input  [3:0] AluOP,
  output out_4,
  output Equal,
  output out_6,
  output [31:0] Result,
  output [31:0] Result_2
);

  wire [0:0] comparator_1_lt, comparator_2_lt;
  wire [31:0] adder_1_out, AND_out, divider_1_out, divider_1_rem, multiplier_1_cout, multiplier_1_out,
       NOR_out, OR_out, shifter_1_out, shifter_2_out, shifter_3_out, subtractor_1_out, XOR_out;

  assign AND_out = X & Y;  // AND_Gate AND, 32 bits wide
  assign OR_out = X | Y;  // OR_Gate OR, 32 bits wide
  Shifter #(.width(32), .shift("ll")) shifter_1 (.in(X), .\dist (Y[4:0]), .out(shifter_1_out));
  Shifter #(.width(32), .shift("ar")) shifter_2 (.in(X), .\dist (Y[4:0]), .out(shifter_2_out));
  Shifter #(.width(32), .shift("lr")) shifter_3 (.in(X), .\dist (Y[4:0]), .out(shifter_3_out));
  Multiplier #(.width(32)) multiplier_1 (.a(X), .b(Y), .out(multiplier_1_out), .cout(multiplier_1_cout));  // open: cin
  Divider #(.width(32)) divider_1 (.a(X), .b(Y), .out(divider_1_out), .rem(divider_1_rem));  // open: upper
  Adder #(.width(32)) adder_1 (.a(X), .b(Y), .out(adder_1_out));  // open: cin, cout
  Subtractor #(.width(32)) subtractor_1 (.a(X), .b(Y), .out(subtractor_1_out));  // open: bin, bout
  assign XOR_out = X ^ Y;  // XOR_Gate XOR, 32 bits wide
  assign NOR_out = ~(X | Y);  // NOR_Gate NOR, 32 bits wide
  Comparator #(.width(32), .mode("twosComplement")) comparator_1 (
    .a(X), .b(Y), .eq(Equal), .lt(comparator_1_lt[0]));  // open: gt
  Comparator #(.width(32), .mode("unsigned")) comparator_2 (.a(X), .b(Y), .lt(comparator_2_lt[0]));  // open: gt, eq
  Multiplexer #(.select(4), .width(32), .disabled("Z"), .enable("false")) multiplexer_1 (
    .in0(shifter_1_out), .in1(shifter_2_out), .in2(shifter_3_out), .in3(multiplier_1_out),
    .in4(divider_1_out), .in5(adder_1_out), .in6(subtractor_1_out), .in7(AND_out), .in8(OR_out),
    .in9(XOR_out), .in10(NOR_out), .in11({{31{1'b0}}, comparator_1_lt[0]}),
    .in12({{31{1'b0}}, comparator_2_lt[0]}), .in13({32{1'b0}}), .in14({32{1'b0}}), .in15({32{1'b0}}),
    .out(Result), .sel(AluOP));
  Multiplexer #(.select(4), .width(32), .disabled("Z"), .enable("false")) multiplexer_2 (
    .in0({32{1'b0}}), .in1({32{1'b0}}), .in2({32{1'b0}}), .in3(multiplier_1_cout), .in4(divider_1_rem),
    .in5({32{1'b0}}), .in6({32{1'b0}}), .in7({32{1'b0}}), .in8({32{1'b0}}), .in9({32{1'b0}}),
    .in10({32{1'b0}}), .in11({32{1'b0}}), .in12({32{1'b0}}), .in13({32{1'b0}}), .in14({32{1'b0}}),
    .in15({32{1'b0}}), .out(Result_2), .sel(AluOP));
  Multiplexer #(.select(4), .width(1), .disabled("Z"), .enable("false")) multiplexer_3 (
    .in0(1'b0), .in1(1'b0), .in2(1'b0), .in3(1'b0), .in4(1'b0), .in5(1'b0), .in6(1'b0), .in7(1'b0),
    .in8(1'b0), .in9(1'b0), .in10(1'b0), .in11(comparator_1_lt[0]), .in12(comparator_2_lt[0]), .in13(1'b0),
    .in14(1'b0), .in15(1'b0), .out(out_6), .sel(AluOP));
  not not_1 (out_4, out_6);

  // Other names for the same wires on the sheet: Result2[31:0] = Result_2; S[3:0] = AluOP; tunnel = out_6;
  //   tunnel_t = out_4

  // Notes on the sheet:
  //   不要改变此引脚区域内容，也不要改变ALU封装形式
  //   输入引脚
  //   输出引脚
endmodule

module Regifile (
  input  [31:0] Din,
  input  Clk,
  input  WE,
  input  [4:0] R1_num,
  input  [4:0] W_num,
  input  [4:0] R2_num,
  output [31:0] R1,
  output [31:0] R2
);

  // RegisterFile registerfile_1: pin names not known; wires that end beside it: Din, Clk, WE, W_num, R1_num, R2_num, R1, R2
endmodule

module \理想流水线  (
  output RegWrite,
  output MemWrite,
  output [31:0] IF_PC,
  output [31:0] ID_PC,
  output [31:0] EX_PC,
  output [31:0] M_PC,
  output [31:0] WB_PC,
  output [31:0] RDin,
  output [31:0] MDin,
  output [31:0] LedData
);

  wire alu_1_equal, alu_1_out_4, and_1_out, and_2_out, and_3_out, and_4_out, CLK, clock_1_out,
       comparator_1_eq, comparator_1_lt, d_ff_1_q, EX_B, EX_ecall, EX_HALT, EX_JAL, EX_JALR, EX_LBU,
       ex_mem_1_halt_2, ex_mem_1_jal_2, ex_mem_1_jalr_2, ex_mem_1_lbu_2, ex_mem_1_memtoreg_2,
       ex_mem_1_regwrite_2, Go, halt, ID_ecall, id_ex_1_alusrcb_2, id_ex_1_beq_2, id_ex_1_bgeu_2,
       id_ex_1_bne_2, id_ex_1_memtoreg_2, id_ex_1_memwrite_2, id_ex_1_regwrite_2, ID_JAL, ID_JALR, ID_LBU,
       IR1, IR2, IR3, mem_wb_1_halt_2, mem_wb_1_jal_2, mem_wb_1_jalr_2, mem_wb_1_lbu_2, mem_wb_1_memtoreg_2,
       nand_1_out, not_1_out, not_2_out, or_2_out, RST, W1, W2, W3, \单周期硬布线控制器_1_alu_src , \单周期硬布线控制器_1_beq ,
       \单周期硬布线控制器_1_bgeu , \单周期硬布线控制器_1_bne , \单周期硬布线控制器_1_memtoreg , \单周期硬布线控制器_1_memwrite ,
       \单周期硬布线控制器_1_regwrite , \单周期硬布线控制器_1_s_type ;
  wire [1:0] priority_encoder_1_out, priority_encoder_2_out;
  wire [3:0] id_ex_1_aluop_2, \单周期硬布线控制器_1_alu_op ;
  wire [4:0] ex_mem_1_rd_2, id_ex_1_rd_2, multiplexer_3_out, multiplexer_4_out, WB_rd;
  wire [7:0] multiplexer_6_out;
  wire [11:0] multiplexer_2_out;
  wire [12:0] CNT_num;
  wire [15:0] \LoadUse次数 , \总周期数 , \插入气泡数 , \无条件分支数 , \条件分支成功数 ;
  wire [31:0] ALU_result, B_PC, bit_extender_1_out, bit_extender_2_out, bit_extender_3_out,
       bit_extender_4_out, EX_IR, ex_mem_1_alu_result_2, EX_PC_4, id_ex_1_imm1_2, id_ex_1_imm2_2,
       id_ex_1_imm3_2, id_ex_1_r1_2, ID_IR, ID_PC_4, IF_IR, IF_PC_4, J_PC, MEM_IR, MEM_PC_4,
       mem_wb_1_alu_result_2, mem_wb_1_lbu_data_2, mem_wb_1_readdata_2, multiplexer_1_out, multiplexer_5_out,
       R2, ram_1_data, regifile_1_r1, regifile_1_r2, shifter_1_out, shifter_2_out, WB_IR, WB_PC_4;

  Button \u_总复位  (.out(RST));
  Button _1 (.out(IR1));
  Button _2 (.out(IR2));
  Button _3 (.out(IR3));
  // Probe on \总周期数 
  // Probe on \总周期数 
  Button \u_继续运行  (.out(Go));
  LED #(.active("true")) led_1 (.in(W1));
  LED #(.active("true")) led_2 (.in(W2));
  LED #(.active("true")) led_3 (.in(W3));
  Hex_Digit_Display hex_digit_display_1 (.value(LedData[31:28]));  // open: dp
  // Probe on IF_PC[19:0]
  // RiscV_Probe riscv_probe_1: pin names not known; wires that end beside it: IF_IR
  Priority_Encoder #(.select(2), .disabled("Z")) priority_encoder_1 (
    .in0(1'b1), .in1(EX_B), .in2(EX_JAL), .in3(EX_JALR), .out(priority_encoder_1_out));  // open: gs, en_out, en_in
  Multiplexer #(.select(2), .width(32), .disabled("Z"), .enable("false")) multiplexer_1 (
    .in0(IF_PC_4), .in1(B_PC), .in2(J_PC), .in3(ALU_result), .out(multiplexer_1_out),
    .sel(priority_encoder_1_out));
  not not_1 (not_1_out, halt);
  Hex_Digit_Display hex_digit_display_2 (.value(LedData[23:20]));  // open: dp
  Hex_Digit_Display hex_digit_display_3 (.value(LedData[27:24]));  // open: dp
  // Probe on ID_PC[19:0]
  // RiscV_Probe riscv_probe_2: pin names not known; wires that end beside it: ID_IR
  not not_2 (not_2_out, halt);
  Register #(.width(32), .trigger("rising"), .Select("low")) PC (
    .D(multiplexer_1_out), .en(not_1_out), .Q(IF_PC), .clk(CLK), .clr(RST));
  Hex_Digit_Display hex_digit_display_4 (.value(LedData[15:12]));  // open: dp
  Hex_Digit_Display hex_digit_display_5 (.value(LedData[19:16]));  // open: dp
  Counter #(.width(16), .max('hffff), .ongoal("wrap"), .trigger("rising"), .behavior("new")) counter_1 (
    .count(not_2_out), .Q(\总周期数 ), .clk(CLK));  // open: load, D, carry, clr, preset, down
  Hex_Digit_Display hex_digit_display_6 (.value(LedData[11:8]));  // open: dp
  Hex_Digit_Display hex_digit_display_7 (.value(LedData[7:4]));  // open: dp
  // Probe on EX_PC[19:0]
  // RiscV_Probe riscv_probe_3: pin names not known; wires that end beside it: EX_IR
  Hex_Digit_Display hex_digit_display_8 (.value(LedData[3:0]));  // open: dp
  ROM #(.addrWidth(10), .dataWidth(32), .Select("high")) rom_1 (.addr(IF_PC[11:2]), .data(IF_IR));
  Adder #(.width(32)) adder_1 (.a(IF_PC), .b(32'h4), .out(IF_PC_4));  // open: cin, cout
  // Probe on \总周期数 
  // Probe on M_PC[19:0]
  // RiscV_Probe riscv_probe_4: pin names not known; wires that end beside it: MEM_IR
  IF_ID if_id_1 (
    .IR(IF_IR), .PC_4(IF_PC_4), .IR_2(ID_IR), .PC_4_2(ID_PC_4), .reset(RST), .BranchTaken(1'b0), .en(1'b1),
    .clk(CLK), .PC(IF_PC), .PC_2(ID_PC));  // open: PredictJump, PredictJump_2
  // Probe on \总周期数 
  // Probe on \无条件分支数 
  // Probe on \条件分支成功数 
  // Probe on \插入气泡数 
  // Probe on \LoadUse次数 
  // Probe on ID_IR
  // Probe on IF_PC[11:0]
  // Probe on WB_PC[19:0]
  // RiscV_Probe riscv_probe_5: pin names not known; wires that end beside it: WB_IR
  Multiplexer #(.select(1), .width(12), .disabled("Z"), .enable("false")) multiplexer_2 (
    .in0(ID_IR[31:20]), .in1({ID_IR[31:25], ID_IR[11:7]}), .out(multiplexer_2_out), .sel(\单周期硬布线控制器_1_s_type ));
  // Probe on EX_PC[11:0]
  // Probe on ID_PC[11:0]
  \单周期硬布线控制器  \u_单周期硬布线控制器_1  (
    .Funct({ID_IR[30], ID_IR[25], ID_IR[14:12]}), .OP(ID_IR[6:2]), .ALU_OP(\单周期硬布线控制器_1_alu_op ),
    .MemToReg(\单周期硬布线控制器_1_memtoreg ), .MemWrite(\单周期硬布线控制器_1_memwrite ), .ALU_SRC(\单周期硬布线控制器_1_alu_src ),
    .RegWrite(\单周期硬布线控制器_1_regwrite ), .ecall(ID_ecall), .S_type(\单周期硬布线控制器_1_s_type ), .Jalr(ID_JALR),
    .Beq(\单周期硬布线控制器_1_beq ), .JAL(ID_JAL), .Bne(\单周期硬布线控制器_1_bne ), .in_3(ID_IR[21]), .LBU(ID_LBU),
    .BGEU(\单周期硬布线控制器_1_bgeu ));  // open: uret, CSRRSI, CSEECI, rs1_use, rs2_use
  Multiplexer #(.select(1), .width(5), .disabled("Z"), .enable("false")) multiplexer_3 (
    .in0(ID_IR[19:15]), .in1(5'b10001), .out(multiplexer_3_out), .sel(ID_ecall));
  Multiplexer #(.select(1), .width(5), .disabled("Z"), .enable("false")) multiplexer_4 (
    .in0(ID_IR[24:20]), .in1(5'b01010), .out(multiplexer_4_out), .sel(ID_ecall));
  assign bit_extender_1_out = {{20{1'b0}}, multiplexer_2_out};  // Bit_Extender bit_extender_1
  assign bit_extender_2_out = {{20{1'b0}}, {ID_IR[31], ID_IR[7], ID_IR[30:25], ID_IR[11:8]}};  // Bit_Extender bit_extender_2
  assign bit_extender_3_out = {{12{1'b0}}, {ID_IR[31], ID_IR[19:12], ID_IR[20], ID_IR[30:21]}};  // Bit_Extender bit_extender_3
  // Probe on M_PC[11:0]
  D_Flip_Flop #(.trigger("high"), .Pre_Clr_Positions("LEGACY"), .NegatePresetClear("false"), .enable("true"), .NewFFLayout("false")) d_ff_1 (.Q(d_ff_1_q));  // open: clk, D, Qn, preset, en, reset
  // Probe on 13'h20
  // Probe on WB_PC[11:0]
  Comparator #(.width(13), .mode("twosComplement")) comparator_1 (
    .a(CNT_num), .b(13'h20), .eq(comparator_1_eq), .lt(comparator_1_lt));  // open: gt
  Clock #(.highDuration(1), .lowDuration(1)) clock_1 (.out(clock_1_out));
  Regifile regifile_1 (
    .Din(RDin), .Clk(CLK), .R1(regifile_1_r1), .R2(regifile_1_r2), .WE(RegWrite), .W_num(WB_rd),
    .R1_num(multiplexer_3_out), .R2_num(multiplexer_4_out));
  nand nand_1 (nand_1_out, d_ff_1_q, comparator_1_eq);
  Counter #(.width(13), .max('h1fff), .ongoal("stay"), .trigger("rising"), .behavior("old")) counter_2 (
    .count(comparator_1_lt), .Q(CNT_num), .clk(clock_1_out));  // open: load, D, carry, clr, preset
  assign CLK = nand_1_out ? clock_1_out : 1'bz;  // Controlled_Buffer controlled_buffer_1
  ID_EX id_ex_1 (
    .Beq(\单周期硬布线控制器_1_beq ), .R1(regifile_1_r1), .Bgeu(\单周期硬布线控制器_1_bgeu ), .Bne(\单周期硬布线控制器_1_bne ),
    .R2(regifile_1_r2), .MemToReg(\单周期硬布线控制器_1_memtoreg ), .imm1(bit_extender_1_out),
    .MemWrite(\单周期硬布线控制器_1_memwrite ), .imm2(bit_extender_2_out), .RegWrite(\单周期硬布线控制器_1_regwrite ),
    .JAL(ID_JAL), .PC(ID_PC), .JALR(ID_JALR), .PC_4(ID_PC_4), .LBU(ID_LBU), .IR(ID_IR), .ecall(ID_ecall),
    .AluOP(\单周期硬布线控制器_1_alu_op ), .rd(ID_IR[11:7]), .AluSrcB(\单周期硬布线控制器_1_alu_src ), .Beq_2(id_ex_1_beq_2),
    .R1_2(id_ex_1_r1_2), .Bgeu_2(id_ex_1_bgeu_2), .Bne_2(id_ex_1_bne_2), .R2_2(R2),
    .MemToReg_2(id_ex_1_memtoreg_2), .imm1_2(id_ex_1_imm1_2), .MemWrite_2(id_ex_1_memwrite_2),
    .imm2_2(id_ex_1_imm2_2), .RegWrite_2(id_ex_1_regwrite_2), .JAL_2(EX_JAL), .PC_2(EX_PC), .JALR_2(EX_JALR),
    .PC_4_2(EX_PC_4), .LBU_2(EX_LBU), .IR_2(EX_IR), .ecall_2(EX_ecall), .AluOP_2(id_ex_1_aluop_2),
    .rd_2(id_ex_1_rd_2), .AluSrcB_2(id_ex_1_alusrcb_2), .reset(RST), .flush(1'b0), .en(1'b1), .clk(CLK),
    .imm3(bit_extender_3_out), .imm3_2(id_ex_1_imm3_2));  // open: PredictJump, Branch, PredictJump_2, Branch_2, rs1forward, rs1forward_2, rs2forward, rs2forward_2, URET, URET_2
  Pull_Resistor #(.pull(1)) pull_resistor_1 (.node(CLK));
  Multiplexer #(.select(1), .width(32), .disabled("Z"), .enable("false")) multiplexer_5 (
    .in0(R2), .in1(id_ex_1_imm1_2), .out(multiplexer_5_out), .sel(id_ex_1_alusrcb_2));
  Comparator #(.width(32), .mode("unsigned")) comparator_2 (.a(id_ex_1_r1_2), .b(32'ha), .eq(EX_HALT));  // open: gt, lt
  Shifter #(.width(32), .shift("ll")) shifter_1 (.in(id_ex_1_imm3_2), .\dist (5'b00001), .out(shifter_1_out));
  Shifter #(.width(32), .shift("ll")) shifter_2 (.in(id_ex_1_imm2_2), .\dist (5'b00001), .out(shifter_2_out));
  and and_1 (and_1_out, ~EX_HALT, EX_ecall);  // AND_Gate
  ALU alu_1 (
    .X(id_ex_1_r1_2), .Y(multiplexer_5_out), .AluOP(id_ex_1_aluop_2), .Equal(alu_1_equal),
    .Result(ALU_result), .out_4(alu_1_out_4));  // open: Result_2, out_6
  Adder #(.width(32)) adder_2 (.a(shifter_1_out), .b(EX_PC), .out(J_PC));  // open: cin, cout
  Adder #(.width(32)) adder_3 (.a(shifter_2_out), .b(EX_PC), .out(B_PC));  // open: cin, cout
  Register #(.width(32), .trigger("rising"), .Select("low")) register_1 (
    .D(R2), .en(and_1_out), .Q(LedData), .clk(CLK));  // open: clr
  and and_2 (and_2_out, id_ex_1_beq_2, alu_1_equal);
  and and_3 (and_3_out, id_ex_1_bne_2, ~alu_1_equal);  // AND_Gate
  and and_4 (and_4_out, id_ex_1_bgeu_2, alu_1_out_4);
  or or_1 (EX_B, and_2_out, and_3_out, and_4_out);
  EX_MEM ex_mem_1 (
    .MemToReg(id_ex_1_memtoreg_2), .ALU_result(ALU_result), .MemWrite(id_ex_1_memwrite_2), .WriteData(R2),
    .RegWrite(id_ex_1_regwrite_2), .IR(EX_IR), .JAL(EX_JAL), .PC(EX_PC), .JALR(EX_JALR), .PC_4(EX_PC_4),
    .LBU(EX_LBU), .HALT(EX_HALT), .rd(id_ex_1_rd_2), .MemToReg_2(ex_mem_1_memtoreg_2),
    .ALU_result_2(ex_mem_1_alu_result_2), .MemWrite_2(MemWrite), .WriteData_2(MDin),
    .RegWrite_2(ex_mem_1_regwrite_2), .IR_2(MEM_IR), .JAL_2(ex_mem_1_jal_2), .PC_2(M_PC),
    .JALR_2(ex_mem_1_jalr_2), .PC_4_2(MEM_PC_4), .LBU_2(ex_mem_1_lbu_2), .HALT_2(ex_mem_1_halt_2),
    .rd_2(ex_mem_1_rd_2), .reset(RST), .en(1'b1), .clk(CLK));
  RAM #(.addrWidth(10), .dataWidth(32), .bus("separate"), .Select("high")) ram_1 (
    .addr(ex_mem_1_alu_result_2[11:2]), .din(MDin), .data(ram_1_data), .str(MemWrite), .sel(1'b1), .clk(CLK),
    .ld(1'b1), .clr(RST));
  assign bit_extender_4_out = {{24{1'b0}}, multiplexer_6_out};  // Bit_Extender bit_extender_4
  Multiplexer #(.select(2), .width(8), .disabled("Z"), .enable("false")) multiplexer_6 (
    .in0(ram_1_data[7:0]), .in1(ram_1_data[15:8]), .in2(ram_1_data[23:16]), .in3(ram_1_data[31:24]),
    .out(multiplexer_6_out), .sel(ex_mem_1_alu_result_2[1:0]));
  MEM_WB mem_wb_1 (
    .MemToReg(ex_mem_1_memtoreg_2), .ALU_result(ex_mem_1_alu_result_2), .RegWrite(ex_mem_1_regwrite_2),
    .ReadData(ram_1_data), .JAL(ex_mem_1_jal_2), .IR(MEM_IR), .JALR(ex_mem_1_jalr_2), .PC(M_PC),
    .HALT(ex_mem_1_halt_2), .PC_4(MEM_PC_4), .rd(ex_mem_1_rd_2), .MemToReg_2(mem_wb_1_memtoreg_2),
    .ALU_result_2(mem_wb_1_alu_result_2), .RegWrite_2(RegWrite), .ReadData_2(mem_wb_1_readdata_2),
    .JAL_2(mem_wb_1_jal_2), .IR_2(WB_IR), .JALR_2(mem_wb_1_jalr_2), .PC_2(WB_PC), .HALT_2(mem_wb_1_halt_2),
    .PC_4_2(WB_PC_4), .rd_2(WB_rd), .reset(RST), .en(1'b1), .clk(CLK), .LBU(ex_mem_1_lbu_2),
    .LBU_2(mem_wb_1_lbu_2), .LBU_Data(bit_extender_4_out), .LBU_Data_2(mem_wb_1_lbu_data_2));
  or or_2 (or_2_out, mem_wb_1_jal_2, mem_wb_1_jalr_2);
  Priority_Encoder #(.select(2), .disabled("Z")) priority_encoder_2 (
    .in0(1'b1), .in1(mem_wb_1_memtoreg_2), .in2(mem_wb_1_lbu_2), .in3(or_2_out), .out(priority_encoder_2_out));  // open: gs, en_out, en_in
  Multiplexer #(.select(2), .width(32), .disabled("Z"), .enable("false")) multiplexer_7 (
    .in0(mem_wb_1_alu_result_2), .in1(mem_wb_1_readdata_2), .in2(mem_wb_1_lbu_data_2), .in3(WB_PC_4),
    .out(RDin), .sel(priority_encoder_2_out));
  D_Flip_Flop #(.trigger("rising"), .Pre_Clr_Positions("ABOVE_BELOW"), .NegatePresetClear("false"), .enable("true"), .NewFFLayout("true")) d_ff_2 (
    .clk(mem_wb_1_halt_2), .D(1'b1), .Q(halt), .en(1'b1), .reset(Go));  // open: Qn, preset

  // Other names for the same wires on the sheet: MEM_PC[31:0] = M_PC; WB_RegWrite = RegWrite

  // Notes on the sheet:
  //   中断源
  //   时空图监测，可删除
  //   中断等待指示
  //   数码管输出
  //   指令存储器
  //   contents of rom_1 (hex, n*v repeats v):
  //   413 493 913 993 46413 14e493 296913 39e993 842023 942223 1242423 1342623 a00893 493 913 993 73
  //   指令字
  //   rd
  //   rs1
  //   $a7
  //   rs2
  //   $a0
  //   B型
  //   J型
  //   控制位
  //   流水调试日志用
  //   暂停节拍，不能为0
  //   戳工具置1进入计数暂停模式，ctrl+k时钟自动运行到对应节拍暂停
  //   ctrl+k关闭时钟连续运行，将控制位置零，进入单步调试模式调试
  //   用这个时钟源需要去掉电路中的其他时钟源
  //   可计数暂停的时钟源
  //   这里设置为10是为了过头歌
  //   和任务书中的要求确实有出入
  //   beq
  //   bne
  //   bgeu
  //   为方便自动评测，需要输出流水线各段保存的PC值，注意是PC不是PC+4，另外ID段寄存器写入信息，Mem段内存写入信息也要输出
  //   ALU_result
  //   WriteData
  //   MemWrite
  //   MemToReg
  //   RegWrite
  //   JAL
  //   JALR
  //   ALU_result
  //   LBU_Data
  //   中止必须在这里进行
  //   否则第19（十进制）拍时报错
endmodule

module \气泡流水线  (
  output RegWrite,
  output MemWrite,
  output [31:0] IF_PC,
  output [31:0] ID_PC,
  output [31:0] EX_PC,
  output [31:0] M_PC,
  output [31:0] WB_PC,
  output [31:0] RDin,
  output [31:0] MDin,
  output [31:0] LedData
);

  wire alu_1_equal, alu_1_out_4, and_1_out, and_2_out, and_4_out, and_5_out, and_6_out, and_7_out, and_8_out,
       and_9_out, and_10_out, BranchTaken, CLK, clock_1_out, comparator_1_eq, comparator_1_lt,
       comparator_2_eq, d_ff_1_q, EX_B, EX_ecall, EX_HALT, EX_JAL, EX_JALR, EX_LBU, ex_mem_1_halt_2,
       ex_mem_1_jal_2, ex_mem_1_jalr_2, ex_mem_1_lbu_2, ex_mem_1_memtoreg_2, ex_mem_1_regwrite_2,
       EX_RegWrite, Go, halt, ID_ecall, id_ex_1_alusrcb_2, id_ex_1_beq_2, id_ex_1_bgeu_2, id_ex_1_bne_2,
       id_ex_1_memtoreg_2, id_ex_1_memwrite_2, ID_JAL, ID_JALR, ID_LBU, IR1, IR2, IR3, mem_wb_1_halt_2,
       mem_wb_1_jal_2, mem_wb_1_jalr_2, mem_wb_1_lbu_2, mem_wb_1_memtoreg_2, nand_1_out, not_1_out,
       not_2_out, not_3_out, not_4_out, not_5_out, or_2_out, or_4_out, or_5_out, RST, stall, W1, W2, W3,
       \单周期硬布线控制器_1_alu_src , \单周期硬布线控制器_1_beq , \单周期硬布线控制器_1_bgeu , \单周期硬布线控制器_1_bne ,
       \单周期硬布线控制器_1_memtoreg , \单周期硬布线控制器_1_memwrite , \单周期硬布线控制器_1_regwrite , \单周期硬布线控制器_1_rs1_use ,
       \单周期硬布线控制器_1_rs2_use , \单周期硬布线控制器_1_s_type , \气泡处理逻辑_1_flush ;
  wire [1:0] priority_encoder_1_out, priority_encoder_2_out;
  wire [3:0] id_ex_1_aluop_2, \单周期硬布线控制器_1_alu_op ;
  wire [4:0] EX_rd, MEM_rd, multiplexer_3_out, multiplexer_4_out, WB_rd;
  wire [7:0] multiplexer_6_out;
  wire [11:0] multiplexer_2_out;
  wire [12:0] CNT_num;
  wire [15:0] \LoadUse次数 , \总周期数 , \插入气泡数 , \无条件分支数 , \条件分支成功数 ;
  wire [31:0] ALU_result, B_PC, bit_extender_1_out, bit_extender_2_out, bit_extender_3_out,
       bit_extender_4_out, EX_IR, ex_mem_1_alu_result_2, EX_PC_4, EX_R2, id_ex_1_imm1_2, id_ex_1_imm2_2,
       id_ex_1_imm3_2, id_ex_1_r1_2, ID_IR, ID_PC_4, IF_IR, IF_PC_4, J_PC, MEM_IR, MEM_PC_4,
       mem_wb_1_alu_result_2, mem_wb_1_lbu_data_2, mem_wb_1_readdata_2, multiplexer_1_out, multiplexer_5_out,
       ram_1_data, regifile_1_r1, regifile_1_r2, shifter_1_out, shifter_2_out, WB_IR, WB_PC_4;

  Button \u_总复位  (.out(RST));
  Button _1 (.out(IR1));
  Button _2 (.out(IR2));
  Button _3 (.out(IR3));
  // Probe on \总周期数 
  // Probe on \总周期数 
  // Probe on B_PC
  Button \u_继续运行  (.out(Go));
  LED #(.active("true")) led_1 (.in(W1));
  LED #(.active("true")) led_2 (.in(W2));
  LED #(.active("true")) led_3 (.in(W3));
  // Probe on J_PC
  Hex_Digit_Display hex_digit_display_1 (.value(LedData[31:28]));  // open: dp
  // Probe on IF_PC[19:0]
  // RiscV_Probe riscv_probe_1: pin names not known; wires that end beside it: IF_IR
  \气泡处理逻辑  \u_气泡处理逻辑_1  (
    .EX_rd(EX_rd), .rs1_rs(ID_IR[19:15]), .BranchTaken(BranchTaken), .rs2_rt(ID_IR[24:20]), .MEM_rd(MEM_rd),
    .stall(stall), .flush(\气泡处理逻辑_1_flush ), .rs1_used(\单周期硬布线控制器_1_rs1_use ), .EX_RegWrite(EX_RegWrite),
    .rs2_used(\单周期硬布线控制器_1_rs2_use ), .MEM_RegWrite(ex_mem_1_regwrite_2), .ecall(ID_ecall));
  Priority_Encoder #(.select(2), .disabled("Z")) priority_encoder_1 (
    .in0(1'b1), .in1(EX_B), .in2(EX_JAL), .in3(EX_JALR), .out(priority_encoder_1_out));  // open: gs, en_out, en_in
  and and_1 (and_1_out, ~halt, ~stall);  // AND_Gate
  Multiplexer #(.select(2), .width(32), .disabled("Z"), .enable("false")) multiplexer_1 (
    .in0(IF_PC_4), .in1(B_PC), .in2(J_PC), .in3(ALU_result), .out(multiplexer_1_out),
    .sel(priority_encoder_1_out));
  Hex_Digit_Display hex_digit_display_2 (.value(LedData[23:20]));  // open: dp
  Hex_Digit_Display hex_digit_display_3 (.value(LedData[27:24]));  // open: dp
  // Probe on ID_PC[19:0]
  // RiscV_Probe riscv_probe_2: pin names not known; wires that end beside it: ID_IR
  Register #(.width(32), .trigger("rising"), .Select("low")) PC (
    .D(multiplexer_1_out), .en(and_1_out), .Q(IF_PC), .clk(CLK), .clr(RST));
  Hex_Digit_Display hex_digit_display_4 (.value(LedData[19:16]));  // open: dp
  Hex_Digit_Display hex_digit_display_5 (.value(LedData[15:12]));  // open: dp
  Hex_Digit_Display hex_digit_display_6 (.value(LedData[11:8]));  // open: dp
  Hex_Digit_Display hex_digit_display_7 (.value(LedData[7:4]));  // open: dp
  // Probe on EX_PC[19:0]
  // RiscV_Probe riscv_probe_3: pin names not known; wires that end beside it: EX_IR
  or or_1 (BranchTaken, EX_B, EX_JALR, EX_JAL);
  Hex_Digit_Display hex_digit_display_8 (.value(LedData[3:0]));  // open: dp
  ROM #(.addrWidth(10), .dataWidth(32), .Select("high")) rom_1 (.addr(IF_PC[11:2]), .data(IF_IR));
  Adder #(.width(32)) adder_1 (.a(IF_PC), .b(32'h4), .out(IF_PC_4));  // open: cin, cout
  and and_2 (and_2_out, ~halt, ~stall);  // AND_Gate
  // Probe on \总周期数 
  // Probe on M_PC[19:0]
  // RiscV_Probe riscv_probe_4: pin names not known; wires that end beside it: MEM_IR
  IF_ID if_id_1 (
    .IR(IF_IR), .PC_4(IF_PC_4), .IR_2(ID_IR), .PC_4_2(ID_PC_4), .reset(RST), .BranchTaken(BranchTaken),
    .en(and_2_out), .clk(CLK), .PC(IF_PC), .PC_2(ID_PC));  // open: PredictJump, PredictJump_2
  // Probe on \总周期数 
  // Probe on \无条件分支数 
  // Probe on \条件分支成功数 
  // Probe on \插入气泡数 
  // Probe on \LoadUse次数 
  // Probe on IF_PC[11:0]
  // Probe on WB_PC[19:0]
  // RiscV_Probe riscv_probe_5: pin names not known; wires that end beside it: WB_IR
  Multiplexer #(.select(1), .width(12), .disabled("Z"), .enable("false")) multiplexer_2 (
    .in0(ID_IR[31:20]), .in1({ID_IR[31:25], ID_IR[11:7]}), .out(multiplexer_2_out), .sel(\单周期硬布线控制器_1_s_type ));
  // Probe on EX_PC[11:0]
  // Probe on ID_PC[11:0]
  \单周期硬布线控制器  \u_单周期硬布线控制器_1  (
    .Funct({ID_IR[30], ID_IR[25], ID_IR[14:12]}), .OP(ID_IR[6:2]), .ALU_OP(\单周期硬布线控制器_1_alu_op ),
    .MemToReg(\单周期硬布线控制器_1_memtoreg ), .MemWrite(\单周期硬布线控制器_1_memwrite ), .ALU_SRC(\单周期硬布线控制器_1_alu_src ),
    .RegWrite(\单周期硬布线控制器_1_regwrite ), .ecall(ID_ecall), .S_type(\单周期硬布线控制器_1_s_type ), .Jalr(ID_JALR),
    .Beq(\单周期硬布线控制器_1_beq ), .JAL(ID_JAL), .Bne(\单周期硬布线控制器_1_bne ), .in_3(ID_IR[21]), .LBU(ID_LBU),
    .BGEU(\单周期硬布线控制器_1_bgeu ), .rs1_use(\单周期硬布线控制器_1_rs1_use ), .rs2_use(\单周期硬布线控制器_1_rs2_use ));  // open: uret, CSRRSI, CSEECI
  Multiplexer #(.select(1), .width(5), .disabled("Z"), .enable("false")) multiplexer_3 (
    .in0(ID_IR[19:15]), .in1(5'b10001), .out(multiplexer_3_out), .sel(ID_ecall));
  Multiplexer #(.select(1), .width(5), .disabled("Z"), .enable("false")) multiplexer_4 (
    .in0(ID_IR[24:20]), .in1(5'b01010), .out(multiplexer_4_out), .sel(ID_ecall));
  assign bit_extender_1_out = {{20{multiplexer_2_out[11]}}, multiplexer_2_out};  // Bit_Extender bit_extender_1
  assign bit_extender_2_out = {{20{ID_IR[31]}}, {ID_IR[31], ID_IR[7], ID_IR[30:25], ID_IR[11:8]}};  // Bit_Extender bit_extender_2
  assign bit_extender_3_out = {{12{ID_IR[31]}}, {ID_IR[31], ID_IR[19:12], ID_IR[20], ID_IR[30:21]}};  // Bit_Extender bit_extender_3
  // Probe on M_PC[11:0]
  D_Flip_Flop #(.trigger("high"), .Pre_Clr_Positions("LEGACY"), .NegatePresetClear("false"), .enable("true"), .NewFFLayout("false")) d_ff_1 (.Q(d_ff_1_q));  // open: clk, D, Qn, preset, en, reset
  // Probe on 13'h75
  // Probe on WB_PC[11:0]
  Comparator #(.width(13), .mode("twosComplement")) comparator_1 (
    .a(CNT_num), .b(13'h75), .eq(comparator_1_eq), .lt(comparator_1_lt));  // open: gt
  Clock #(.highDuration(1), .lowDuration(1)) clock_1 (.out(clock_1_out));
  not not_1 (not_1_out, CLK);
  Regifile regifile_1 (
    .Din(RDin), .Clk(not_1_out), .R1(regifile_1_r1), .R2(regifile_1_r2), .WE(RegWrite), .W_num(WB_rd),
    .R1_num(multiplexer_3_out), .R2_num(multiplexer_4_out));
  nand nand_1 (nand_1_out, d_ff_1_q, comparator_1_eq);
  Counter #(.width(13), .max('h1fff), .ongoal("stay"), .trigger("rising"), .behavior("old")) counter_1 (
    .count(comparator_1_lt), .Q(CNT_num), .clk(clock_1_out));  // open: load, D, carry, clr, preset
  not not_2 (not_2_out, halt);
  // Probe on id_ex_1_r1_2
  assign CLK = nand_1_out ? clock_1_out : 1'bz;  // Controlled_Buffer controlled_buffer_1
  ID_EX id_ex_1 (
    .Beq(\单周期硬布线控制器_1_beq ), .R1(regifile_1_r1), .Bgeu(\单周期硬布线控制器_1_bgeu ), .Bne(\单周期硬布线控制器_1_bne ),
    .R2(regifile_1_r2), .MemToReg(\单周期硬布线控制器_1_memtoreg ), .imm1(bit_extender_1_out),
    .MemWrite(\单周期硬布线控制器_1_memwrite ), .imm2(bit_extender_2_out), .RegWrite(\单周期硬布线控制器_1_regwrite ),
    .JAL(ID_JAL), .PC(ID_PC), .JALR(ID_JALR), .PC_4(ID_PC_4), .LBU(ID_LBU), .IR(ID_IR), .ecall(ID_ecall),
    .AluOP(\单周期硬布线控制器_1_alu_op ), .rd(ID_IR[11:7]), .AluSrcB(\单周期硬布线控制器_1_alu_src ), .Beq_2(id_ex_1_beq_2),
    .R1_2(id_ex_1_r1_2), .Bgeu_2(id_ex_1_bgeu_2), .Bne_2(id_ex_1_bne_2), .R2_2(EX_R2),
    .MemToReg_2(id_ex_1_memtoreg_2), .imm1_2(id_ex_1_imm1_2), .MemWrite_2(id_ex_1_memwrite_2),
    .imm2_2(id_ex_1_imm2_2), .RegWrite_2(EX_RegWrite), .JAL_2(EX_JAL), .PC_2(EX_PC), .JALR_2(EX_JALR),
    .PC_4_2(EX_PC_4), .LBU_2(EX_LBU), .IR_2(EX_IR), .ecall_2(EX_ecall), .AluOP_2(id_ex_1_aluop_2),
    .rd_2(EX_rd), .AluSrcB_2(id_ex_1_alusrcb_2), .reset(RST), .flush(\气泡处理逻辑_1_flush ), .en(not_2_out),
    .clk(CLK), .imm3(bit_extender_3_out), .imm3_2(id_ex_1_imm3_2));  // open: PredictJump, Branch, PredictJump_2, Branch_2, rs1forward, rs1forward_2, rs2forward, rs2forward_2, URET, URET_2
  Pull_Resistor #(.pull(1)) pull_resistor_1 (.node(CLK));
  Multiplexer #(.select(1), .width(32), .disabled("Z"), .enable("false")) multiplexer_5 (
    .in0(EX_R2), .in1(id_ex_1_imm1_2), .out(multiplexer_5_out), .sel(id_ex_1_alusrcb_2));
  Comparator #(.width(32), .mode("unsigned")) comparator_2 (
    .a(id_ex_1_r1_2), .b(32'ha), .eq(comparator_2_eq));  // open: gt, lt
  Shifter #(.width(32), .shift("ll")) shifter_1 (.in(id_ex_1_imm3_2), .\dist (5'b00001), .out(shifter_1_out));
  Shifter #(.width(32), .shift("ll")) shifter_2 (.in(id_ex_1_imm2_2), .\dist (5'b00001), .out(shifter_2_out));
  and and_3 (EX_HALT, comparator_2_eq, EX_ecall);
  and and_4 (and_4_out, ~comparator_2_eq, EX_ecall);  // AND_Gate
  // Probe on EX_R2
  Counter #(.width(16), .max('hffff), .ongoal("wrap"), .trigger("rising"), .behavior("old")) counter_2 (
    .count(not_3_out), .Q(\总周期数 ), .clk(CLK), .clr(RST));  // open: load, D, carry, preset
  not not_3 (not_3_out, halt);
  ALU alu_1 (
    .X(id_ex_1_r1_2), .Y(multiplexer_5_out), .AluOP(id_ex_1_aluop_2), .Equal(alu_1_equal),
    .Result(ALU_result), .out_4(alu_1_out_4));  // open: Result_2, out_6
  Adder #(.width(32)) adder_2 (.a(shifter_1_out), .b(EX_PC), .out(J_PC));  // open: cin, cout
  Adder #(.width(32)) adder_3 (.a(shifter_2_out), .b(EX_PC), .out(B_PC));  // open: cin, cout
  Register #(.width(32), .trigger("rising"), .Select("low")) register_1 (
    .D(EX_R2), .en(and_4_out), .Q(LedData), .clk(CLK), .clr(RST));
  and and_5 (and_5_out, not_3_out, or_2_out);
  or or_2 (or_2_out, EX_JAL, EX_JALR);
  and and_6 (and_6_out, id_ex_1_beq_2, alu_1_equal);
  and and_7 (and_7_out, id_ex_1_bne_2, ~alu_1_equal);  // AND_Gate
  and and_8 (and_8_out, id_ex_1_bgeu_2, alu_1_out_4);
  Counter #(.width(16), .max('hffff), .ongoal("wrap"), .trigger("rising"), .behavior("old")) counter_3 (
    .count(and_5_out), .Q(\无条件分支数 ), .clk(CLK), .clr(RST));  // open: load, D, carry, preset
  or or_3 (EX_B, and_6_out, and_7_out, and_8_out);
  // Probe on EX_JAL
  not not_4 (not_4_out, halt);
  // Probe on J_PC
  and and_9 (and_9_out, not_3_out, EX_B);
  EX_MEM ex_mem_1 (
    .MemToReg(id_ex_1_memtoreg_2), .ALU_result(ALU_result), .MemWrite(id_ex_1_memwrite_2), .WriteData(EX_R2),
    .RegWrite(EX_RegWrite), .IR(EX_IR), .JAL(EX_JAL), .PC(EX_PC), .JALR(EX_JALR), .PC_4(EX_PC_4),
    .LBU(EX_LBU), .HALT(EX_HALT), .rd(EX_rd), .MemToReg_2(ex_mem_1_memtoreg_2),
    .ALU_result_2(ex_mem_1_alu_result_2), .MemWrite_2(MemWrite), .WriteData_2(MDin),
    .RegWrite_2(ex_mem_1_regwrite_2), .IR_2(MEM_IR), .JAL_2(ex_mem_1_jal_2), .PC_2(M_PC),
    .JALR_2(ex_mem_1_jalr_2), .PC_4_2(MEM_PC_4), .LBU_2(ex_mem_1_lbu_2), .HALT_2(ex_mem_1_halt_2),
    .rd_2(MEM_rd), .reset(RST), .en(not_4_out), .clk(CLK));
  Counter #(.width(16), .max('hffff), .ongoal("wrap"), .trigger("rising"), .behavior("old")) counter_4 (
    .count(and_9_out), .Q(\条件分支成功数 ), .clk(CLK), .clr(RST));  // open: load, D, carry, preset
  and and_10 (and_10_out, not_3_out, or_4_out);
  Counter #(.width(16), .max('hffff), .ongoal("wrap"), .trigger("rising"), .behavior("old")) counter_5 (
    .count(and_10_out), .Q(\插入气泡数 ), .clk(CLK), .clr(RST));  // open: load, D, carry, preset
  or or_4 (or_4_out, BranchTaken, stall);
  RAM #(.addrWidth(10), .dataWidth(32), .bus("separate"), .Select("high")) ram_1 (
    .addr(ex_mem_1_alu_result_2[11:2]), .din(MDin), .data(ram_1_data), .str(MemWrite), .sel(1'b1), .clk(CLK),
    .ld(1'b1), .clr(RST));
  Multiplexer #(.select(2), .width(8), .disabled("Z"), .enable("false")) multiplexer_6 (
    .in0(ram_1_data[7:0]), .in1(ram_1_data[15:8]), .in2(ram_1_data[23:16]), .in3(ram_1_data[31:24]),
    .out(multiplexer_6_out), .sel(ex_mem_1_alu_result_2[1:0]));
  assign bit_extender_4_out = {{24{1'b0}}, multiplexer_6_out};  // Bit_Extender bit_extender_4
  not not_5 (not_5_out, halt);
  MEM_WB mem_wb_1 (
    .MemToReg(ex_mem_1_memtoreg_2), .ALU_result(ex_mem_1_alu_result_2), .RegWrite(ex_mem_1_regwrite_2),
    .ReadData(ram_1_data), .JAL(ex_mem_1_jal_2), .IR(MEM_IR), .JALR(ex_mem_1_jalr_2), .PC(M_PC),
    .HALT(ex_mem_1_halt_2), .PC_4(MEM_PC_4), .rd(MEM_rd), .MemToReg_2(mem_wb_1_memtoreg_2),
    .ALU_result_2(mem_wb_1_alu_result_2), .RegWrite_2(RegWrite), .ReadData_2(mem_wb_1_readdata_2),
    .JAL_2(mem_wb_1_jal_2), .IR_2(WB_IR), .JALR_2(mem_wb_1_jalr_2), .PC_2(WB_PC), .HALT_2(mem_wb_1_halt_2),
    .PC_4_2(WB_PC_4), .rd_2(WB_rd), .reset(RST), .en(not_5_out), .clk(CLK), .LBU(ex_mem_1_lbu_2),
    .LBU_2(mem_wb_1_lbu_2), .LBU_Data(bit_extender_4_out), .LBU_Data_2(mem_wb_1_lbu_data_2));
  or or_5 (or_5_out, mem_wb_1_jal_2, mem_wb_1_jalr_2);
  Priority_Encoder #(.select(2), .disabled("Z")) priority_encoder_2 (
    .in0(1'b1), .in1(mem_wb_1_memtoreg_2), .in2(mem_wb_1_lbu_2), .in3(or_5_out), .out(priority_encoder_2_out));  // open: gs, en_out, en_in
  Multiplexer #(.select(2), .width(32), .disabled("Z"), .enable("false")) multiplexer_7 (
    .in0(mem_wb_1_alu_result_2), .in1(mem_wb_1_readdata_2), .in2(mem_wb_1_lbu_data_2), .in3(WB_PC_4),
    .out(RDin), .sel(priority_encoder_2_out));
  D_Flip_Flop #(.trigger("rising"), .Pre_Clr_Positions("ABOVE_BELOW"), .NegatePresetClear("false"), .enable("true"), .NewFFLayout("true")) d_ff_2 (
    .clk(mem_wb_1_halt_2), .D(1'b1), .Q(halt), .en(1'b1), .reset(Go));  // open: Qn, preset
  // Probe on RDin
  // Probe on WB_PC_4

  // Other names for the same wires on the sheet: rs2[4:0] = ID_IR[24:20]; rs1[4:0] = ID_IR[19:15];
  //   MEM_PC[31:0] = M_PC; WB_RegWrite = RegWrite

  // Notes on the sheet:
  //   中断源
  //   时空图监测，可删除
  //   中断等待指示
  //   数码管输出
  //   指令存储器
  //   contents of rom_1 (hex, n*v repeats v):
  //   100493 100006f 100493 200913 300993 100006f 100493 200913 300993 100006f 100493 200913 300993
  //   100006f 100493 200913 300993 3d8000ef 100413 100493 1f49493 900533 2200893 73 24d493 48463 fedff06f
  //   900533 2200893 73 100493 249493 900533 2200893 73 48463 fedff06f 100493 1f49493 900533 2200893 73
  //   4034d493 900533 2200893 73 4044d493 900533 2200893 73 4044d493 900533 2200893 73 4044d493 900533
  //   2200893 73 4044d493 900533 2200893 73 4044d493 900533 2200893 73 4044d493 900533 2200893 73 4044d493
  //   900533 2200893 73 100413 1f41993 41f9d993 433 c00913 300b13 140413 f47413 800293 100313 499993
  //   89e9b3 1300533 2200893 73 406282b3 fe0294e3 140413 f00f93 1f47433 1c41413 800293 100313 49d993
  //   89e9b3 1300533 2200893 73 406282b3 fe0294e3 1c45413 406b0b33 b0463 f95ff06f 2b3 fff2c293 829293
  //   ff2e293 500533 2200893 73 fff00413 493 84a023 140413 448493 84a023 140413 448493 84a023 140413
  //   448493 84a023 140413 448493 84a023 140413 448493 84a023 140413 448493 84a023 140413 448493 84a023
  //   140413 448493 84a023 140413 448493 84a023 140413 448493 84a023 140413 448493 84a023 140413 448493
  //   84a023 140413 448493 84a023 140413 448493 84a023 140413 448493 84a023 140413 448493 140413 433
  //   3c00493 42983 4aa03 149a2b3 28663 134a023 1442023 ffc48493 fe9412e3 800533 2200893 73 440413 3c00493
  //   fc9416e3 a00893 73 100293 300313 800493 849493 7648493 900533 2200893 73 800e13 5494b3 6494b3 900533
  //   2200893 73 fffe0e13 fe0e14e3 a00893 73 100293 300313 800493 849493 7648493 1449493 900533 2200893 73
  //   800e13 4054d4b3 4064d4b3 900533 2200893 73 fffe0e13 fe0e14e3 a00893 73 313 1000e13 8400493 849493
  //   8348493 400913 891913 490913 849493 8248493 849493 8148493 891913 490913 891913 490913 932023
  //   12484b3 430313 fffe0e13 fe0e18e3 2000e13 313 34483 900533 2200893 73 130313 fffe0e13 fe0e14e3 a00893
  //   73 f00493 100913 409909b3 900533 2200893 73 fff48493 ff29f6e3 a00893 73 413 140413 800533 2200893 73
  //   240413 800533 2200893 73 340413 800533 2200893 73 440413 800533 2200893 73 540413 800533 2200893 73
  //   640413 800533 2200893 73 740413 800533 2200893 73 840413 800533 2200893 2200893 73 8067
  //   指令字
  //   rd
  //   rs1
  //   $a7
  //   rs2
  //   $a0
  //   B型
  //   J型
  //   控制位
  //   流水调试日志用
  //   暂停节拍，不能为0
  //   戳工具置1进入计数暂停模式，ctrl+k时钟自动运行到对应节拍暂停
  //   ctrl+k关闭时钟连续运行，将控制位置零，进入单步调试模式调试
  //   可计数暂停的时钟源
  //   这里设置为10是为了过头歌
  //   和任务书中的要求确实有出入
  //   beq
  //   bne
  //   bgeu
  //   为方便自动评测，需要输出流水线各段保存的PC值，注意是PC不是PC+4，另外ID段寄存器写入信息，Mem段内存写入信息也要输出
  //   ALU_result
  //   WriteData
  //   MemWrite
  //   MemToReg
  //   RegWrite
  //   JAL
  //   JALR
  //   ALU_result
  //   LBU_Data
  //   中止必须在这里进行
  //   否则第19（十进制）拍时报错
endmodule
module \重定向流水线  (
  output RegWrite,
  output MemWrite,
  output [31:0] IF_PC,
  output [31:0] ID_PC,
  output [31:0] EX_PC,
  output [31:0] M_PC,
  output [31:0] WB_PC,
  output [31:0] RDin,
  output [31:0] MDin,
  output [31:0] LedData
);

  wire alu_1_equal, alu_1_out_4, and_1_out, and_2_out, and_3_out, and_4_out, and_5_out, and_6_out, and_8_out,
       and_9_out, and_10_out, and_11_out, BranchTaken, CLK, clock_1_out, comparator_1_eq, comparator_1_lt,
       comparator_2_eq, d_ff_1_q, EX_B, EX_ecall, EX_HALT, EX_JAL, EX_JALR, EX_LBU, ex_mem_1_halt_2,
       ex_mem_1_jal_2, ex_mem_1_jalr_2, ex_mem_1_lbu_2, ex_mem_1_memtoreg_2, ex_mem_1_regwrite_2,
       EX_RegWrite, Go, halt, ID_ecall, id_ex_1_alusrcb_2, id_ex_1_beq_2, id_ex_1_bgeu_2, id_ex_1_bne_2,
       id_ex_1_memtoreg_2, id_ex_1_memwrite_2, ID_JAL, ID_JALR, ID_LBU, IR1, IR2, IR3, mem_wb_1_halt_2,
       mem_wb_1_jal_2, mem_wb_1_jalr_2, mem_wb_1_lbu_2, mem_wb_1_memtoreg_2, nand_1_out, not_1_out,
       not_2_out, not_3_out, not_4_out, not_5_out, or_2_out, or_4_out, or_5_out, RST, stall, W1, W2, W3,
       \单周期硬布线控制器_1_alu_src , \单周期硬布线控制器_1_beq , \单周期硬布线控制器_1_bgeu , \单周期硬布线控制器_1_bne ,
       \单周期硬布线控制器_1_memtoreg , \单周期硬布线控制器_1_memwrite , \单周期硬布线控制器_1_regwrite , \单周期硬布线控制器_1_rs1_use ,
       \单周期硬布线控制器_1_rs2_use , \单周期硬布线控制器_1_s_type , \重定向处理逻辑_1_flush ;
  wire [1:0] EX_rs1forward, EX_rs2forward, priority_encoder_1_out, priority_encoder_2_out,
       \重定向处理逻辑_1_rs1forward , \重定向处理逻辑_1_rs2forward ;
  wire [3:0] id_ex_1_aluop_2, \单周期硬布线控制器_1_alu_op ;
  wire [4:0] EX_rd, MEM_rd, multiplexer_3_out, multiplexer_4_out, WB_rd;
  wire [7:0] multiplexer_6_out;
  wire [11:0] multiplexer_2_out;
  wire [12:0] CNT_num;
  wire [15:0] \LoadUse次数 , \总周期数 , \插入气泡数 , \无条件分支数 , \条件分支成功数 ;
  wire [31:0] ALU_result, B_PC, bit_extender_1_out, bit_extender_2_out, bit_extender_3_out,
       bit_extender_4_out, EX_IR, EX_PC_4, EX_R1, EX_R2, EX_realR1, EX_realR2, id_ex_1_imm1_2,
       id_ex_1_imm2_2, id_ex_1_imm3_2, ID_IR, ID_PC_4, IF_IR, IF_PC_4, J_PC, MEM_ALU_result, MEM_IR,
       MEM_PC_4, mem_wb_1_alu_result_2, mem_wb_1_lbu_data_2, mem_wb_1_readdata_2, multiplexer_1_out,
       multiplexer_5_out, ram_1_data, regifile_1_r1, regifile_1_r2, shifter_1_out, shifter_2_out, WB_IR,
       WB_PC_4;

  Button \u_总复位  (.out(RST));
  Button _1 (.out(IR1));
  Button _2 (.out(IR2));
  Button _3 (.out(IR3));
  // Probe on \总周期数 
  // Probe on \总周期数 
  Button \u_继续运行  (.out(Go));
  LED #(.active("true")) led_1 (.in(W1));
  LED #(.active("true")) led_2 (.in(W2));
  LED #(.active("true")) led_3 (.in(W3));
  // Probe on B_PC
  Hex_Digit_Display hex_digit_display_1 (.value(LedData[31:28]));  // open: dp
  // Probe on IF_PC[19:0]
  // RiscV_Probe riscv_probe_1: pin names not known; wires that end beside it: IF_IR
  Priority_Encoder #(.select(2), .disabled("Z")) priority_encoder_1 (
    .in0(1'b1), .in1(EX_B), .in2(EX_JAL), .in3(EX_JALR), .out(priority_encoder_1_out));  // open: gs, en_out, en_in
  Multiplexer #(.select(2), .width(32), .disabled("Z"), .enable("false")) multiplexer_1 (
    .in0(IF_PC_4), .in1(B_PC), .in2(J_PC), .in3(ALU_result), .out(multiplexer_1_out),
    .sel(priority_encoder_1_out));
  // Probe on J_PC
  Hex_Digit_Display hex_digit_display_2 (.value(LedData[27:24]));  // open: dp
  Hex_Digit_Display hex_digit_display_3 (.value(LedData[23:20]));  // open: dp
  // Probe on ID_PC[19:0]
  // RiscV_Probe riscv_probe_2: pin names not known; wires that end beside it: ID_IR
  \重定向处理逻辑  \u_重定向处理逻辑_1  (
    .rs1_rs(ID_IR[19:15]), .rs2_rt(ID_IR[24:20]), .rs1_used(\单周期硬布线控制器_1_rs1_use ), .EX_rd(EX_rd),
    .EX_MemToReg(id_ex_1_memtoreg_2), .rs2_used(\单周期硬布线控制器_1_rs2_use ), .MEM_rd(MEM_rd),
    .BranchTaken(BranchTaken), .rs1forward(\重定向处理逻辑_1_rs1forward ), .rs2forward(\重定向处理逻辑_1_rs2forward ),
    .stall(stall), .flush(\重定向处理逻辑_1_flush ), .ecall(ID_ecall), .EX_RegWrite(EX_RegWrite),
    .MEM_RegWrite(ex_mem_1_regwrite_2));
  and and_1 (and_1_out, ~halt, ~stall);  // AND_Gate
  Register #(.width(32), .trigger("rising"), .Select("low")) PC (
    .D(multiplexer_1_out), .en(and_1_out), .Q(IF_PC), .clk(CLK), .clr(RST));
  Hex_Digit_Display hex_digit_display_4 (.value(LedData[19:16]));  // open: dp
  Hex_Digit_Display hex_digit_display_5 (.value(LedData[15:12]));  // open: dp
  Hex_Digit_Display hex_digit_display_6 (.value(LedData[7:4]));  // open: dp
  Hex_Digit_Display hex_digit_display_7 (.value(LedData[11:8]));  // open: dp
  // Probe on EX_PC[19:0]
  // RiscV_Probe riscv_probe_3: pin names not known; wires that end beside it: EX_IR
  or or_1 (BranchTaken, EX_B, EX_JALR, EX_JAL);
  Hex_Digit_Display hex_digit_display_8 (.value(LedData[3:0]));  // open: dp
  ROM #(.addrWidth(10), .dataWidth(32), .Select("high")) rom_1 (.addr(IF_PC[11:2]), .data(IF_IR));
  Adder #(.width(32)) adder_1 (.a(IF_PC), .b(32'h4), .out(IF_PC_4));  // open: cin, cout
  and and_2 (and_2_out, ~halt, ~stall);  // AND_Gate
  // Probe on \总周期数 
  // Probe on M_PC[19:0]
  // RiscV_Probe riscv_probe_4: pin names not known; wires that end beside it: MEM_IR
  IF_ID if_id_1 (
    .IR(IF_IR), .PC_4(IF_PC_4), .IR_2(ID_IR), .PC_4_2(ID_PC_4), .reset(RST), .BranchTaken(BranchTaken),
    .en(and_2_out), .clk(CLK), .PC(IF_PC), .PC_2(ID_PC));  // open: PredictJump, PredictJump_2
  // Probe on \总周期数 
  // Probe on \无条件分支数 
  // Probe on \条件分支成功数 
  // Probe on \插入气泡数 
  // Probe on \LoadUse次数 
  // Probe on IF_PC[11:0]
  // Probe on WB_PC[19:0]
  // RiscV_Probe riscv_probe_5: pin names not known; wires that end beside it: WB_IR
  Multiplexer #(.select(1), .width(12), .disabled("Z"), .enable("false")) multiplexer_2 (
    .in0(ID_IR[31:20]), .in1({ID_IR[31:25], ID_IR[11:7]}), .out(multiplexer_2_out), .sel(\单周期硬布线控制器_1_s_type ));
  // Probe on ID_PC[11:0]
  // Probe on EX_PC[11:0]
  \单周期硬布线控制器  \u_单周期硬布线控制器_1  (
    .Funct({ID_IR[30], ID_IR[25], ID_IR[14:12]}), .OP(ID_IR[6:2]), .ALU_OP(\单周期硬布线控制器_1_alu_op ),
    .MemToReg(\单周期硬布线控制器_1_memtoreg ), .MemWrite(\单周期硬布线控制器_1_memwrite ), .ALU_SRC(\单周期硬布线控制器_1_alu_src ),
    .RegWrite(\单周期硬布线控制器_1_regwrite ), .ecall(ID_ecall), .S_type(\单周期硬布线控制器_1_s_type ), .Jalr(ID_JALR),
    .Beq(\单周期硬布线控制器_1_beq ), .JAL(ID_JAL), .Bne(\单周期硬布线控制器_1_bne ), .in_3(ID_IR[21]), .LBU(ID_LBU),
    .BGEU(\单周期硬布线控制器_1_bgeu ), .rs1_use(\单周期硬布线控制器_1_rs1_use ), .rs2_use(\单周期硬布线控制器_1_rs2_use ));  // open: uret, CSRRSI, CSEECI
  Multiplexer #(.select(1), .width(5), .disabled("Z"), .enable("false")) multiplexer_3 (
    .in0(ID_IR[19:15]), .in1(5'b10001), .out(multiplexer_3_out), .sel(ID_ecall));
  Multiplexer #(.select(1), .width(5), .disabled("Z"), .enable("false")) multiplexer_4 (
    .in0(ID_IR[24:20]), .in1(5'b01010), .out(multiplexer_4_out), .sel(ID_ecall));
  assign bit_extender_1_out = {{20{multiplexer_2_out[11]}}, multiplexer_2_out};  // Bit_Extender bit_extender_1
  assign bit_extender_2_out = {{20{ID_IR[31]}}, {ID_IR[31], ID_IR[7], ID_IR[30:25], ID_IR[11:8]}};  // Bit_Extender bit_extender_2
  assign bit_extender_3_out = {{12{ID_IR[31]}}, {ID_IR[31], ID_IR[19:12], ID_IR[20], ID_IR[30:21]}};  // Bit_Extender bit_extender_3
  // Probe on M_PC[11:0]
  D_Flip_Flop #(.trigger("high"), .Pre_Clr_Positions("LEGACY"), .NegatePresetClear("false"), .enable("true"), .NewFFLayout("false")) d_ff_1 (.Q(d_ff_1_q));  // open: clk, D, Qn, preset, en, reset
  // Probe on 13'he
  // Probe on WB_PC[11:0]
  Comparator #(.width(13), .mode("twosComplement")) comparator_1 (
    .a(CNT_num), .b(13'he), .eq(comparator_1_eq), .lt(comparator_1_lt));  // open: gt
  Clock #(.highDuration(1), .lowDuration(1)) clock_1 (.out(clock_1_out));
  not not_1 (not_1_out, CLK);
  Regifile regifile_1 (
    .Din(RDin), .Clk(not_1_out), .R1(regifile_1_r1), .R2(regifile_1_r2), .WE(RegWrite), .W_num(WB_rd),
    .R1_num(multiplexer_3_out), .R2_num(multiplexer_4_out));
  nand nand_1 (nand_1_out, d_ff_1_q, comparator_1_eq);
  Counter #(.width(13), .max('h1fff), .ongoal("stay"), .trigger("rising"), .behavior("old")) counter_1 (
    .count(comparator_1_lt), .Q(CNT_num), .clk(clock_1_out));  // open: load, D, carry, clr, preset
  not not_2 (not_2_out, halt);
  assign CLK = nand_1_out ? clock_1_out : 1'bz;  // Controlled_Buffer controlled_buffer_1
  ID_EX id_ex_1 (
    .Beq(\单周期硬布线控制器_1_beq ), .R1(regifile_1_r1), .Bgeu(\单周期硬布线控制器_1_bgeu ), .Bne(\单周期硬布线控制器_1_bne ),
    .R2(regifile_1_r2), .MemToReg(\单周期硬布线控制器_1_memtoreg ), .imm1(bit_extender_1_out),
    .MemWrite(\单周期硬布线控制器_1_memwrite ), .imm2(bit_extender_2_out), .RegWrite(\单周期硬布线控制器_1_regwrite ),
    .JAL(ID_JAL), .PC(ID_PC), .JALR(ID_JALR), .PC_4(ID_PC_4), .LBU(ID_LBU), .IR(ID_IR), .ecall(ID_ecall),
    .AluOP(\单周期硬布线控制器_1_alu_op ), .rd(ID_IR[11:7]), .AluSrcB(\单周期硬布线控制器_1_alu_src ), .Beq_2(id_ex_1_beq_2),
    .R1_2(EX_R1), .Bgeu_2(id_ex_1_bgeu_2), .Bne_2(id_ex_1_bne_2), .R2_2(EX_R2),
    .MemToReg_2(id_ex_1_memtoreg_2), .imm1_2(id_ex_1_imm1_2), .MemWrite_2(id_ex_1_memwrite_2),
    .imm2_2(id_ex_1_imm2_2), .RegWrite_2(EX_RegWrite), .JAL_2(EX_JAL), .PC_2(EX_PC), .JALR_2(EX_JALR),
    .PC_4_2(EX_PC_4), .LBU_2(EX_LBU), .IR_2(EX_IR), .ecall_2(EX_ecall), .AluOP_2(id_ex_1_aluop_2),
    .rd_2(EX_rd), .AluSrcB_2(id_ex_1_alusrcb_2), .reset(RST), .flush(\重定向处理逻辑_1_flush ), .en(not_2_out),
    .clk(CLK), .imm3(bit_extender_3_out), .imm3_2(id_ex_1_imm3_2), .rs1forward(\重定向处理逻辑_1_rs1forward ),
    .rs1forward_2(EX_rs1forward), .rs2forward(\重定向处理逻辑_1_rs2forward ), .rs2forward_2(EX_rs2forward));  // open: PredictJump, Branch, PredictJump_2, Branch_2, URET, URET_2
  Pull_Resistor #(.pull(1)) pull_resistor_1 (.node(CLK));
  Multiplexer #(.select(1), .width(32), .disabled("Z"), .enable("false")) multiplexer_5 (
    .in0(EX_realR2), .in1(id_ex_1_imm1_2), .out(multiplexer_5_out), .sel(id_ex_1_alusrcb_2));
  Shifter #(.width(32), .shift("ll")) shifter_1 (.in(id_ex_1_imm3_2), .\dist (5'b00001), .out(shifter_1_out));
  Shifter #(.width(32), .shift("ll")) shifter_2 (.in(id_ex_1_imm2_2), .\dist (5'b00001), .out(shifter_2_out));
  // Probe on EX_realR1
  Counter #(.width(16), .max('hffff), .ongoal("wrap"), .trigger("rising"), .behavior("old")) counter_2 (
    .count(not_3_out), .Q(\总周期数 ), .clk(CLK), .clr(RST));  // open: load, D, carry, preset
  not not_3 (not_3_out, halt);
  ALU alu_1 (
    .X(EX_realR1), .Y(multiplexer_5_out), .AluOP(id_ex_1_aluop_2), .Equal(alu_1_equal), .Result(ALU_result),
    .out_4(alu_1_out_4));  // open: Result_2, out_6
  Adder #(.width(32)) adder_2 (.a(shifter_1_out), .b(EX_PC), .out(J_PC));  // open: cin, cout
  Adder #(.width(32)) adder_3 (.a(shifter_2_out), .b(EX_PC), .out(B_PC));  // open: cin, cout
  and and_3 (and_3_out, not_3_out, or_2_out);
  or or_2 (or_2_out, EX_JAL, EX_JALR);
  and and_4 (and_4_out, id_ex_1_beq_2, alu_1_equal);
  and and_5 (and_5_out, id_ex_1_bne_2, ~alu_1_equal);  // AND_Gate
  and and_6 (and_6_out, id_ex_1_bgeu_2, alu_1_out_4);
  // Probe on J_PC
  Comparator #(.width(32), .mode("unsigned")) comparator_2 (
    .a(EX_realR1), .b(32'ha), .eq(comparator_2_eq));  // open: gt, lt
  Counter #(.width(16), .max('hffff), .ongoal("wrap"), .trigger("rising"), .behavior("old")) counter_3 (
    .count(and_3_out), .Q(\无条件分支数 ), .clk(CLK), .clr(RST));  // open: load, D, carry, preset
  or or_3 (EX_B, and_4_out, and_5_out, and_6_out);
  not not_4 (not_4_out, halt);
  and and_7 (EX_HALT, comparator_2_eq, EX_ecall);
  and and_8 (and_8_out, ~comparator_2_eq, EX_ecall);  // AND_Gate
  // Probe on EX_realR2
  and and_9 (and_9_out, not_3_out, EX_B);
  EX_MEM ex_mem_1 (
    .MemToReg(id_ex_1_memtoreg_2), .ALU_result(ALU_result), .MemWrite(id_ex_1_memwrite_2),
    .WriteData(EX_realR2), .RegWrite(EX_RegWrite), .IR(EX_IR), .JAL(EX_JAL), .PC(EX_PC), .JALR(EX_JALR),
    .PC_4(EX_PC_4), .LBU(EX_LBU), .HALT(EX_HALT), .rd(EX_rd), .MemToReg_2(ex_mem_1_memtoreg_2),
    .ALU_result_2(MEM_ALU_result), .MemWrite_2(MemWrite), .WriteData_2(MDin),
    .RegWrite_2(ex_mem_1_regwrite_2), .IR_2(MEM_IR), .JAL_2(ex_mem_1_jal_2), .PC_2(M_PC),
    .JALR_2(ex_mem_1_jalr_2), .PC_4_2(MEM_PC_4), .LBU_2(ex_mem_1_lbu_2), .HALT_2(ex_mem_1_halt_2),
    .rd_2(MEM_rd), .reset(RST), .en(not_4_out), .clk(CLK));
  // Probe on EX_JAL
  Register #(.width(32), .trigger("rising"), .Select("low")) register_1 (
    .D(EX_realR2), .en(and_8_out), .Q(LedData), .clk(CLK), .clr(RST));
  Counter #(.width(16), .max('hffff), .ongoal("wrap"), .trigger("rising"), .behavior("old")) counter_4 (
    .count(and_9_out), .Q(\条件分支成功数 ), .clk(CLK), .clr(RST));  // open: load, D, carry, preset
  and and_10 (and_10_out, not_3_out, or_4_out);
  Counter #(.width(16), .max('hffff), .ongoal("wrap"), .trigger("rising"), .behavior("old")) counter_5 (
    .count(and_10_out), .Q(\插入气泡数 ), .clk(CLK), .clr(RST));  // open: load, D, carry, preset
  or or_4 (or_4_out, BranchTaken, stall);
  and and_11 (and_11_out, not_3_out, stall);
  RAM #(.addrWidth(10), .dataWidth(32), .bus("separate"), .Select("high")) ram_1 (
    .addr(MEM_ALU_result[11:2]), .din(MDin), .data(ram_1_data), .str(MemWrite), .sel(1'b1), .clk(CLK),
    .ld(1'b1), .clr(RST));
  Counter #(.width(16), .max('hffff), .ongoal("wrap"), .trigger("rising"), .behavior("old")) counter_6 (
    .count(and_11_out), .Q(\LoadUse次数 ), .clk(CLK), .clr(RST));  // open: load, D, carry, preset
  Multiplexer #(.select(2), .width(8), .disabled("Z"), .enable("false")) multiplexer_6 (
    .in0(ram_1_data[7:0]), .in1(ram_1_data[15:8]), .in2(ram_1_data[23:16]), .in3(ram_1_data[31:24]),
    .out(multiplexer_6_out), .sel(MEM_ALU_result[1:0]));
  Multiplexer #(.select(2), .width(32), .disabled("Z"), .enable("false")) multiplexer_7 (
    .in0(EX_R1), .in1(RDin), .in2(MEM_ALU_result), .out(EX_realR1), .sel(EX_rs1forward));  // open: in3
  Multiplexer #(.select(2), .width(32), .disabled("Z"), .enable("false")) multiplexer_8 (
    .in0(EX_R2), .in1(RDin), .in2(MEM_ALU_result), .out(EX_realR2), .sel(EX_rs2forward));  // open: in3
  assign bit_extender_4_out = {{24{1'b0}}, multiplexer_6_out};  // Bit_Extender bit_extender_4
  not not_5 (not_5_out, halt);
  // Probe on EX_rs1forward
  // Probe on EX_rs2forward
  MEM_WB mem_wb_1 (
    .MemToReg(ex_mem_1_memtoreg_2), .ALU_result(MEM_ALU_result), .RegWrite(ex_mem_1_regwrite_2),
    .ReadData(ram_1_data), .JAL(ex_mem_1_jal_2), .IR(MEM_IR), .JALR(ex_mem_1_jalr_2), .PC(M_PC),
    .HALT(ex_mem_1_halt_2), .PC_4(MEM_PC_4), .rd(MEM_rd), .MemToReg_2(mem_wb_1_memtoreg_2),
    .ALU_result_2(mem_wb_1_alu_result_2), .RegWrite_2(RegWrite), .ReadData_2(mem_wb_1_readdata_2),
    .JAL_2(mem_wb_1_jal_2), .IR_2(WB_IR), .JALR_2(mem_wb_1_jalr_2), .PC_2(WB_PC), .HALT_2(mem_wb_1_halt_2),
    .PC_4_2(WB_PC_4), .rd_2(WB_rd), .reset(RST), .en(not_5_out), .clk(CLK), .LBU(ex_mem_1_lbu_2),
    .LBU_2(mem_wb_1_lbu_2), .LBU_Data(bit_extender_4_out), .LBU_Data_2(mem_wb_1_lbu_data_2));
  or or_5 (or_5_out, mem_wb_1_jal_2, mem_wb_1_jalr_2);
  Priority_Encoder #(.select(2), .disabled("Z")) priority_encoder_2 (
    .in0(1'b1), .in1(mem_wb_1_memtoreg_2), .in2(mem_wb_1_lbu_2), .in3(or_5_out), .out(priority_encoder_2_out));  // open: gs, en_out, en_in
  Multiplexer #(.select(2), .width(32), .disabled("Z"), .enable("false")) multiplexer_9 (
    .in0(mem_wb_1_alu_result_2), .in1(mem_wb_1_readdata_2), .in2(mem_wb_1_lbu_data_2), .in3(WB_PC_4),
    .out(RDin), .sel(priority_encoder_2_out));
  D_Flip_Flop #(.trigger("rising"), .Pre_Clr_Positions("ABOVE_BELOW"), .NegatePresetClear("false"), .enable("true"), .NewFFLayout("true")) d_ff_2 (
    .clk(mem_wb_1_halt_2), .D(1'b1), .Q(halt), .en(1'b1), .reset(Go));  // open: Qn, preset
  // Probe on RDin
  // Probe on WB_PC_4

  // Other names for the same wires on the sheet: rs2[4:0] = ID_IR[24:20]; rs1[4:0] = ID_IR[19:15];
  //   MEM_PC[31:0] = M_PC; WB_RegWrite = RegWrite

  // Notes on the sheet:
  //   中断源
  //   时空图监测，可删除
  //   中断等待指示
  //   数码管输出
  //   指令存储器
  //   contents of rom_1 (hex, n*v repeats v):
  //   100493 100006f 100493 200913 300993 100006f 100493 200913 300993 100006f 100493 200913 300993
  //   100006f 100493 200913 300993 3d8000ef 100413 100493 1f49493 900533 2200893 73 24d493 48463 fedff06f
  //   900533 2200893 73 100493 249493 900533 2200893 73 48463 fedff06f 100493 1f49493 900533 2200893 73
  //   4034d493 900533 2200893 73 4044d493 900533 2200893 73 4044d493 900533 2200893 73 4044d493 900533
  //   2200893 73 4044d493 900533 2200893 73 4044d493 900533 2200893 73 4044d493 900533 2200893 73 4044d493
  //   900533 2200893 73 100413 1f41993 41f9d993 433 c00913 300b13 140413 f47413 800293 100313 499993
  //   89e9b3 1300533 2200893 73 406282b3 fe0294e3 140413 f00f93 1f47433 1c41413 800293 100313 49d993
  //   89e9b3 1300533 2200893 73 406282b3 fe0294e3 1c45413 406b0b33 b0463 f95ff06f 2b3 fff2c293 829293
  //   ff2e293 500533 2200893 73 fff00413 493 84a023 140413 448493 84a023 140413 448493 84a023 140413
  //   448493 84a023 140413 448493 84a023 140413 448493 84a023 140413 448493 84a023 140413 448493 84a023
  //   140413 448493 84a023 140413 448493 84a023 140413 448493 84a023 140413 448493 84a023 140413 448493
  //   84a023 140413 448493 84a023 140413 448493 84a023 140413 448493 84a023 140413 448493 140413 433
  //   3c00493 42983 4aa03 149a2b3 28663 134a023 1442023 ffc48493 fe9412e3 800533 2200893 73 440413 3c00493
  //   fc9416e3 a00893 73 100293 300313 800493 849493 7648493 900533 2200893 73 800e13 5494b3 6494b3 900533
  //   2200893 73 fffe0e13 fe0e14e3 a00893 73 100293 300313 800493 849493 7648493 1449493 900533 2200893 73
  //   800e13 4054d4b3 4064d4b3 900533 2200893 73 fffe0e13 fe0e14e3 a00893 73 313 1000e13 8400493 849493
  //   8348493 400913 891913 490913 849493 8248493 849493 8148493 891913 490913 891913 490913 932023
  //   12484b3 430313 fffe0e13 fe0e18e3 2000e13 313 34483 900533 2200893 73 130313 fffe0e13 fe0e14e3 a00893
  //   73 f00493 100913 409909b3 900533 2200893 73 fff48493 ff29f6e3 a00893 73 413 140413 800533 2200893 73
  //   240413 800533 2200893 73 340413 800533 2200893 73 440413 800533 2200893 73 540413 800533 2200893 73
  //   640413 800533 2200893 73 740413 800533 2200893 73 840413 800533 2200893 2200893 73 8067
  //   指令字
  //   rd
  //   rs1
  //   $a7
  //   rs2
  //   $a0
  //   B型
  //   J型
  //   控制位
  //   流水调试日志用
  //   暂停节拍，不能为0
  //   戳工具置1进入计数暂停模式，ctrl+k时钟自动运行到对应节拍暂停
  //   ctrl+k关闭时钟连续运行，将控制位置零，进入单步调试模式调试
  //   可计数暂停的时钟源
  //   ecall指令处理
  //   beq
  //   bne
  //   bgeu
  //   这里设置为10是为了过头歌
  //   和任务书中的要求确实有出入
  //   为方便自动评测，需要输出流水线各段保存的PC值，注意是PC不是PC+4，另外ID段寄存器写入信息，Mem段内存写入信息也要输出
  //   ALU_result
  //   WriteData
  //   MemWrite
  //   EX段重定向处理
  //   即flush数
  //   MemToReg
  //   RegWrite
  //   JAL
  //   JALR
  //   ALU_result
  //   LBU_Data
  //   中止必须在这里进行
  //   否则第19（十进制）拍时报错
endmodule

module \中断按键参考电路  (
  input  \同步清零信号 ,
  output \与中断屏蔽位与 
);

  wire \_1号中断_out , and_1_out, clock_1_out, d_ff_1_q, or_1_out, or_2_out;

  Clock #(.highDuration(1), .lowDuration(1)) clock_1 (.out(clock_1_out));
  Button \_1号中断  (.out(\_1号中断_out ));
  or or_1 (or_1_out, \与中断屏蔽位与 , d_ff_1_q);
  LED #(.active("true")) \_1号中断等待指示灯  (.in(or_1_out));
  D_Flip_Flop #(.trigger("rising"), .Pre_Clr_Positions("LEGACY"), .NegatePresetClear("false"), .enable("true"), .NewFFLayout("false")) d_ff_1 (
    .clk(\_1号中断_out ), .D(1'b1), .Q(d_ff_1_q), .reset(\与中断屏蔽位与 ));  // open: Qn, preset, en
  or or_2 (or_2_out, d_ff_1_q, \与中断屏蔽位与 );
  and and_1 (and_1_out, or_2_out, ~\同步清零信号 );  // AND_Gate
  D_Flip_Flop #(.trigger("rising"), .Pre_Clr_Positions("LEGACY"), .NegatePresetClear("false"), .enable("true"), .NewFFLayout("false")) IR1 (
    .clk(clock_1_out), .D(and_1_out), .Q(\与中断屏蔽位与 ));  // open: Qn, preset, en, reset

  // Notes on the sheet:
  //   中断信号采样参考电路
  //   Reset 
endmodule

module \单周期_单级中断  (
  input  IR1,
  input  IR2,
  input  IR3,
  output RegWrite,
  output MemWrite,
  output [31:0] PC,
  output [31:0] IR,
  output [31:0] RDin,
  output [31:0] MDin,
  output [31:0] LedData
);

  wire alu_1_equal, alu_1_out_4, and_1_out, and_2_out, and_3_out, and_4_out, and_6_out, and_10_out,
       and_11_out, and_12_out, Beq, Bgeu, Bne, \B型 , CLK, clock_1_out, comparator_1_eq, comparator_2_eq,
       comparator_3_eq, comparator_4_eq, comparator_5_eq, comparator_6_eq, comparator_6_lt,
       controlled_inverter_1_out, controlled_inverter_2_out, controlled_inverter_3_out, CSRRCI, CSRRSI,
       d_ff_1_q, d_ff_2_q, d_ff_3_q, d_ff_5_q, d_ff_6_q, d_ff_7_q, d_ff_8_q, decoder_1_out1, decoder_1_out2,
       decoder_1_out3, ecall, Go, halt, INT, INT_IE, INT_IR, IR1_t, IR2_t, IR3_t, IRA, IRA_RST, IRB, IRB_RST,
       IRC, IRC_RST, JAL, JALR, LBU, MemToReg, nand_1_out, not_1_out, not_2_out, not_3_out, or_4_out,
       or_5_out, or_6_out, or_7_out, or_12_out, register_4_q, RST, URET, W1, W2, W3, \单周期硬布线控制器_1_alu_src ,
       \单周期硬布线控制器_1_s_type ;
  wire [1:0] priority_encoder_1_out, priority_encoder_2_out, priority_encoder_3_out, register_3_q;
  wire [3:0] \单周期硬布线控制器_1_alu_op ;
  wire [4:0] multiplexer_5_out, multiplexer_6_out;
  wire [7:0] multiplexer_9_out;
  wire [11:0] multiplexer_7_out;
  wire [12:0] CNT_num;
  wire [15:0] \总周期数 ;
  wire [31:0] adder_1_out, adder_2_out, adder_3_out, ALU_result, and_5_out, bit_extender_1_out,
       bit_extender_2_out, bit_extender_3_out, bit_extender_4_out, INT_PC, multiplexer_2_out,
       multiplexer_3_out, multiplexer_8_out, R1, ram_1_data, shifter_1_out, shifter_2_out, \断点地址 , \返回地址 ;

  Button \u_继续运行  (.out(Go));
  Button _1 (.out(IRA));
  Button _2 (.out(IRB));
  Button _3 (.out(IRC));
  LED #(.active("true")) led_1 (.in(W1));
  LED #(.active("true")) led_2 (.in(W2));
  LED #(.active("true")) led_3 (.in(W3));
  Hex_Digit_Display hex_digit_display_1 (.value(LedData[31:28]));  // open: dp
  Comparator #(.width(16), .mode("twosComplement")) comparator_1 (
    .a(16'h23b), .b(\总周期数 ), .eq(comparator_1_eq));  // open: gt, lt
  Comparator #(.width(16), .mode("twosComplement")) comparator_2 (
    .a(\总周期数 ), .b(16'h1), .eq(comparator_2_eq));  // open: gt, lt
  Comparator #(.width(16), .mode("twosComplement")) comparator_3 (
    .a(\总周期数 ), .b(16'h4), .eq(comparator_3_eq));  // open: gt, lt
  Comparator #(.width(16), .mode("twosComplement")) comparator_4 (
    .a(\总周期数 ), .b(16'h7), .eq(comparator_4_eq));  // open: gt, lt
  Comparator #(.width(32), .mode("unsigned")) comparator_5 (.a(R1), .b(32'ha), .eq(comparator_5_eq));  // open: gt, lt
  // Probe on \返回地址 
  // Probe on \断点地址 
  or or_1 (W1, d_ff_5_q, d_ff_1_q);
  or or_2 (W2, d_ff_6_q, d_ff_2_q);
  or or_3 (W3, d_ff_7_q, d_ff_3_q);
  Hex_Digit_Display hex_digit_display_2 (.value(LedData[23:20]));  // open: dp
  Hex_Digit_Display hex_digit_display_3 (.value(LedData[27:24]));  // open: dp
  or or_4 (or_4_out, comparator_1_eq, comparator_2_eq);
  assign controlled_inverter_1_out = or_4_out ? ~CLK : 1'bz;  // Controlled_Inverter controlled_inverter_1
  assign controlled_inverter_2_out = comparator_3_eq ? ~CLK : 1'bz;  // Controlled_Inverter controlled_inverter_2
  assign controlled_inverter_3_out = comparator_4_eq ? ~CLK : 1'bz;  // Controlled_Inverter controlled_inverter_3
  and and_1 (and_1_out, ~comparator_5_eq, ecall);  // AND_Gate
  D_Flip_Flop #(.trigger("rising"), .Pre_Clr_Positions("LEGACY"), .NegatePresetClear("false"), .enable("true"), .NewFFLayout("false")) d_ff_1 (
    .clk(IRA), .D(1'b1), .Q(d_ff_1_q), .reset(d_ff_5_q));  // open: Qn, preset, en
  D_Flip_Flop #(.trigger("rising"), .Pre_Clr_Positions("LEGACY"), .NegatePresetClear("false"), .enable("true"), .NewFFLayout("false")) d_ff_2 (
    .clk(IRB), .D(1'b1), .Q(d_ff_2_q), .reset(d_ff_6_q));  // open: Qn, preset, en
  D_Flip_Flop #(.trigger("rising"), .Pre_Clr_Positions("LEGACY"), .NegatePresetClear("false"), .enable("true"), .NewFFLayout("false")) d_ff_3 (
    .clk(IRC), .D(1'b1), .Q(d_ff_3_q), .reset(d_ff_7_q));  // open: Qn, preset, en
  Hex_Digit_Display hex_digit_display_4 (.value(LedData[15:12]));  // open: dp
  Hex_Digit_Display hex_digit_display_5 (.value(LedData[19:16]));  // open: dp
  Pull_Resistor #(.pull(0)) pull_resistor_1 (.node(controlled_inverter_1_out));
  Pull_Resistor #(.pull(0)) pull_resistor_2 (.node(controlled_inverter_2_out));
  Pull_Resistor #(.pull(0)) pull_resistor_3 (.node(controlled_inverter_3_out));
  D_Flip_Flop #(.trigger("rising"), .Pre_Clr_Positions("ABOVE_BELOW"), .NegatePresetClear("false"), .enable("true"), .NewFFLayout("true")) d_ff_4 (
    .clk(comparator_5_eq), .D(1'b1), .Q(halt), .en(ecall), .reset(Go));  // open: Qn, preset
  Register #(.width(32), .trigger("rising"), .Select("low")) register_1 (
    .D(MDin), .en(and_1_out), .Q(LedData), .clk(CLK));  // open: clr
  // Probe on PC
  or or_5 (or_5_out, d_ff_1_q, d_ff_5_q);
  or or_6 (or_6_out, d_ff_2_q, d_ff_6_q);
  or or_7 (or_7_out, d_ff_3_q, d_ff_7_q);
  Hex_Digit_Display hex_digit_display_6 (.value(LedData[11:8]));  // open: dp
  Hex_Digit_Display hex_digit_display_7 (.value(LedData[7:4]));  // open: dp
  // Probe on \总周期数 
  and and_2 (and_2_out, or_5_out, ~IRA_RST);  // AND_Gate
  and and_3 (and_3_out, or_6_out, ~IRB_RST);  // AND_Gate
  and and_4 (and_4_out, or_7_out, ~IRC_RST);  // AND_Gate
  Hex_Digit_Display hex_digit_display_8 (.value(LedData[3:0]));  // open: dp
  Priority_Encoder #(.select(2), .disabled("Z")) priority_encoder_1 (
    .in0(1'b1), .in1(\B型 ), .in2(JAL), .in3(JALR), .out(priority_encoder_1_out));  // open: gs, en_out, en_in
  Multiplexer #(.select(2), .width(32), .disabled("Z"), .enable("false")) multiplexer_1 (
    .in0(adder_1_out), .in1(adder_2_out), .in2(adder_3_out), .in3(and_5_out), .out(\断点地址 ),
    .sel(priority_encoder_1_out));
  assign and_5_out = 32'hfffffffe & ALU_result;  // AND_Gate and_5, 32 bits wide
  D_Flip_Flop #(.trigger("rising"), .Pre_Clr_Positions("LEGACY"), .NegatePresetClear("false"), .enable("true"), .NewFFLayout("false")) d_ff_5 (
    .clk(CLK), .D(and_2_out), .Q(d_ff_5_q));  // open: Qn, preset, en, reset
  D_Flip_Flop #(.trigger("rising"), .Pre_Clr_Positions("LEGACY"), .NegatePresetClear("false"), .enable("true"), .NewFFLayout("false")) d_ff_6 (
    .clk(CLK), .D(and_3_out), .Q(d_ff_6_q));  // open: Qn, preset, en, reset
  D_Flip_Flop #(.trigger("rising"), .Pre_Clr_Positions("LEGACY"), .NegatePresetClear("false"), .enable("true"), .NewFFLayout("false")) d_ff_7 (
    .clk(CLK), .D(and_4_out), .Q(d_ff_7_q));  // open: Qn, preset, en, reset
  or or_8 (IR1_t, IR1, IRA);
  Multiplexer #(.select(1), .width(32), .disabled("Z"), .enable("false")) multiplexer_2 (
    .in0(\返回地址 ), .in1(multiplexer_3_out), .out(multiplexer_2_out), .sel(not_1_out));
  Multiplexer #(.select(1), .width(32), .disabled("Z"), .enable("false")) multiplexer_3 (
    .in0(\断点地址 ), .in1(INT_PC), .out(multiplexer_3_out), .sel(INT));
  not not_1 (not_1_out, URET);
  Counter #(.width(16), .max('hffff), .ongoal("wrap"), .trigger("rising"), .behavior("new")) counter_1 (
    .count(not_2_out), .Q(\总周期数 ), .clk(CLK));  // open: load, D, carry, clr, preset, down
  not not_2 (not_2_out, halt);
  Priority_Encoder #(.select(2), .disabled("Z")) priority_encoder_2 (
    .in0(1'b0), .in1(d_ff_5_q), .in2(d_ff_6_q), .in3(d_ff_7_q), .out(priority_encoder_2_out), .gs(INT_IR),
    .en_in(1'b1));  // open: en_out
  or or_9 (IR2_t, IR2, IRB);
  Register #(.width(32), .trigger("rising"), .Select("low")) u_PC (
    .D(multiplexer_2_out), .en(not_3_out), .Q(PC), .clk(CLK), .clr(RST));
  not not_3 (not_3_out, halt);
  Multiplexer #(.select(2), .width(32), .disabled("Z"), .enable("false")) multiplexer_4 (
    .in1(32'h30ac), .in2(32'h3150), .in3(32'h31f4), .out(INT_PC), .sel(priority_encoder_2_out));  // open: in0
  and and_6 (and_6_out, INT_IR, INT_IE);
  Register #(.width(1), .trigger("falling"), .Select("low")) register_2 (
    .D(and_6_out), .Q(INT), .clk(CLK));  // open: en, clr
  Register #(.width(2), .trigger("rising"), .Select("low")) register_3 (
    .D(priority_encoder_2_out), .Q(register_3_q), .clk(INT));  // open: en, clr
  or or_10 (IR3_t, IR3, IRC);
  // RiscV_Probe riscv_probe_1: pin names not known; wires that end beside it: IR
  Decoder #(.select(2), .tristate("false"), .disabled("Z"), .enable("false")) decoder_1 (
    .out1(decoder_1_out1), .out2(decoder_1_out2), .out3(decoder_1_out3), .sel(register_3_q));  // open: out0
  and and_7 (IRA_RST, URET, decoder_1_out1);
  and and_8 (IRB_RST, URET, decoder_1_out2);
  and and_9 (IRC_RST, URET, decoder_1_out3);
  Register #(.width(32), .trigger("rising"), .Select("low")) EPC (
    .D(\断点地址 ), .en(INT), .Q(\返回地址 ), .clk(CLK));  // open: clr
  ROM #(.addrWidth(10), .dataWidth(32), .Select("high")) rom_1 (.addr(PC[11:2]), .data(IR));
  Register #(.width(1), .trigger("falling"), .Select("low")) register_4 (
    .D(1'b0), .en(URET), .Q(register_4_q), .clk(CLK), .preset(INT));  // open: clr, cs
  \单周期硬布线控制器  \u_单周期硬布线控制器_1  (
    .Funct({IR[30], IR[25], IR[14:12]}), .OP(IR[6:2]), .ALU_OP(\单周期硬布线控制器_1_alu_op ), .MemToReg(MemToReg),
    .MemWrite(MemWrite), .ALU_SRC(\单周期硬布线控制器_1_alu_src ), .RegWrite(RegWrite), .ecall(ecall),
    .S_type(\单周期硬布线控制器_1_s_type ), .Jalr(JALR), .Beq(Beq), .JAL(JAL), .Bne(Bne), .in_3(IR[21]), .uret(URET),
    .LBU(LBU), .BGEU(Bgeu), .CSRRSI(CSRRSI), .CSEECI(CSRRCI));  // open: rs1_use, rs2_use
  Multiplexer #(.select(1), .width(5), .disabled("Z"), .enable("false")) multiplexer_5 (
    .in0(IR[19:15]), .in1(5'b10001), .out(multiplexer_5_out), .sel(ecall));
  Multiplexer #(.select(1), .width(5), .disabled("Z"), .enable("false")) multiplexer_6 (
    .in0(IR[24:20]), .in1(5'b01010), .out(multiplexer_6_out), .sel(ecall));
  Multiplexer #(.select(1), .width(12), .disabled("Z"), .enable("false")) multiplexer_7 (
    .in0(IR[31:20]), .in1({IR[31:25], IR[11:7]}), .out(multiplexer_7_out), .sel(\单周期硬布线控制器_1_s_type ));
  assign bit_extender_1_out = {{20{IR[31]}}, {IR[31], IR[7], IR[30:25], IR[11:8]}};  // Bit_Extender bit_extender_1
  assign bit_extender_2_out = {{12{IR[31]}}, {IR[31], IR[19:12], IR[20], IR[30:21]}};  // Bit_Extender bit_extender_2
  not not_4 (INT_IE, register_4_q);
  assign bit_extender_3_out = {{20{multiplexer_7_out[11]}}, multiplexer_7_out};  // Bit_Extender bit_extender_3
  Shifter #(.width(32), .shift("ll")) shifter_1 (.in(bit_extender_1_out), .\dist (5'b00001), .out(shifter_1_out));
  Shifter #(.width(32), .shift("ll")) shifter_2 (.in(bit_extender_2_out), .\dist (5'b00001), .out(shifter_2_out));
  Regifile regifile_1 (
    .Din(RDin), .Clk(CLK), .R1(R1), .R2(MDin), .WE(RegWrite), .W_num(IR[11:7]), .R1_num(multiplexer_5_out),
    .R2_num(multiplexer_6_out));
  Adder #(.width(32)) adder_1 (.a(PC), .b(32'h4), .out(adder_1_out));  // open: cin, cout
  Adder #(.width(32)) adder_2 (.a(shifter_1_out), .b(PC), .out(adder_2_out));  // open: cin, cout
  Adder #(.width(32)) adder_3 (.a(shifter_2_out), .b(PC), .out(adder_3_out));  // open: cin, cout
  Multiplexer #(.select(1), .width(32), .disabled("Z"), .enable("false")) multiplexer_8 (
    .in0(MDin), .in1(bit_extender_3_out), .out(multiplexer_8_out), .sel(\单周期硬布线控制器_1_alu_src ));
  D_Flip_Flop #(.trigger("high"), .Pre_Clr_Positions("LEGACY"), .NegatePresetClear("false"), .enable("true"), .NewFFLayout("false")) d_ff_8 (.Q(d_ff_8_q));  // open: clk, D, Qn, preset, en, reset
  // Probe on 13'hbc
  ALU alu_1 (
    .X(R1), .Y(multiplexer_8_out), .AluOP(\单周期硬布线控制器_1_alu_op ), .Equal(alu_1_equal), .Result(ALU_result),
    .out_4(alu_1_out_4));  // open: Result_2, out_6
  Comparator #(.width(13), .mode("twosComplement")) comparator_6 (
    .a(CNT_num), .b(13'hbc), .eq(comparator_6_eq), .lt(comparator_6_lt));  // open: gt
  Clock #(.highDuration(1), .lowDuration(1)) clock_1 (.out(clock_1_out));
  and and_10 (and_10_out, Beq, alu_1_equal);
  and and_11 (and_11_out, Bne, ~alu_1_equal);  // AND_Gate
  and and_12 (and_12_out, Bgeu, alu_1_out_4);
  Counter #(.width(13), .max('h1fff), .ongoal("stay"), .trigger("rising"), .behavior("old")) counter_2 (
    .count(comparator_6_lt), .Q(CNT_num), .clk(clock_1_out));  // open: load, D, carry, clr, preset
  or or_11 (\B型 , and_10_out, and_11_out, and_12_out);
  nand nand_1 (nand_1_out, d_ff_8_q, comparator_6_eq);
  RAM #(.addrWidth(10), .dataWidth(32), .bus("separate"), .Select("high")) ram_1 (
    .addr(ALU_result[11:2]), .din(MDin), .data(ram_1_data), .str(MemWrite), .sel(1'b1), .clk(CLK), .ld(1'b1),
    .clr(RST));
  assign CLK = nand_1_out ? clock_1_out : 1'bz;  // Controlled_Buffer controlled_buffer_1
  Pull_Resistor #(.pull(1)) pull_resistor_4 (.node(CLK));
  Multiplexer #(.select(2), .width(8), .disabled("Z"), .enable("false")) multiplexer_9 (
    .in0(ram_1_data[7:0]), .in1(ram_1_data[15:8]), .in2(ram_1_data[23:16]), .in3(ram_1_data[31:24]),
    .out(multiplexer_9_out), .sel(ALU_result[1:0]));
  Priority_Encoder #(.select(2), .disabled("Z")) priority_encoder_3 (
    .in0(1'b1), .in1(MemToReg), .in2(LBU), .in3(or_12_out), .out(priority_encoder_3_out));  // open: gs, en_out, en_in
  assign bit_extender_4_out = {{24{1'b0}}, multiplexer_9_out};  // Bit_Extender bit_extender_4
  or or_12 (or_12_out, JAL, JALR);
  Multiplexer #(.select(2), .width(32), .disabled("Z"), .enable("false")) multiplexer_10 (
    .in0(ALU_result), .in1(ram_1_data), .in2(bit_extender_4_out), .in3(adder_1_out), .out(RDin),
    .sel(priority_encoder_3_out));

  // Notes on the sheet:
  //   中断源
  //   中断等待指示
  //   总复位信号应将除ROM以外所有存储组件全部清零
  //   这里设置为10是为了过头歌
  //   和任务书中的要求确实有出入
  //   单级中断测试信号模拟器
  //   数码管输出
  //   数码管输出应该用寄存器锁存，否则显示数据只能一闪而过
  //   INT_IR为1说明有中断请求出现
  //   选择对应的中断程序地址
  //   第二拍：保存断点地址
  //   在出现中断请求后（即IRA/IRB/IRC置为1后）：
  //   第一拍：上升沿：请求到达优先编码器，INT_IR变为1
  //   下降沿：INT变为1，INT_IE变为0
  //   即在第一拍实现关中断的操作，因此逻辑与后面的寄存器与IE的那个寄存器，设置成下降沿是必须的
  //   指令探针
  //   指令存储器
  //   此寄存器必须为上升沿触发，在INT到来时即刻完成中断识别
  //   指令字
  //   contents of rom_1 (hex, n*v repeats v):
  //   7d000113 100413 1f41993 41f9d993 433 c00913 800b13 140413 f47413 800293 100313 499993 89e9b3 1300533
  //   2200893 73 406282b3 fe0294e3 140413 f00f93 1f47433 1c41413 800293 100313 49d993 89e9b3 1300533
  //   2200893 73 406282b3 fe0294e3 1c45413 406b0b33 b0463 f95ff06f 2b3 fff2c293 1029293 fff2e293 500533
  //   2200893 73 f5dff06f 1112023 410113 a12023 410113 812023 410113 1312023 410113 1412023 410113 1512023
  //   410113 1612023 410113 100b13 300a13 100a93 1600433 441413 14469b3 1300533 2200893 73 fe0416e3
  //   415a0a33 fe0a10e3 ffc10113 12b03 ffc10113 12a83 ffc10113 12a03 ffc10113 12983 ffc10113 12403
  //   ffc10113 12503 ffc10113 12883 200073 1112023 410113 a12023 410113 812023 410113 1312023 410113
  //   1412023 410113 1512023 410113 1612023 410113 200b13 300a13 100a93 1600433 441413 14469b3 1300533
  //   2200893 73 fe0416e3 415a0a33 fe0a10e3 ffc10113 12b03 ffc10113 12a83 ffc10113 12a03 ffc10113 12983
  //   ffc10113 12403 ffc10113 12503 ffc10113 12883 200073 1112023 410113 a12023 410113 812023 410113
  //   1312023 410113 1412023 410113 1512023 410113 1612023 410113 300b13 300a13 100a93 1600433 441413
  //   14469b3 1300533 2200893 73 fe0416e3 415a0a33 fe0a10e3 ffc10113 12b03 ffc10113 12a83 ffc10113 12a03
  //   ffc10113 12983 ffc10113 12403 ffc10113 12503 ffc10113 12883 200073
  //   中断识别
  //   JAL
  //   JALR
  //   URET
  //   LBU
  //   $a7
  //   $a0
  //   I型（上）/sw（下）
  //   B型指令立即数
  //   J型指令立即数
  //   注意JALR是I型指令
  //   为方便自动评测，需要输出PC，IR，寄存器堆写如数据RDin
  //   Beq
  //   Bgeu
  //   Bne
  //   MemToReg
  //   MemWrite
  //   AluOP
  //   AluSrcB
  //   RegWrite
  //   S_Type
  //   RAM写使能MemWrite、RAM写入数据MDin等信号
  //   中断使能寄存器IE（初值为1）
  //   AluSrcB为1代表是lw/sw/立即数指令
  //   控制位
  //   暂停节拍，不能为0
  //   戳工具置1进入计数暂停模式，ctrl+k时钟自动运行到对应节拍暂停
  //   ctrl+k关闭时钟连续运行，将控制位置零，进入单步调试模式调试
  //   只有sw指令会往存储器存数据
  //   数据存储器
  //   可计数暂停的时钟源
  //   LBU无符号加载字节指令
endmodule

module \单周期_多级中断  (
  input  IR1,
  input  IR2,
  input  IR3,
  output RegWrite,
  output MemWrite,
  output [31:0] PC,
  output [31:0] IR,
  output [31:0] RDin,
  output [31:0] MDin,
  output [31:0] LedData
);

  wire alu_1_equal, alu_1_out_4, and_1_out, and_2_out, and_3_out, and_4_out, and_6_out, and_7_out, and_8_out,
       and_9_out, and_10_out, and_11_out, and_12_out, Beq, Bgeu, Bne, \B型 , CLK, clock_1_out,
       comparator_1_eq, comparator_2_eq, comparator_3_eq, comparator_4_eq, comparator_5_eq, comparator_6_eq,
       comparator_7_eq, comparator_7_lt, CSRRCI, CSRRSI, d_ff_1_q, d_ff_2_q, d_ff_3_q, d_ff_5_q, d_ff_6_q,
       d_ff_7_q, d_ff_8_q, decoder_1_out1, decoder_1_out2, decoder_1_out3, decoder_2_out0, decoder_2_out1,
       decoder_2_out2, decoder_3_out1, decoder_3_out2, decoder_3_out3, ecall, Go, halt, INT, INT_HIGH,
       INT_IE, IR1_t, IR2_t, IR3_t, IRA, IRA_RST, IRB, IRB_RST, IRC, IRC_RST, JAL, JALR, LBU, MemToReg,
       nand_1_out, not_1_out, not_2_out, not_3_out, or_4_out, or_5_out, or_6_out, or_7_out, or_8_out,
       or_12_out, or_13_out, or_14_out, or_16_out, pull_resistor_1_node, pull_resistor_2_node,
       pull_resistor_3_node, register_3_q, RST, URET, W1, W2, W3, \单周期硬布线控制器_1_alu_src , \单周期硬布线控制器_1_s_type ;
  wire [1:0] case0_q, case1_q, case2_q, counter_2_q, multiplexer_10_out, priority_encoder_1_out,
       priority_encoder_2_out, priority_encoder_3_out, subtractor_1_out;
  wire [3:0] \单周期硬布线控制器_1_alu_op ;
  wire [4:0] multiplexer_6_out, multiplexer_7_out;
  wire [7:0] multiplexer_11_out;
  wire [11:0] multiplexer_8_out;
  wire [12:0] CNT_num;
  wire [15:0] \总周期数 ;
  wire [31:0] adder_1_out, adder_2_out, adder_3_out, ALU_result, and_5_out, bit_extender_1_out,
       bit_extender_2_out, bit_extender_3_out, bit_extender_4_out, INT_PC, multiplexer_2_out,
       multiplexer_3_out, multiplexer_9_out, R1, ram_1_data, shifter_1_out, shifter_2_out, \断点地址 , \返回地址 ,
       \返回地址1 , \返回地址2 , \返回地址3 ;

  Button \u_继续运行  (.out(Go));
  Button _1 (.out(IRA));
  Button _2 (.out(IRB));
  Button _3 (.out(IRC));
  LED #(.active("true")) led_1 (.in(W1));
  LED #(.active("true")) led_2 (.in(W2));
  LED #(.active("true")) led_3 (.in(W3));
  Hex_Digit_Display hex_digit_display_1 (.value(LedData[31:28]));  // open: dp
  Comparator #(.width(16), .mode("twosComplement")) comparator_1 (
    .a(\总周期数 ), .b(16'h7), .eq(comparator_1_eq));  // open: gt, lt
  Comparator #(.width(16), .mode("twosComplement")) comparator_2 (
    .a(\总周期数 ), .b(16'h241), .eq(comparator_2_eq));  // open: gt, lt
  or or_1 (W1, d_ff_5_q, d_ff_1_q);
  or or_2 (W2, d_ff_6_q, d_ff_2_q);
  or or_3 (W3, d_ff_7_q, d_ff_3_q);
  Hex_Digit_Display hex_digit_display_2 (.value(LedData[23:20]));  // open: dp
  Hex_Digit_Display hex_digit_display_3 (.value(LedData[27:24]));  // open: dp
  Comparator #(.width(16), .mode("twosComplement")) comparator_3 (
    .a(16'h258), .b(\总周期数 ), .eq(comparator_3_eq));  // open: gt, lt
  or or_4 (or_4_out, comparator_3_eq, comparator_4_eq);
  Comparator #(.width(16), .mode("twosComplement")) comparator_4 (
    .a(\总周期数 ), .b(16'h1), .eq(comparator_4_eq));  // open: gt, lt
  Comparator #(.width(16), .mode("twosComplement")) comparator_5 (
    .a(\总周期数 ), .b(16'h4), .eq(comparator_5_eq));  // open: gt, lt
  or or_5 (or_5_out, comparator_1_eq, comparator_2_eq);
  Comparator #(.width(32), .mode("unsigned")) comparator_6 (.a(R1), .b(32'ha), .eq(comparator_6_eq));  // open: gt, lt
  D_Flip_Flop #(.trigger("rising"), .Pre_Clr_Positions("LEGACY"), .NegatePresetClear("false"), .enable("true"), .NewFFLayout("false")) d_ff_1 (
    .clk(IRA), .D(1'b1), .Q(d_ff_1_q), .reset(d_ff_5_q));  // open: Qn, preset, en
  D_Flip_Flop #(.trigger("rising"), .Pre_Clr_Positions("LEGACY"), .NegatePresetClear("false"), .enable("true"), .NewFFLayout("false")) d_ff_2 (
    .clk(IRB), .D(1'b1), .Q(d_ff_2_q), .reset(d_ff_6_q));  // open: Qn, preset, en
  D_Flip_Flop #(.trigger("rising"), .Pre_Clr_Positions("LEGACY"), .NegatePresetClear("false"), .enable("true"), .NewFFLayout("false")) d_ff_3 (
    .clk(IRC), .D(1'b1), .Q(d_ff_3_q), .reset(d_ff_7_q));  // open: Qn, preset, en
  Hex_Digit_Display hex_digit_display_4 (.value(LedData[15:12]));  // open: dp
  Hex_Digit_Display hex_digit_display_5 (.value(LedData[19:16]));  // open: dp
  Pull_Resistor #(.pull(0)) pull_resistor_1 (.node(pull_resistor_1_node));
  assign pull_resistor_1_node = or_4_out ? ~CLK : 1'bz;  // Controlled_Inverter controlled_inverter_1
  Pull_Resistor #(.pull(0)) pull_resistor_2 (.node(pull_resistor_2_node));
  assign pull_resistor_2_node = comparator_5_eq ? ~CLK : 1'bz;  // Controlled_Inverter controlled_inverter_2
  Pull_Resistor #(.pull(0)) pull_resistor_3 (.node(pull_resistor_3_node));
  assign pull_resistor_3_node = or_5_out ? ~CLK : 1'bz;  // Controlled_Inverter controlled_inverter_3
  and and_1 (and_1_out, ~comparator_6_eq, ecall);  // AND_Gate
  or or_6 (or_6_out, d_ff_1_q, d_ff_5_q);
  or or_7 (or_7_out, d_ff_2_q, d_ff_6_q);
  or or_8 (or_8_out, d_ff_3_q, d_ff_7_q);
  Hex_Digit_Display hex_digit_display_6 (.value(LedData[11:8]));  // open: dp
  Hex_Digit_Display hex_digit_display_7 (.value(LedData[7:4]));  // open: dp
  // Probe on \总周期数 
  D_Flip_Flop #(.trigger("rising"), .Pre_Clr_Positions("ABOVE_BELOW"), .NegatePresetClear("false"), .enable("true"), .NewFFLayout("true")) d_ff_4 (
    .clk(comparator_6_eq), .D(1'b1), .Q(halt), .en(ecall), .reset(Go));  // open: Qn, preset
  Register #(.width(32), .trigger("rising"), .Select("low")) register_1 (
    .D(MDin), .en(and_1_out), .Q(LedData), .clk(CLK));  // open: clr
  Hex_Digit_Display hex_digit_display_8 (.value(LedData[3:0]));  // open: dp
  and and_2 (and_2_out, or_6_out, ~IRA_RST);  // AND_Gate
  and and_3 (and_3_out, or_7_out, ~IRB_RST);  // AND_Gate
  and and_4 (and_4_out, or_8_out, ~IRC_RST);  // AND_Gate
  Priority_Encoder #(.select(2), .disabled("Z")) priority_encoder_1 (
    .in0(1'b1), .in1(\B型 ), .in2(JAL), .in3(JALR), .out(priority_encoder_1_out));  // open: gs, en_out, en_in
  Multiplexer #(.select(2), .width(32), .disabled("Z"), .enable("false")) multiplexer_1 (
    .in0(adder_1_out), .in1(adder_2_out), .in2(adder_3_out), .in3(and_5_out), .out(\断点地址 ),
    .sel(priority_encoder_1_out));
  assign and_5_out = 32'hfffffffe & ALU_result;  // AND_Gate and_5, 32 bits wide
  D_Flip_Flop #(.trigger("rising"), .Pre_Clr_Positions("LEGACY"), .NegatePresetClear("false"), .enable("true"), .NewFFLayout("false")) d_ff_5 (
    .clk(CLK), .D(and_2_out), .Q(d_ff_5_q));  // open: Qn, preset, en, reset
  D_Flip_Flop #(.trigger("rising"), .Pre_Clr_Positions("LEGACY"), .NegatePresetClear("false"), .enable("true"), .NewFFLayout("false")) d_ff_6 (
    .clk(CLK), .D(and_3_out), .Q(d_ff_6_q));  // open: Qn, preset, en, reset
  D_Flip_Flop #(.trigger("rising"), .Pre_Clr_Positions("LEGACY"), .NegatePresetClear("false"), .enable("true"), .NewFFLayout("false")) d_ff_7 (
    .clk(CLK), .D(and_4_out), .Q(d_ff_7_q));  // open: Qn, preset, en, reset
  or or_9 (IR1_t, IR1, IRA);
  Multiplexer #(.select(1), .width(32), .disabled("Z"), .enable("false")) multiplexer_2 (
    .in0(\断点地址 ), .in1(INT_PC), .out(multiplexer_2_out), .sel(INT));
  not not_1 (not_1_out, halt);
  Priority_Encoder #(.select(2), .disabled("Z")) priority_encoder_2 (
    .in0(1'b1), .in1(d_ff_5_q), .in2(d_ff_6_q), .in3(d_ff_7_q), .out(priority_encoder_2_out), .en_in(1'b1));  // open: gs, en_out
  and and_6 (and_6_out, INT_HIGH, INT_IE);
  or or_10 (IR2_t, IR2, IRB);
  Multiplexer #(.select(1), .width(32), .disabled("Z"), .enable("false")) multiplexer_3 (
    .in0(\返回地址 ), .in1(multiplexer_2_out), .out(multiplexer_3_out), .sel(not_3_out));
  not not_2 (not_2_out, halt);
  not not_3 (not_3_out, URET);
  Counter #(.width(16), .max('hffff), .ongoal("wrap"), .trigger("rising"), .behavior("new")) counter_1 (
    .count(not_1_out), .Q(\总周期数 ), .clk(CLK));  // open: load, D, carry, clr, preset, down
  Multiplexer #(.select(2), .width(32), .disabled("Z"), .enable("false")) multiplexer_4 (
    .in1(32'h30ac), .in2(32'h3158), .in3(32'h3204), .out(INT_PC), .sel(priority_encoder_2_out));  // open: in0
  Register #(.width(1), .trigger("falling"), .Select("low")) register_2 (
    .D(and_6_out), .Q(INT), .clk(CLK));  // open: en, clr
  Register #(.width(32), .trigger("rising"), .Select("low")) u_PC (
    .D(multiplexer_3_out), .en(not_2_out), .Q(PC), .clk(CLK), .clr(RST));
  Decoder #(.select(2), .tristate("false"), .disabled("Z"), .enable("false")) decoder_1 (
    .out1(decoder_1_out1), .out2(decoder_1_out2), .out3(decoder_1_out3), .sel(priority_encoder_2_out));  // open: out0
  or or_11 (IR3_t, IR3, IRC);
  Multiplexer #(.select(2), .width(32), .disabled("Z"), .enable("false")) multiplexer_5 (
    .in1(\返回地址1 ), .in2(\返回地址2 ), .in3(\返回地址3 ), .out(\返回地址 ), .sel(priority_encoder_2_out));  // open: in0
  and and_7 (and_7_out, decoder_1_out3, INT);
  and and_8 (and_8_out, decoder_1_out2, INT);
  and and_9 (and_9_out, decoder_1_out1, INT);
  or or_12 (or_12_out, INT, CSRRCI);
  or or_13 (or_13_out, URET, CSRRSI);
  // RiscV_Probe riscv_probe_1: pin names not known; wires that end beside it: IR
  ROM #(.addrWidth(10), .dataWidth(32), .Select("high")) rom_1 (.addr(PC[11:2]), .data(IR));
  Register #(.width(32), .trigger("rising"), .Select("low")) EPC3 (
    .D(\断点地址 ), .en(and_7_out), .Q(\返回地址3 ), .clk(CLK));  // open: clr
  Register #(.width(32), .trigger("rising"), .Select("low")) EPC2 (
    .D(\断点地址 ), .en(and_8_out), .Q(\返回地址2 ), .clk(CLK));  // open: clr
  Register #(.width(32), .trigger("rising"), .Select("low")) EPC1 (
    .D(\断点地址 ), .en(and_9_out), .Q(\返回地址1 ), .clk(CLK));  // open: clr
  not not_4 (INT_IE, register_3_q);
  Register #(.width(1), .trigger("falling"), .Select("low")) register_3 (
    .D(1'b0), .en(or_13_out), .Q(register_3_q), .clk(CLK), .preset(or_12_out));  // open: clr, cs
  \单周期硬布线控制器  \u_单周期硬布线控制器_1  (
    .Funct({IR[30], IR[25], IR[14:12]}), .OP(IR[6:2]), .ALU_OP(\单周期硬布线控制器_1_alu_op ), .MemToReg(MemToReg),
    .MemWrite(MemWrite), .ALU_SRC(\单周期硬布线控制器_1_alu_src ), .RegWrite(RegWrite), .ecall(ecall),
    .S_type(\单周期硬布线控制器_1_s_type ), .Jalr(JALR), .Beq(Beq), .JAL(JAL), .Bne(Bne), .in_3(IR[21]), .uret(URET),
    .LBU(LBU), .BGEU(Bgeu), .CSRRSI(CSRRSI), .CSEECI(CSRRCI));  // open: rs1_use, rs2_use
  Multiplexer #(.select(1), .width(5), .disabled("Z"), .enable("false")) multiplexer_6 (
    .in0(IR[19:15]), .in1(5'b10001), .out(multiplexer_6_out), .sel(ecall));
  Multiplexer #(.select(1), .width(5), .disabled("Z"), .enable("false")) multiplexer_7 (
    .in0(IR[24:20]), .in1(5'b01010), .out(multiplexer_7_out), .sel(ecall));
  or or_14 (or_14_out, INT, URET);
  Counter #(.width(2), .max('h3), .ongoal("wrap"), .trigger("rising"), .behavior("new")) counter_2 (
    .count(or_14_out), .Q(counter_2_q), .clk(CLK), .down(URET));  // open: load, D, carry, clr, preset
  Multiplexer #(.select(1), .width(12), .disabled("Z"), .enable("false")) multiplexer_8 (
    .in0(IR[31:20]), .in1({IR[31:25], IR[11:7]}), .out(multiplexer_8_out), .sel(\单周期硬布线控制器_1_s_type ));
  assign bit_extender_1_out = {{20{IR[31]}}, {IR[31], IR[7], IR[30:25], IR[11:8]}};  // Bit_Extender bit_extender_1
  assign bit_extender_2_out = {{12{IR[31]}}, {IR[31], IR[19:12], IR[20], IR[30:21]}};  // Bit_Extender bit_extender_2
  Decoder #(.select(2), .tristate("false"), .disabled("Z"), .enable("false")) decoder_2 (
    .out0(decoder_2_out0), .out1(decoder_2_out1), .out2(decoder_2_out2), .sel(counter_2_q));  // open: out3
  assign bit_extender_3_out = {{20{multiplexer_8_out[11]}}, multiplexer_8_out};  // Bit_Extender bit_extender_3
  Adder #(.width(32)) adder_1 (.a(PC), .b(32'h4), .out(adder_1_out));  // open: cin, cout
  Shifter #(.width(32), .shift("ll")) shifter_1 (.in(bit_extender_1_out), .\dist (5'b00001), .out(shifter_1_out));
  Adder #(.width(32)) adder_2 (.a(shifter_1_out), .b(PC), .out(adder_2_out));  // open: cin, cout
  Shifter #(.width(32), .shift("ll")) shifter_2 (.in(bit_extender_2_out), .\dist (5'b00001), .out(shifter_2_out));
  Adder #(.width(32)) adder_3 (.a(shifter_2_out), .b(PC), .out(adder_3_out));  // open: cin, cout
  Regifile regifile_1 (
    .Din(RDin), .Clk(CLK), .R1(R1), .R2(MDin), .WE(RegWrite), .W_num(IR[11:7]), .R1_num(multiplexer_6_out),
    .R2_num(multiplexer_7_out));
  Register #(.width(2), .trigger("rising"), .Select("low")) case0 (
    .D(priority_encoder_2_out), .en(decoder_2_out0), .Q(case0_q), .clk(CLK));  // open: clr
  Register #(.width(2), .trigger("rising"), .Select("low")) case1 (
    .D(priority_encoder_2_out), .en(decoder_2_out1), .Q(case1_q), .clk(CLK));  // open: clr
  Register #(.width(2), .trigger("rising"), .Select("low")) case2 (
    .D(priority_encoder_2_out), .en(decoder_2_out2), .Q(case2_q), .clk(CLK));  // open: clr
  Subtractor #(.width(2)) subtractor_1 (.a(counter_2_q), .b(2'b01), .out(subtractor_1_out));  // open: bin, bout
  D_Flip_Flop #(.trigger("high"), .Pre_Clr_Positions("LEGACY"), .NegatePresetClear("false"), .enable("true"), .NewFFLayout("false")) d_ff_8 (.Q(d_ff_8_q));  // open: clk, D, Qn, preset, en, reset
  // Probe on 13'h10
  Multiplexer #(.select(1), .width(32), .disabled("Z"), .enable("false")) multiplexer_9 (
    .in0(MDin), .in1(bit_extender_3_out), .out(multiplexer_9_out), .sel(\单周期硬布线控制器_1_alu_src ));
  Multiplexer #(.select(2), .width(2), .disabled("Z"), .enable("false")) multiplexer_10 (
    .in0(case0_q), .in1(case1_q), .in2(case2_q), .in3(2'b00), .out(multiplexer_10_out), .sel(subtractor_1_out));
  Comparator #(.width(13), .mode("twosComplement")) comparator_7 (
    .a(CNT_num), .b(13'h10), .eq(comparator_7_eq), .lt(comparator_7_lt));  // open: gt
  Clock #(.highDuration(1), .lowDuration(1)) clock_1 (.out(clock_1_out));
  ALU alu_1 (
    .X(R1), .Y(multiplexer_9_out), .AluOP(\单周期硬布线控制器_1_alu_op ), .Equal(alu_1_equal), .Result(ALU_result),
    .out_4(alu_1_out_4));  // open: Result_2, out_6
  Counter #(.width(13), .max('h1fff), .ongoal("stay"), .trigger("rising"), .behavior("old")) counter_3 (
    .count(comparator_7_lt), .Q(CNT_num), .clk(clock_1_out));  // open: load, D, carry, clr, preset
  and and_10 (and_10_out, Beq, alu_1_equal);
  and and_11 (and_11_out, Bne, ~alu_1_equal);  // AND_Gate
  and and_12 (and_12_out, Bgeu, alu_1_out_4);
  Decoder #(.select(2), .tristate("false"), .disabled("Z"), .enable("false")) decoder_3 (
    .out1(decoder_3_out1), .out2(decoder_3_out2), .out3(decoder_3_out3), .sel(multiplexer_10_out));  // open: out0
  and and_13 (IRB_RST, URET, decoder_3_out2);
  and and_14 (IRA_RST, URET, decoder_3_out1);
  and and_15 (IRC_RST, URET, decoder_3_out3);
  nand nand_1 (nand_1_out, d_ff_8_q, comparator_7_eq);
  or or_15 (\B型 , and_10_out, and_11_out, and_12_out);
  RAM #(.addrWidth(10), .dataWidth(32), .bus("separate"), .Select("high")) ram_1 (
    .addr(ALU_result[11:2]), .din(MDin), .data(ram_1_data), .str(MemWrite), .sel(1'b1), .clk(CLK), .ld(1'b1),
    .clr(RST));
  Comparator #(.width(2), .mode("unsigned")) comparator_8 (
    .a(priority_encoder_2_out), .b(multiplexer_10_out), .gt(INT_HIGH));  // open: eq, lt
  assign CLK = nand_1_out ? clock_1_out : 1'bz;  // Controlled_Buffer controlled_buffer_1
  Pull_Resistor #(.pull(1)) pull_resistor_4 (.node(CLK));
  Multiplexer #(.select(2), .width(8), .disabled("Z"), .enable("false")) multiplexer_11 (
    .in0(ram_1_data[7:0]), .in1(ram_1_data[15:8]), .in2(ram_1_data[23:16]), .in3(ram_1_data[31:24]),
    .out(multiplexer_11_out), .sel(ALU_result[1:0]));
  assign bit_extender_4_out = {{24{1'b0}}, multiplexer_11_out};  // Bit_Extender bit_extender_4
  or or_16 (or_16_out, JAL, JALR);
  Priority_Encoder #(.select(2), .disabled("Z")) priority_encoder_3 (
    .in0(1'b1), .in1(MemToReg), .in2(LBU), .in3(or_16_out), .out(priority_encoder_3_out));  // open: gs, en_out, en_in
  Multiplexer #(.select(2), .width(32), .disabled("Z"), .enable("false")) multiplexer_12 (
    .in0(ALU_result), .in1(ram_1_data), .in2(bit_extender_4_out), .in3(adder_1_out), .out(RDin),
    .sel(priority_encoder_3_out));

  // Notes on the sheet:
  //   中断源
  //   中断等待指示
  //   总复位信号应将除ROM以外所有存储组件全部清零
  //   多级中断测试信号模拟器
  //   这里设置为10是为了过头歌
  //   和任务书中的要求确实有出入
  //   数码管输出
  //   数码管输出应该用寄存器锁存，否则显示数据只能一闪而过
  //   INT_IR为1说明有中断请求出现
  //   选择对应的中断程序地址
  //   指令存储器
  //   指令探针
  //   contents of rom_1 (hex, n*v repeats v):
  //   7d000113 100413 1f41993 41f9d993 433 c00913 800b13 140413 f47413 800293 100313 499993 89e9b3 1300533
  //   2200893 73 406282b3 fe0294e3 140413 f00f93 1f47433 1c41413 800293 100313 49d993 89e9b3 1300533
  //   2200893 73 406282b3 fe0294e3 1c45413 406b0b33 b0463 f95ff06f 2b3 fff2c293 1029293 fff2e293 500533
  //   2200893 73 f5dff06f 1112023 410113 a12023 410113 812023 410113 1312023 410113 1412023 410113 1512023
  //   410113 1612023 410113 40e073 100b13 300a13 100a93 1600433 441413 14469b3 1300533 2200893 73 fe0416e3
  //   415a0a33 fe0a10e3 40f073 ffc10113 12b03 ffc10113 12a83 ffc10113 12a03 ffc10113 12983 ffc10113 12403
  //   ffc10113 12503 ffc10113 12883 200073 1112023 410113 a12023 410113 812023 410113 1312023 410113
  //   1412023 410113 1512023 410113 1612023 410113 40e073 200b13 300a13 100a93 1600433 441413 14469b3
  //   1300533 2200893 73 fe0416e3 415a0a33 fe0a10e3 40f073 ffc10113 12b03 ffc10113 12a83 ffc10113 12a03
  //   ffc10113 12983 ffc10113 12403 ffc10113 12503 ffc10113 12883 200073 1112023 410113 a12023 410113
  //   812023 410113 1312023 410113 1412023 410113 1512023 410113 1612023 410113 40e073 300b13 300a13
  //   100a93 1600433 441413 14469b3 1300533 2200893 73 fe0416e3 415a0a33 fe0a10e3 40f073 ffc10113 12b03
  //   ffc10113 12a83 ffc10113 12a03 ffc10113 12983 ffc10113 12403 ffc10113 12503 ffc10113 12883 200073
  //   JALR
  //   指令字
  //   B型指令立即数
  //   注意JALR是I型指令
  //   为方便自动评测，需要输出PC，IR，寄存器堆写如数据RDin
  //   Beq
  //   JAL
  //   Bgeu
  //   Bne
  //   URET
  //   LBU
  //   $a7
  //   $a0
  //   I型（上）/sw（下）
  //   J型指令立即数
  //   RAM写使能MemWrite、RAM写入数据MDin等信号
  //   MemToReg
  //   MemWrite
  //   AluOP
  //   AluSrcB
  //   RegWrite
  //   S_Type
  //   AluSrcB为1代表是lw/sw/立即数指令
  //   控制位
  //   暂停节拍，不能为0
  //   戳工具置1进入计数暂停模式，ctrl+k时钟自动运行到对应节拍暂停
  //   ctrl+k关闭时钟连续运行，将控制位置零，进入单步调试模式调试
  //   只有sw指令会往存储器存数据
  //   数据存储器
  //   中断识别
  //   可计数暂停的时钟源
  //   LBU无符号加载字节指令
endmodule

module \封装正确性测试  (
);

  wire IR1, IR2, IR3, MemW, RegW;
  wire [31:0] EX_PC, ID_PC, IF_PC, IR, LED, MDin, MDinr, MEM_PC, PC, RDin, RDinr, WB_PC;

  \单周期RISC_V  \u_单周期risc_v_1  (
    .IR1(IR1), .IR2(IR2), .IR3(IR3), .RegWrite(RegW), .MemWrite(MemW), .PC(PC), .IR(IR), .RDin(RDin),
    .MDin(MDin), .LedData(LED));
  \气泡流水线  \u_气泡流水线_1  (
    .RegWrite(RegW), .MemWrite(MemW), .IF_PC(IF_PC), .ID_PC(ID_PC), .EX_PC(EX_PC), .M_PC(MEM_PC),
    .WB_PC(WB_PC), .RDin(RDinr), .MDin(MDinr), .LedData(LED));
  \单周期_单级中断  \u_单周期_单级中断_1  (
    .IR1(IR1), .IR2(IR2), .IR3(IR3), .RegWrite(RegW), .MemWrite(MemW), .PC(PC), .IR(IR), .RDin(RDin),
    .MDin(MDin), .LedData(LED));
  \理想流水线  \u_理想流水线_1  (
    .RegWrite(RegW), .MemWrite(MemW), .IF_PC(IF_PC), .ID_PC(ID_PC), .EX_PC(EX_PC), .M_PC(MEM_PC),
    .WB_PC(WB_PC), .RDin(RDinr), .MDin(MDinr), .LedData(LED));
  \重定向流水线  \u_重定向流水线_1  (
    .RegWrite(RegW), .MemWrite(MemW), .IF_PC(IF_PC), .ID_PC(ID_PC), .EX_PC(EX_PC), .M_PC(MEM_PC),
    .WB_PC(WB_PC), .RDin(RDinr), .MDin(MDinr), .LedData(LED));
  \单周期_多级中断  \u_单周期_多级中断_1  (
    .IR1(IR1), .IR2(IR2), .IR3(IR3), .RegWrite(RegW), .MemWrite(MemW), .PC(PC), .IR(IR), .RDin(RDin),
    .MDin(MDin), .LedData(LED));

  // Notes on the sheet:
  //   单周期封装测试
  //   气泡流水封装测试
  //   单周期+单级中断封装测试
  //   请检查上面封装有无位宽不匹配，引脚标签是否和连接的标签相对应，否则无法在educoder平台上正确测试
  //   理想流水封装测试
  //   重定向流水封装测试
  //   单周期+多级中断封装测试
endmodule

module IF_ID (
  input  [31:0] PC,
  input  [31:0] IR,
  input  [31:0] PC_4,
  input  PredictJump,
  input  BranchTaken,
  input  reset,
  input  en,
  input  clk,
  output [31:0] PC_2,
  output [31:0] IR_2,
  output [31:0] PC_4_2,
  output PredictJump_2
);

  wire multiplexer_4_out;
  wire [31:0] multiplexer_1_out, multiplexer_2_out, multiplexer_3_out;

  Multiplexer #(.select(1), .width(32), .disabled("Z"), .enable("false")) multiplexer_1 (
    .in0(PC), .in1({32{1'b0}}), .out(multiplexer_1_out), .sel(BranchTaken));
  Multiplexer #(.select(1), .width(32), .disabled("Z"), .enable("false")) multiplexer_2 (
    .in0(IR), .in1({32{1'b0}}), .out(multiplexer_2_out), .sel(BranchTaken));
  Multiplexer #(.select(1), .width(32), .disabled("Z"), .enable("false")) multiplexer_3 (
    .in0(PC_4), .in1({32{1'b0}}), .out(multiplexer_3_out), .sel(BranchTaken));
  Multiplexer #(.select(1), .width(1), .disabled("Z"), .enable("false")) multiplexer_4 (
    .in0(PredictJump), .in1(1'b0), .out(multiplexer_4_out), .sel(BranchTaken));
  Register #(.width(32), .trigger("rising"), .Select("low")) register_1 (
    .D(multiplexer_1_out), .en(en), .Q(PC_2), .clk(clk), .clr(reset));
  Register #(.width(32), .trigger("rising"), .Select("low")) register_2 (
    .D(multiplexer_2_out), .en(en), .Q(IR_2), .clk(clk), .clr(reset));
  Register #(.width(32), .trigger("rising"), .Select("low")) register_3 (
    .D(multiplexer_3_out), .en(en), .Q(PC_4_2), .clk(clk), .clr(reset));
  Register #(.width(1), .trigger("rising"), .Select("low")) register_4 (
    .D(multiplexer_4_out), .en(en), .Q(PredictJump_2), .clk(clk), .clr(reset));
endmodule

module ID_EX (
  input  [31:0] imm3,
  input  Beq,
  input  [31:0] R1,
  input  Bgeu,
  input  Bne,
  input  [31:0] R2,
  input  MemToReg,
  input  [31:0] imm1,
  input  MemWrite,
  input  [31:0] imm2,
  input  RegWrite,
  input  JAL,
  input  [31:0] PC,
  input  JALR,
  input  [31:0] PC_4,
  input  LBU,
  input  [31:0] IR,
  input  ecall,
  input  [3:0] AluOP,
  input  PredictJump,
  input  [4:0] rd,
  input  AluSrcB,
  input  [1:0] rs1forward,
  input  Branch,
  input  [1:0] rs2forward,
  input  URET,
  input  flush,
  input  reset,
  input  en,
  input  clk,
  output [31:0] imm3_2,
  output Beq_2,
  output [31:0] R1_2,
  output Bgeu_2,
  output Bne_2,
  output [31:0] R2_2,
  output MemToReg_2,
  output [31:0] imm1_2,
  output MemWrite_2,
  output [31:0] imm2_2,
  output RegWrite_2,
  output JAL_2,
  output [31:0] PC_2,
  output JALR_2,
  output [31:0] PC_4_2,
  output LBU_2,
  output [31:0] IR_2,
  output ecall_2,
  output [3:0] AluOP_2,
  output PredictJump_2,
  output [4:0] rd_2,
  output AluSrcB_2,
  output [1:0] rs1forward_2,
  output Branch_2,
  output [1:0] rs2forward_2,
  output URET_2
);

  wire multiplexer_1_out, multiplexer_2_out, multiplexer_3_out, multiplexer_4_out, multiplexer_5_out,
       multiplexer_6_out, multiplexer_7_out, multiplexer_8_out, multiplexer_9_out, multiplexer_10_out,
       multiplexer_11_out, multiplexer_12_out, multiplexer_13_out, multiplexer_14_out;
  wire [1:0] multiplexer_25_out, multiplexer_26_out;
  wire [3:0] multiplexer_23_out;
  wire [4:0] multiplexer_24_out;
  wire [31:0] multiplexer_15_out, multiplexer_16_out, multiplexer_17_out, multiplexer_18_out,
       multiplexer_19_out, multiplexer_20_out, multiplexer_21_out, multiplexer_22_out;

  Multiplexer #(.select(1), .width(1), .disabled("Z"), .enable("false")) multiplexer_1 (
    .in0(Beq), .in1(1'b0), .out(multiplexer_1_out), .sel(flush));
  Multiplexer #(.select(1), .width(1), .disabled("Z"), .enable("false")) multiplexer_2 (
    .in0(Bgeu), .in1(1'b0), .out(multiplexer_2_out), .sel(flush));
  Multiplexer #(.select(1), .width(1), .disabled("Z"), .enable("false")) multiplexer_3 (
    .in0(Bne), .in1(1'b0), .out(multiplexer_3_out), .sel(flush));
  Multiplexer #(.select(1), .width(1), .disabled("Z"), .enable("false")) multiplexer_4 (
    .in0(MemToReg), .in1(1'b0), .out(multiplexer_4_out), .sel(flush));
  Multiplexer #(.select(1), .width(1), .disabled("Z"), .enable("false")) multiplexer_5 (
    .in0(MemWrite), .in1(1'b0), .out(multiplexer_5_out), .sel(flush));
  Multiplexer #(.select(1), .width(1), .disabled("Z"), .enable("false")) multiplexer_6 (
    .in0(RegWrite), .in1(1'b0), .out(multiplexer_6_out), .sel(flush));
  Multiplexer #(.select(1), .width(1), .disabled("Z"), .enable("false")) multiplexer_7 (
    .in0(JAL), .in1(1'b0), .out(multiplexer_7_out), .sel(flush));
  Multiplexer #(.select(1), .width(1), .disabled("Z"), .enable("false")) multiplexer_8 (
    .in0(JALR), .in1(1'b0), .out(multiplexer_8_out), .sel(flush));
  Multiplexer #(.select(1), .width(1), .disabled("Z"), .enable("false")) multiplexer_9 (
    .in0(LBU), .in1(1'b0), .out(multiplexer_9_out), .sel(flush));
  Multiplexer #(.select(1), .width(1), .disabled("Z"), .enable("false")) multiplexer_10 (
    .in0(ecall), .in1(1'b0), .out(multiplexer_10_out), .sel(flush));
  Multiplexer #(.select(1), .width(1), .disabled("Z"), .enable("false")) multiplexer_11 (
    .in0(PredictJump), .in1(1'b0), .out(multiplexer_11_out), .sel(flush));
  Multiplexer #(.select(1), .width(1), .disabled("Z"), .enable("false")) multiplexer_12 (
    .in0(AluSrcB), .in1(1'b0), .out(multiplexer_12_out), .sel(flush));
  Multiplexer #(.select(1), .width(1), .disabled("Z"), .enable("false")) multiplexer_13 (
    .in0(Branch), .in1(1'b0), .out(multiplexer_13_out), .sel(flush));
  Multiplexer #(.select(1), .width(1), .disabled("Z"), .enable("false")) multiplexer_14 (
    .in0(URET), .in1(1'b0), .out(multiplexer_14_out), .sel(flush));
  Register #(.width(1), .trigger("rising"), .Select("low")) register_1 (
    .D(multiplexer_1_out), .en(en), .Q(Beq_2), .clk(clk), .clr(reset));
  Register #(.width(1), .trigger("rising"), .Select("low")) register_2 (
    .D(multiplexer_2_out), .en(en), .Q(Bgeu_2), .clk(clk), .clr(reset));
  Register #(.width(1), .trigger("rising"), .Select("low")) register_3 (
    .D(multiplexer_3_out), .en(en), .Q(Bne_2), .clk(clk), .clr(reset));
  Register #(.width(1), .trigger("rising"), .Select("low")) register_4 (
    .D(multiplexer_4_out), .en(en), .Q(MemToReg_2), .clk(clk), .clr(reset));
  Register #(.width(1), .trigger("rising"), .Select("low")) register_5 (
    .D(multiplexer_5_out), .en(en), .Q(MemWrite_2), .clk(clk), .clr(reset));
  Register #(.width(1), .trigger("rising"), .Select("low")) register_6 (
    .D(multiplexer_6_out), .en(en), .Q(RegWrite_2), .clk(clk), .clr(reset));
  Register #(.width(1), .trigger("rising"), .Select("low")) register_7 (
    .D(multiplexer_7_out), .en(en), .Q(JAL_2), .clk(clk), .clr(reset));
  Register #(.width(1), .trigger("rising"), .Select("low")) register_8 (
    .D(multiplexer_8_out), .en(en), .Q(JALR_2), .clk(clk), .clr(reset));
  Register #(.width(1), .trigger("rising"), .Select("low")) register_9 (
    .D(multiplexer_9_out), .en(en), .Q(LBU_2), .clk(clk), .clr(reset));
  Register #(.width(1), .trigger("rising"), .Select("low")) register_10 (
    .D(multiplexer_10_out), .en(en), .Q(ecall_2), .clk(clk), .clr(reset));
  Register #(.width(1), .trigger("rising"), .Select("low")) register_11 (
    .D(multiplexer_11_out), .en(en), .Q(PredictJump_2), .clk(clk), .clr(reset));
  Register #(.width(1), .trigger("rising"), .Select("low")) register_12 (
    .D(multiplexer_12_out), .en(en), .Q(AluSrcB_2), .clk(clk), .clr(reset));
  Register #(.width(1), .trigger("rising"), .Select("low")) register_13 (
    .D(multiplexer_13_out), .en(en), .Q(Branch_2), .clk(clk), .clr(reset));
  Register #(.width(1), .trigger("rising"), .Select("low")) register_14 (
    .D(multiplexer_14_out), .en(en), .Q(URET_2), .clk(clk), .clr(reset));
  Multiplexer #(.select(1), .width(32), .disabled("Z"), .enable("false")) multiplexer_15 (
    .in0(imm3), .in1({32{1'b0}}), .out(multiplexer_15_out), .sel(flush));
  Multiplexer #(.select(1), .width(32), .disabled("Z"), .enable("false")) multiplexer_16 (
    .in0(R1), .in1({32{1'b0}}), .out(multiplexer_16_out), .sel(flush));
  Multiplexer #(.select(1), .width(32), .disabled("Z"), .enable("false")) multiplexer_17 (
    .in0(R2), .in1({32{1'b0}}), .out(multiplexer_17_out), .sel(flush));
  Multiplexer #(.select(1), .width(32), .disabled("Z"), .enable("false")) multiplexer_18 (
    .in0(imm1), .in1({32{1'b0}}), .out(multiplexer_18_out), .sel(flush));
  Multiplexer #(.select(1), .width(32), .disabled("Z"), .enable("false")) multiplexer_19 (
    .in0(imm2), .in1({32{1'b0}}), .out(multiplexer_19_out), .sel(flush));
  Multiplexer #(.select(1), .width(32), .disabled("Z"), .enable("false")) multiplexer_20 (
    .in0(PC), .in1({32{1'b0}}), .out(multiplexer_20_out), .sel(flush));
  Multiplexer #(.select(1), .width(32), .disabled("Z"), .enable("false")) multiplexer_21 (
    .in0(PC_4), .in1({32{1'b0}}), .out(multiplexer_21_out), .sel(flush));
  Multiplexer #(.select(1), .width(32), .disabled("Z"), .enable("false")) multiplexer_22 (
    .in0(IR), .in1({32{1'b0}}), .out(multiplexer_22_out), .sel(flush));
  Multiplexer #(.select(1), .width(4), .disabled("Z"), .enable("false")) multiplexer_23 (
    .in0(AluOP), .in1(4'b0000), .out(multiplexer_23_out), .sel(flush));
  Multiplexer #(.select(1), .width(5), .disabled("Z"), .enable("false")) multiplexer_24 (
    .in0(rd), .in1({5{1'b0}}), .out(multiplexer_24_out), .sel(flush));
  Multiplexer #(.select(1), .width(2), .disabled("Z"), .enable("false")) multiplexer_25 (
    .in0(rs1forward), .in1(2'b00), .out(multiplexer_25_out), .sel(flush));
  Multiplexer #(.select(1), .width(2), .disabled("Z"), .enable("false")) multiplexer_26 (
    .in0(rs2forward), .in1(2'b00), .out(multiplexer_26_out), .sel(flush));
  Register #(.width(32), .trigger("rising"), .Select("low")) register_15 (
    .D(multiplexer_15_out), .en(en), .Q(imm3_2), .clk(clk), .clr(reset));
  Register #(.width(32), .trigger("rising"), .Select("low")) register_16 (
    .D(multiplexer_16_out), .en(en), .Q(R1_2), .clk(clk), .clr(reset));
  Register #(.width(32), .trigger("rising"), .Select("low")) register_17 (
    .D(multiplexer_17_out), .en(en), .Q(R2_2), .clk(clk), .clr(reset));
  Register #(.width(32), .trigger("rising"), .Select("low")) register_18 (
    .D(multiplexer_18_out), .en(en), .Q(imm1_2), .clk(clk), .clr(reset));
  Register #(.width(32), .trigger("rising"), .Select("low")) register_19 (
    .D(multiplexer_19_out), .en(en), .Q(imm2_2), .clk(clk), .clr(reset));
  Register #(.width(32), .trigger("rising"), .Select("low")) register_20 (
    .D(multiplexer_20_out), .en(en), .Q(PC_2), .clk(clk), .clr(reset));
  Register #(.width(32), .trigger("rising"), .Select("low")) register_21 (
    .D(multiplexer_21_out), .en(en), .Q(PC_4_2), .clk(clk), .clr(reset));
  Register #(.width(32), .trigger("rising"), .Select("low")) register_22 (
    .D(multiplexer_22_out), .en(en), .Q(IR_2), .clk(clk), .clr(reset));
  Register #(.width(4), .trigger("rising"), .Select("low")) register_23 (
    .D(multiplexer_23_out), .en(en), .Q(AluOP_2), .clk(clk), .clr(reset));
  Register #(.width(5), .trigger("rising"), .Select("low")) register_24 (
    .D(multiplexer_24_out), .en(en), .Q(rd_2), .clk(clk), .clr(reset));
  Register #(.width(2), .trigger("rising"), .Select("low")) register_25 (
    .D(multiplexer_25_out), .en(en), .Q(rs1forward_2), .clk(clk), .clr(reset));
  Register #(.width(2), .trigger("rising"), .Select("low")) register_26 (
    .D(multiplexer_26_out), .en(en), .Q(rs2forward_2), .clk(clk), .clr(reset));
endmodule

module EX_MEM (
  input  MemToReg,
  input  [31:0] ALU_result,
  input  MemWrite,
  input  [31:0] WriteData,
  input  RegWrite,
  input  [31:0] IR,
  input  JAL,
  input  [31:0] PC,
  input  JALR,
  input  [31:0] PC_4,
  input  LBU,
  input  HALT,
  input  [4:0] rd,
  input  reset,
  input  en,
  input  clk,
  output MemToReg_2,
  output [31:0] ALU_result_2,
  output MemWrite_2,
  output [31:0] WriteData_2,
  output RegWrite_2,
  output [31:0] IR_2,
  output JAL_2,
  output [31:0] PC_2,
  output JALR_2,
  output [31:0] PC_4_2,
  output LBU_2,
  output HALT_2,
  output [4:0] rd_2
);

  wire multiplexer_1_out, multiplexer_2_out, multiplexer_3_out, multiplexer_4_out, multiplexer_5_out,
       multiplexer_6_out, multiplexer_7_out;
  wire [4:0] multiplexer_13_out;
  wire [31:0] multiplexer_8_out, multiplexer_9_out, multiplexer_10_out, multiplexer_11_out,
       multiplexer_12_out;

  Multiplexer #(.select(1), .width(1), .disabled("Z"), .enable("false")) multiplexer_1 (
    .in0(MemToReg), .in1(1'b0), .out(multiplexer_1_out), .sel(reset));
  Multiplexer #(.select(1), .width(1), .disabled("Z"), .enable("false")) multiplexer_2 (
    .in0(MemWrite), .in1(1'b0), .out(multiplexer_2_out), .sel(reset));
  Multiplexer #(.select(1), .width(1), .disabled("Z"), .enable("false")) multiplexer_3 (
    .in0(RegWrite), .in1(1'b0), .out(multiplexer_3_out), .sel(reset));
  Multiplexer #(.select(1), .width(1), .disabled("Z"), .enable("false")) multiplexer_4 (
    .in0(JAL), .in1(1'b0), .out(multiplexer_4_out), .sel(reset));
  Multiplexer #(.select(1), .width(1), .disabled("Z"), .enable("false")) multiplexer_5 (
    .in0(JALR), .in1(1'b0), .out(multiplexer_5_out), .sel(reset));
  Multiplexer #(.select(1), .width(1), .disabled("Z"), .enable("false")) multiplexer_6 (
    .in0(LBU), .in1(1'b0), .out(multiplexer_6_out), .sel(reset));
  Multiplexer #(.select(1), .width(1), .disabled("Z"), .enable("false")) multiplexer_7 (
    .in0(HALT), .in1(1'b0), .out(multiplexer_7_out), .sel(reset));
  Register #(.width(1), .trigger("rising"), .Select("low")) register_1 (
    .D(multiplexer_1_out), .en(en), .Q(MemToReg_2), .clk(clk), .clr(reset));
  Register #(.width(1), .trigger("rising"), .Select("low")) register_2 (
    .D(multiplexer_2_out), .en(en), .Q(MemWrite_2), .clk(clk), .clr(reset));
  Register #(.width(1), .trigger("rising"), .Select("low")) register_3 (
    .D(multiplexer_3_out), .en(en), .Q(RegWrite_2), .clk(clk), .clr(reset));
  Register #(.width(1), .trigger("rising"), .Select("low")) register_4 (
    .D(multiplexer_4_out), .en(en), .Q(JAL_2), .clk(clk), .clr(reset));
  Register #(.width(1), .trigger("rising"), .Select("low")) register_5 (
    .D(multiplexer_5_out), .en(en), .Q(JALR_2), .clk(clk), .clr(reset));
  Register #(.width(1), .trigger("rising"), .Select("low")) register_6 (
    .D(multiplexer_6_out), .en(en), .Q(LBU_2), .clk(clk), .clr(reset));
  Register #(.width(1), .trigger("rising"), .Select("low")) register_7 (
    .D(multiplexer_7_out), .en(en), .Q(HALT_2), .clk(clk), .clr(reset));
  Multiplexer #(.select(1), .width(32), .disabled("Z"), .enable("false")) multiplexer_8 (
    .in0(ALU_result), .in1({32{1'b0}}), .out(multiplexer_8_out), .sel(reset));
  Multiplexer #(.select(1), .width(32), .disabled("Z"), .enable("false")) multiplexer_9 (
    .in0(WriteData), .in1({32{1'b0}}), .out(multiplexer_9_out), .sel(reset));
  Multiplexer #(.select(1), .width(32), .disabled("Z"), .enable("false")) multiplexer_10 (
    .in0(IR), .in1({32{1'b0}}), .out(multiplexer_10_out), .sel(reset));
  Multiplexer #(.select(1), .width(32), .disabled("Z"), .enable("false")) multiplexer_11 (
    .in0(PC), .in1({32{1'b0}}), .out(multiplexer_11_out), .sel(reset));
  Multiplexer #(.select(1), .width(32), .disabled("Z"), .enable("false")) multiplexer_12 (
    .in0(PC_4), .in1({32{1'b0}}), .out(multiplexer_12_out), .sel(reset));
  Multiplexer #(.select(1), .width(5), .disabled("Z"), .enable("false")) multiplexer_13 (
    .in0(rd), .in1({5{1'b0}}), .out(multiplexer_13_out), .sel(reset));
  Register #(.width(32), .trigger("rising"), .Select("low")) register_8 (
    .D(multiplexer_8_out), .en(en), .Q(ALU_result_2), .clk(clk), .clr(reset));
  Register #(.width(32), .trigger("rising"), .Select("low")) register_9 (
    .D(multiplexer_9_out), .en(en), .Q(WriteData_2), .clk(clk), .clr(reset));
  Register #(.width(32), .trigger("rising"), .Select("low")) register_10 (
    .D(multiplexer_10_out), .en(en), .Q(IR_2), .clk(clk), .clr(reset));
  Register #(.width(32), .trigger("rising"), .Select("low")) register_11 (
    .D(multiplexer_11_out), .en(en), .Q(PC_2), .clk(clk), .clr(reset));
  Register #(.width(32), .trigger("rising"), .Select("low")) register_12 (
    .D(multiplexer_12_out), .en(en), .Q(PC_4_2), .clk(clk), .clr(reset));
  Register #(.width(5), .trigger("rising"), .Select("low")) register_13 (
    .D(multiplexer_13_out), .en(en), .Q(rd_2), .clk(clk), .clr(reset));
endmodule

module MEM_WB (
  input  LBU,
  input  [31:0] LBU_Data,
  input  MemToReg,
  input  [31:0] ALU_result,
  input  RegWrite,
  input  [31:0] ReadData,
  input  JAL,
  input  [31:0] IR,
  input  JALR,
  input  [31:0] PC,
  input  HALT,
  input  [31:0] PC_4,
  input  [4:0] rd,
  input  reset,
  input  en,
  input  clk,
  output LBU_2,
  output [31:0] LBU_Data_2,
  output MemToReg_2,
  output [31:0] ALU_result_2,
  output RegWrite_2,
  output [31:0] ReadData_2,
  output JAL_2,
  output [31:0] IR_2,
  output JALR_2,
  output [31:0] PC_2,
  output HALT_2,
  output [31:0] PC_4_2,
  output [4:0] rd_2
);

  wire multiplexer_1_out, multiplexer_2_out, multiplexer_3_out, multiplexer_4_out, multiplexer_5_out,
       multiplexer_6_out;
  wire [4:0] multiplexer_7_out;
  wire [31:0] multiplexer_8_out, multiplexer_9_out, multiplexer_10_out, multiplexer_11_out,
       multiplexer_12_out, multiplexer_13_out;

  Multiplexer #(.select(1), .width(1), .disabled("Z"), .enable("false")) multiplexer_1 (
    .in0(LBU), .in1(1'b0), .out(multiplexer_1_out), .sel(reset));
  Multiplexer #(.select(1), .width(1), .disabled("Z"), .enable("false")) multiplexer_2 (
    .in0(MemToReg), .in1(1'b0), .out(multiplexer_2_out), .sel(reset));
  Multiplexer #(.select(1), .width(1), .disabled("Z"), .enable("false")) multiplexer_3 (
    .in0(RegWrite), .in1(1'b0), .out(multiplexer_3_out), .sel(reset));
  Multiplexer #(.select(1), .width(1), .disabled("Z"), .enable("false")) multiplexer_4 (
    .in0(JAL), .in1(1'b0), .out(multiplexer_4_out), .sel(reset));
  Multiplexer #(.select(1), .width(1), .disabled("Z"), .enable("false")) multiplexer_5 (
    .in0(JALR), .in1(1'b0), .out(multiplexer_5_out), .sel(reset));
  Multiplexer #(.select(1), .width(1), .disabled("Z"), .enable("false")) multiplexer_6 (
    .in0(HALT), .in1(1'b0), .out(multiplexer_6_out), .sel(reset));
  Multiplexer #(.select(1), .width(5), .disabled("Z"), .enable("false")) multiplexer_7 (
    .in0(rd), .in1({5{1'b0}}), .out(multiplexer_7_out), .sel(reset));
  Register #(.width(1), .trigger("rising"), .Select("low")) register_1 (
    .D(multiplexer_1_out), .en(en), .Q(LBU_2), .clk(clk), .clr(reset));
  Register #(.width(1), .trigger("rising"), .Select("low")) register_2 (
    .D(multiplexer_2_out), .en(en), .Q(MemToReg_2), .clk(clk), .clr(reset));
  Register #(.width(1), .trigger("rising"), .Select("low")) register_3 (
    .D(multiplexer_3_out), .en(en), .Q(RegWrite_2), .clk(clk), .clr(reset));
  Register #(.width(1), .trigger("rising"), .Select("low")) register_4 (
    .D(multiplexer_4_out), .en(en), .Q(JAL_2), .clk(clk), .clr(reset));
  Register #(.width(1), .trigger("rising"), .Select("low")) register_5 (
    .D(multiplexer_5_out), .en(en), .Q(JALR_2), .clk(clk), .clr(reset));
  Register #(.width(1), .trigger("rising"), .Select("low")) register_6 (
    .D(multiplexer_6_out), .en(en), .Q(HALT_2), .clk(clk), .clr(reset));
  Register #(.width(5), .trigger("rising"), .Select("low")) register_7 (
    .D(multiplexer_7_out), .en(en), .Q(rd_2), .clk(clk), .clr(reset));
  Multiplexer #(.select(1), .width(32), .disabled("Z"), .enable("false")) multiplexer_8 (
    .in0(LBU_Data), .in1({32{1'b0}}), .out(multiplexer_8_out), .sel(reset));
  Multiplexer #(.select(1), .width(32), .disabled("Z"), .enable("false")) multiplexer_9 (
    .in0(ALU_result), .in1({32{1'b0}}), .out(multiplexer_9_out), .sel(reset));
  Multiplexer #(.select(1), .width(32), .disabled("Z"), .enable("false")) multiplexer_10 (
    .in0(ReadData), .in1({32{1'b0}}), .out(multiplexer_10_out), .sel(reset));
  Multiplexer #(.select(1), .width(32), .disabled("Z"), .enable("false")) multiplexer_11 (
    .in0(IR), .in1({32{1'b0}}), .out(multiplexer_11_out), .sel(reset));
  Multiplexer #(.select(1), .width(32), .disabled("Z"), .enable("false")) multiplexer_12 (
    .in0(PC), .in1({32{1'b0}}), .out(multiplexer_12_out), .sel(reset));
  Multiplexer #(.select(1), .width(32), .disabled("Z"), .enable("false")) multiplexer_13 (
    .in0(PC_4), .in1({32{1'b0}}), .out(multiplexer_13_out), .sel(reset));
  Register #(.width(32), .trigger("rising"), .Select("low")) register_8 (
    .D(multiplexer_8_out), .en(en), .Q(LBU_Data_2), .clk(clk), .clr(reset));
  Register #(.width(32), .trigger("rising"), .Select("low")) register_9 (
    .D(multiplexer_9_out), .en(en), .Q(ALU_result_2), .clk(clk), .clr(reset));
  Register #(.width(32), .trigger("rising"), .Select("low")) register_10 (
    .D(multiplexer_10_out), .en(en), .Q(ReadData_2), .clk(clk), .clr(reset));
  Register #(.width(32), .trigger("rising"), .Select("low")) register_11 (
    .D(multiplexer_11_out), .en(en), .Q(IR_2), .clk(clk), .clr(reset));
  Register #(.width(32), .trigger("rising"), .Select("low")) register_12 (
    .D(multiplexer_12_out), .en(en), .Q(PC_2), .clk(clk), .clr(reset));
  Register #(.width(32), .trigger("rising"), .Select("low")) register_13 (
    .D(multiplexer_13_out), .en(en), .Q(PC_4_2), .clk(clk), .clr(reset));
endmodule

// 气 泡 处 理 逻 辑 气 泡 处 理 逻 辑 气 泡 处 理 逻 辑 气 泡 处 理 逻 辑 气 泡 处 理 逻 辑
module \气泡处理逻辑  (
  input  rs1_used,
  input  EX_RegWrite,
  input  [4:0] EX_rd,
  input  [4:0] rs1_rs,
  input  BranchTaken,
  input  [4:0] rs2_rt,
  input  [4:0] MEM_rd,
  input  rs2_used,
  input  MEM_RegWrite,
  input  ecall,
  output stall,
  output flush
);

  wire and_1_out, and_2_out, and_3_out, and_4_out, and_5_out, and_6_out, comparator_1_eq, comparator_2_eq,
       comparator_3_eq, comparator_4_eq, comparator_5_eq, comparator_6_eq, comparator_7_eq, comparator_8_eq,
       comparator_9_eq, comparator_10_eq, comparator_11_eq, comparator_12_eq, or_1_out, or_2_out, or_3_out,
       or_4_out;

  Comparator #(.width(5), .mode("unsigned")) comparator_1 (
    .a({5{1'b0}}), .b(rs1_rs), .eq(comparator_1_eq));  // open: gt, lt
  Comparator #(.width(5), .mode("unsigned")) comparator_2 (
    .a(EX_rd), .b(rs1_rs), .eq(comparator_2_eq));  // open: gt, lt
  Comparator #(.width(5), .mode("unsigned")) comparator_3 (
    .a(rs1_rs), .b(MEM_rd), .eq(comparator_3_eq));  // open: gt, lt
  Comparator #(.width(5), .mode("unsigned")) comparator_4 (
    .a(rs1_rs), .b({5{1'b0}}), .eq(comparator_4_eq));  // open: gt, lt
  Comparator #(.width(5), .mode("unsigned")) comparator_5 (
    .a({5{1'b0}}), .b(rs2_rt), .eq(comparator_5_eq));  // open: gt, lt
  Comparator #(.width(5), .mode("unsigned")) comparator_6 (
    .a(EX_rd), .b(rs2_rt), .eq(comparator_6_eq));  // open: gt, lt
  Comparator #(.width(5), .mode("unsigned")) comparator_7 (
    .a(rs2_rt), .b(MEM_rd), .eq(comparator_7_eq));  // open: gt, lt
  Comparator #(.width(5), .mode("unsigned")) comparator_8 (
    .a(rs2_rt), .b({5{1'b0}}), .eq(comparator_8_eq));  // open: gt, lt
  Comparator #(.width(5), .mode("unsigned")) comparator_9 (
    .a(5'b01010), .b(EX_rd), .eq(comparator_9_eq));  // open: gt, lt
  Comparator #(.width(5), .mode("unsigned")) comparator_10 (
    .a(EX_rd), .b(5'b10001), .eq(comparator_10_eq));  // open: gt, lt
  Comparator #(.width(5), .mode("unsigned")) comparator_11 (
    .a(5'b01010), .b(MEM_rd), .eq(comparator_11_eq));  // open: gt, lt
  Comparator #(.width(5), .mode("unsigned")) comparator_12 (
    .a(MEM_rd), .b(5'b10001), .eq(comparator_12_eq));  // open: gt, lt
  or or_1 (or_1_out, comparator_9_eq, comparator_10_eq);
  or or_2 (or_2_out, comparator_11_eq, comparator_12_eq);
  and and_1 (and_1_out, ~comparator_1_eq, rs1_used, EX_RegWrite, comparator_2_eq);  // AND_Gate
  and and_2 (and_2_out, comparator_3_eq, rs1_used, MEM_RegWrite, ~comparator_4_eq);  // AND_Gate
  and and_3 (and_3_out, ~comparator_5_eq, EX_RegWrite, rs2_used, comparator_6_eq);  // AND_Gate
  and and_4 (and_4_out, comparator_7_eq, MEM_RegWrite, rs2_used, ~comparator_8_eq);  // AND_Gate
  and and_5 (and_5_out, or_1_out, EX_RegWrite, ecall);
  and and_6 (and_6_out, ecall, MEM_RegWrite, or_2_out);
  or or_3 (or_3_out, and_1_out, and_2_out, and_3_out, and_4_out);
  or or_4 (or_4_out, and_5_out, and_6_out);
  or or_5 (stall, or_3_out, or_4_out);
  or or_6 (flush, stall, BranchTaken);

  // Other names for the same wires on the sheet: DataHazzard = stall

  // Notes on the sheet:
  //   ecall指令支持
endmodule

// 重 定 向 处 理 逻 辑 重 定 向 处 理 逻 辑 重 定 向 处 理 逻 辑 重 定 向 处 理 逻 辑 重 定 向 处 理 逻 辑
module \重定向处理逻辑  (
  input  [4:0] rs1_rs,
  input  [4:0] rs2_rt,
  input  rs1_used,
  input  [4:0] EX_rd,
  input  EX_MemToReg,
  input  rs2_used,
  input  ecall,
  input  EX_RegWrite,
  input  [4:0] MEM_rd,
  input  MEM_RegWrite,
  input  BranchTaken,
  output [1:0] rs1forward,
  output [1:0] rs2forward,
  output stall,
  output flush
);

  wire _1, _2, _3, _4, and_1_out, and_2_out, and_7_out, and_8_out, and_9_out, and_10_out, comparator_1_eq,
       comparator_2_eq, comparator_3_eq, comparator_4_eq, comparator_5_eq, comparator_6_eq, comparator_7_eq,
       comparator_8_eq, comparator_9_eq, comparator_10_eq, comparator_11_eq, comparator_12_eq,
       comparator_13_eq, comparator_14_eq, comparator_15_eq, comparator_16_eq, or_4_out, or_6_out;

  Comparator #(.width(5), .mode("unsigned")) comparator_1 (
    .a(EX_rd), .b(rs1_rs), .eq(comparator_1_eq));  // open: gt, lt
  Comparator #(.width(5), .mode("unsigned")) comparator_2 (
    .a(rs1_rs), .b({5{1'b0}}), .eq(comparator_2_eq));  // open: gt, lt
  Comparator #(.width(5), .mode("unsigned")) comparator_3 (
    .a({5{1'b0}}), .b(rs2_rt), .eq(comparator_3_eq));  // open: gt, lt
  Comparator #(.width(5), .mode("unsigned")) comparator_4 (
    .a(rs2_rt), .b(EX_rd), .eq(comparator_4_eq));  // open: gt, lt
  Comparator #(.width(5), .mode("unsigned")) comparator_5 (
    .a(EX_rd), .b(5'b10001), .eq(comparator_5_eq));  // open: gt, lt
  Comparator #(.width(5), .mode("unsigned")) comparator_6 (
    .a(EX_rd), .b(5'b01010), .eq(comparator_6_eq));  // open: gt, lt
  Comparator #(.width(5), .mode("unsigned")) comparator_7 (
    .a(5'b10001), .b(MEM_rd), .eq(comparator_7_eq));  // open: gt, lt
  Comparator #(.width(5), .mode("unsigned")) comparator_8 (
    .a(5'b01010), .b(MEM_rd), .eq(comparator_8_eq));  // open: gt, lt
  or or_1 (flush, stall, BranchTaken);
  and and_1 (and_1_out, rs1_used, comparator_1_eq, ~comparator_2_eq, EX_MemToReg);  // AND_Gate
  and and_2 (and_2_out, EX_MemToReg, ~comparator_3_eq, comparator_4_eq, rs2_used);  // AND_Gate
  and and_3 (_1, ecall, comparator_5_eq, EX_RegWrite);
  and and_4 (_3, ecall, comparator_6_eq, EX_RegWrite);
  and and_5 (_2, ecall, comparator_7_eq, MEM_RegWrite);
  and and_6 (_4, ecall, comparator_8_eq, MEM_RegWrite);
  or or_2 (stall, and_1_out, and_2_out);
  Comparator #(.width(5), .mode("unsigned")) comparator_9 (
    .a({5{1'b0}}), .b(rs1_rs), .eq(comparator_9_eq));  // open: gt, lt
  Comparator #(.width(5), .mode("unsigned")) comparator_10 (
    .a(rs1_rs), .b(EX_rd), .eq(comparator_10_eq));  // open: gt, lt
  Comparator #(.width(5), .mode("unsigned")) comparator_11 (
    .a({5{1'b0}}), .b(rs1_rs), .eq(comparator_11_eq));  // open: gt, lt
  Comparator #(.width(5), .mode("unsigned")) comparator_12 (
    .a(rs1_rs), .b(MEM_rd), .eq(comparator_12_eq));  // open: gt, lt
  Comparator #(.width(5), .mode("unsigned")) comparator_13 (
    .a({5{1'b0}}), .b(rs2_rt), .eq(comparator_13_eq));  // open: gt, lt
  Comparator #(.width(5), .mode("unsigned")) comparator_14 (
    .a(rs2_rt), .b(EX_rd), .eq(comparator_14_eq));  // open: gt, lt
  Comparator #(.width(5), .mode("unsigned")) comparator_15 (
    .a({5{1'b0}}), .b(rs2_rt), .eq(comparator_15_eq));  // open: gt, lt
  Comparator #(.width(5), .mode("unsigned")) comparator_16 (
    .a(rs2_rt), .b(MEM_rd), .eq(comparator_16_eq));  // open: gt, lt
  and and_7 (and_7_out, ~comparator_9_eq, rs1_used, EX_RegWrite, comparator_10_eq);  // AND_Gate
  and and_8 (and_8_out, ~comparator_11_eq, rs1_used, MEM_RegWrite, comparator_12_eq);  // AND_Gate
  and and_9 (and_9_out, ~comparator_13_eq, rs2_used, EX_RegWrite, comparator_14_eq);  // AND_Gate
  and and_10 (and_10_out, ~comparator_15_eq, rs2_used, MEM_RegWrite, comparator_16_eq);  // AND_Gate
  or or_3 (rs1forward[1], and_7_out, _1);
  or or_4 (or_4_out, and_8_out, _2);
  or or_5 (rs2forward[1], and_9_out, _3);
  or or_6 (or_6_out, and_10_out, _4);
  and and_11 (rs1forward[0], ~rs1forward[1], or_4_out);  // AND_Gate
  and and_12 (rs2forward[0], ~rs2forward[1], or_6_out);  // AND_Gate

  // Other names for the same wires on the sheet: LoadUse = stall; rs1[4:0] = rs1_rs; rs2[4:0] = rs2_rt

  // Notes on the sheet:
  //   支持ecall指令
  //   1、2是rd与$a7寄存器编号相等，重定向rs1
  //   3、4是rd与$a0寄存器编号相等，重定向rs2
  //   LoadUse计算方法详见课本P274公式
  //   计算方法详见课本P274公式
endmodule
module \流水线单级中断  (
  output RegWrite,
  output MemWrite,
  output [31:0] IF_PC,
  output [31:0] ID_PC,
  output [31:0] EX_PC,
  output [31:0] M_PC,
  output [31:0] WB_PC,
  output [31:0] RDin,
  output [31:0] MDin,
  output [31:0] LedData
);

  wire alu_1_equal, alu_1_out_4, and_1_out, and_2_out, and_3_out, and_4_out, and_5_out, and_6_out,
       and_10_out, and_11_out, and_12_out, and_13_out, and_14_out, and_15_out, and_16_out, and_18_out,
       BranchTaken, CLK, clock_1_out, comparator_1_eq, comparator_1_lt, comparator_2_eq, d_ff_1_q, d_ff_2_q,
       d_ff_3_q, d_ff_4_q, d_ff_5_q, d_ff_6_q, d_ff_7_q, d_ff_8_q, decoder_1_out1, decoder_1_out2,
       decoder_1_out3, EX_B, EX_ecall, EX_HALT, EX_JAL, EX_JALR, EX_LBU, ex_mem_1_halt_2, ex_mem_1_jal_2,
       ex_mem_1_jalr_2, ex_mem_1_lbu_2, ex_mem_1_memtoreg_2, ex_mem_1_regwrite_2, EX_RegWrite, EX_URET, Go,
       halt, ID_ecall, id_ex_1_alusrcb_2, id_ex_1_beq_2, id_ex_1_bgeu_2, id_ex_1_bne_2, id_ex_1_memtoreg_2,
       id_ex_1_memwrite_2, ID_JAL, ID_JALR, ID_LBU, ID_URET, INT, INT_IE, INT_IR, IRA, IRA_RST, IRB, IRB_RST,
       IRC, IRC_RST, mem_wb_1_halt_2, mem_wb_1_jal_2, mem_wb_1_jalr_2, mem_wb_1_lbu_2, mem_wb_1_memtoreg_2,
       nand_1_out, not_1_out, not_2_out, not_3_out, not_5_out, not_6_out, not_7_out, or_4_out, or_5_out,
       or_6_out, or_8_out, or_10_out, or_11_out, or_13_out, or_14_out, register_3_q, RST, stall, W1, W2, W3,
       \中断flush , \单周期硬布线控制器_1_alu_src , \单周期硬布线控制器_1_beq , \单周期硬布线控制器_1_bgeu , \单周期硬布线控制器_1_bne ,
       \单周期硬布线控制器_1_memtoreg , \单周期硬布线控制器_1_memwrite , \单周期硬布线控制器_1_regwrite , \单周期硬布线控制器_1_rs1_use ,
       \单周期硬布线控制器_1_rs2_use , \单周期硬布线控制器_1_s_type , \重定向处理逻辑_1_flush ;
  wire [1:0] EX_rs1forward, EX_rs2forward, priority_encoder_1_out, priority_encoder_2_out,
       priority_encoder_3_out, register_2_q, \重定向处理逻辑_1_rs1forward , \重定向处理逻辑_1_rs2forward ;
  wire [3:0] id_ex_1_aluop_2, \单周期硬布线控制器_1_alu_op ;
  wire [4:0] EX_rd, MEM_rd, multiplexer_8_out, multiplexer_9_out, WB_rd;
  wire [7:0] multiplexer_11_out;
  wire [11:0] multiplexer_7_out;
  wire [12:0] CNT_num;
  wire [15:0] \LoadUse次数 , \总周期数 , \插入气泡数 , \无条件分支数 , \条件分支成功数 ;
  wire [31:0] ALU_result, B_PC, bit_extender_1_out, bit_extender_2_out, bit_extender_3_out,
       bit_extender_4_out, EX_IR, EX_PC_4, EX_R1, EX_R2, EX_realR1, EX_realR2, id_ex_1_imm1_2,
       id_ex_1_imm2_2, id_ex_1_imm3_2, ID_IR, ID_PC_4, IF_IR, IF_PC_4, \IF_PC_前 , INT_PC, J_PC,
       MEM_ALU_result, MEM_IR, MEM_PC_4, mem_wb_1_alu_result_2, mem_wb_1_lbu_data_2, mem_wb_1_readdata_2,
       multiplexer_2_out, multiplexer_3_out, multiplexer_4_out, multiplexer_10_out, ram_1_data,
       regifile_1_r1, regifile_1_r2, shifter_1_out, shifter_2_out, WB_IR, WB_PC_4, \断点地址 , \返回地址 ;

  Button \u_总复位  (.out(RST));
  Button _1 (.out(IRA));
  Button _2 (.out(IRB));
  Button _3 (.out(IRC));
  // Probe on \总周期数 
  // Probe on \总周期数 
  Button \u_继续运行  (.out(Go));
  LED #(.active("true")) led_1 (.in(W1));
  LED #(.active("true")) led_2 (.in(W2));
  LED #(.active("true")) led_3 (.in(W3));
  // Probe on B_PC
  Hex_Digit_Display hex_digit_display_1 (.value(LedData[31:28]));  // open: dp
  // Probe on IF_PC[19:0]
  // RiscV_Probe riscv_probe_1: pin names not known; wires that end beside it: IF_IR
  // Probe on \返回地址 
  // Probe on \断点地址 
  // Probe on \IF_PC_前 
  Priority_Encoder #(.select(2), .disabled("Z")) priority_encoder_1 (
    .in0(1'b1), .in1(EX_B), .in2(EX_JAL), .in3(EX_JALR), .out(priority_encoder_1_out));  // open: gs, en_out, en_in
  Multiplexer #(.select(2), .width(32), .disabled("Z"), .enable("false")) multiplexer_1 (
    .in0(IF_PC_4), .in1(B_PC), .in2(J_PC), .in3(ALU_result), .out(\IF_PC_前 ), .sel(priority_encoder_1_out));
  // Probe on J_PC
  Hex_Digit_Display hex_digit_display_2 (.value(LedData[23:20]));  // open: dp
  Hex_Digit_Display hex_digit_display_3 (.value(LedData[27:24]));  // open: dp
  // Probe on ID_PC[19:0]
  // RiscV_Probe riscv_probe_2: pin names not known; wires that end beside it: ID_IR
  or or_1 (W1, d_ff_5_q, d_ff_2_q);
  or or_2 (W2, d_ff_6_q, d_ff_3_q);
  or or_3 (W3, d_ff_7_q, d_ff_4_q);
  D_Flip_Flop #(.trigger("rising"), .Pre_Clr_Positions("LEGACY"), .NegatePresetClear("false"), .enable("true"), .NewFFLayout("true")) d_ff_1 (
    .clk(CLK), .D(EX_URET), .Q(d_ff_1_q));  // open: Qn, preset, en, reset
  Hex_Digit_Display hex_digit_display_4 (.value(LedData[19:16]));  // open: dp
  Hex_Digit_Display hex_digit_display_5 (.value(LedData[15:12]));  // open: dp
  Multiplexer #(.select(1), .width(32), .disabled("Z"), .enable("false")) multiplexer_2 (
    .in0(\返回地址 ), .in1(multiplexer_3_out), .out(multiplexer_2_out), .sel(not_1_out));
  Multiplexer #(.select(1), .width(32), .disabled("Z"), .enable("false")) multiplexer_3 (
    .in0(\IF_PC_前 ), .in1(INT_PC), .out(multiplexer_3_out), .sel(INT));
  not not_1 (not_1_out, EX_URET);
  D_Flip_Flop #(.trigger("rising"), .Pre_Clr_Positions("LEGACY"), .NegatePresetClear("false"), .enable("true"), .NewFFLayout("false")) d_ff_2 (
    .clk(IRA), .D(1'b1), .Q(d_ff_2_q), .reset(d_ff_5_q));  // open: Qn, preset, en
  D_Flip_Flop #(.trigger("rising"), .Pre_Clr_Positions("LEGACY"), .NegatePresetClear("false"), .enable("true"), .NewFFLayout("false")) d_ff_3 (
    .clk(IRB), .D(1'b1), .Q(d_ff_3_q), .reset(d_ff_6_q));  // open: Qn, preset, en
  D_Flip_Flop #(.trigger("rising"), .Pre_Clr_Positions("LEGACY"), .NegatePresetClear("false"), .enable("true"), .NewFFLayout("false")) d_ff_4 (
    .clk(IRC), .D(1'b1), .Q(d_ff_4_q), .reset(d_ff_7_q));  // open: Qn, preset, en
  Multiplexer #(.select(1), .width(32), .disabled("Z"), .enable("false")) multiplexer_4 (
    .in0(ID_PC), .in1(IF_PC), .out(multiplexer_4_out), .sel(d_ff_1_q));
  Hex_Digit_Display hex_digit_display_6 (.value(LedData[11:8]));  // open: dp
  Hex_Digit_Display hex_digit_display_7 (.value(LedData[7:4]));  // open: dp
  // Probe on EX_PC[19:0]
  // RiscV_Probe riscv_probe_3: pin names not known; wires that end beside it: EX_IR
  // Probe on IF_PC
  \重定向处理逻辑  \u_重定向处理逻辑_1  (
    .rs1_rs(ID_IR[19:15]), .rs2_rt(ID_IR[24:20]), .rs1_used(\单周期硬布线控制器_1_rs1_use ), .EX_rd(EX_rd),
    .EX_MemToReg(id_ex_1_memtoreg_2), .rs2_used(\单周期硬布线控制器_1_rs2_use ), .MEM_rd(MEM_rd),
    .BranchTaken(BranchTaken), .rs1forward(\重定向处理逻辑_1_rs1forward ), .rs2forward(\重定向处理逻辑_1_rs2forward ),
    .stall(stall), .flush(\重定向处理逻辑_1_flush ), .ecall(ID_ecall), .EX_RegWrite(EX_RegWrite),
    .MEM_RegWrite(ex_mem_1_regwrite_2));
  and and_1 (and_1_out, ~halt, ~stall);  // AND_Gate
  // Probe on multiplexer_2_out
  Register #(.width(32), .trigger("rising"), .Select("low")) PC (
    .D(multiplexer_2_out), .en(and_1_out), .Q(IF_PC), .clk(CLK), .clr(RST));
  or or_4 (or_4_out, d_ff_2_q, d_ff_5_q);
  or or_5 (or_5_out, d_ff_3_q, d_ff_6_q);
  or or_6 (or_6_out, d_ff_4_q, d_ff_7_q);
  Hex_Digit_Display hex_digit_display_8 (.value(LedData[3:0]));  // open: dp
  and and_2 (and_2_out, or_4_out, ~IRA_RST);  // AND_Gate
  and and_3 (and_3_out, or_5_out, ~IRB_RST);  // AND_Gate
  and and_4 (and_4_out, or_6_out, ~IRC_RST);  // AND_Gate
  Multiplexer #(.select(1), .width(32), .disabled("Z"), .enable("false")) multiplexer_5 (
    .in0(multiplexer_4_out), .in1(\IF_PC_前 ), .out(\断点地址 ), .sel(BranchTaken));
  // Probe on \总周期数 
  // Probe on M_PC[19:0]
  // RiscV_Probe riscv_probe_4: pin names not known; wires that end beside it: MEM_IR
  or or_7 (BranchTaken, EX_B, EX_JALR, EX_JAL);
  D_Flip_Flop #(.trigger("rising"), .Pre_Clr_Positions("LEGACY"), .NegatePresetClear("false"), .enable("true"), .NewFFLayout("false")) d_ff_5 (
    .clk(CLK), .D(and_2_out), .Q(d_ff_5_q));  // open: Qn, preset, en, reset
  D_Flip_Flop #(.trigger("rising"), .Pre_Clr_Positions("LEGACY"), .NegatePresetClear("false"), .enable("true"), .NewFFLayout("false")) d_ff_6 (
    .clk(CLK), .D(and_3_out), .Q(d_ff_6_q));  // open: Qn, preset, en, reset
  D_Flip_Flop #(.trigger("rising"), .Pre_Clr_Positions("LEGACY"), .NegatePresetClear("false"), .enable("true"), .NewFFLayout("false")) d_ff_7 (
    .clk(CLK), .D(and_4_out), .Q(d_ff_7_q));  // open: Qn, preset, en, reset
  // Probe on \总周期数 
  // Probe on \无条件分支数 
  // Probe on \条件分支成功数 
  // Probe on \插入气泡数 
  // Probe on \LoadUse次数 
  ROM #(.addrWidth(10), .dataWidth(32), .Select("high")) rom_1 (.addr(IF_PC[11:2]), .data(IF_IR));
  Adder #(.width(32)) adder_1 (.a(IF_PC), .b(32'h4), .out(IF_PC_4));  // open: cin, cout
  and and_5 (and_5_out, ~halt, ~stall);  // AND_Gate
  // Probe on IF_PC[11:0]
  // Probe on WB_PC[19:0]
  // RiscV_Probe riscv_probe_5: pin names not known; wires that end beside it: WB_IR
  or or_8 (or_8_out, BranchTaken, \中断flush );
  IF_ID if_id_1 (
    .IR(IF_IR), .PC_4(IF_PC_4), .IR_2(ID_IR), .PC_4_2(ID_PC_4), .reset(RST), .BranchTaken(or_8_out),
    .en(and_5_out), .clk(CLK), .PC(IF_PC), .PC_2(ID_PC));  // open: PredictJump, PredictJump_2
  Priority_Encoder #(.select(2), .disabled("Z")) priority_encoder_2 (
    .in0(1'b0), .in1(d_ff_5_q), .in2(d_ff_6_q), .in3(d_ff_7_q), .out(priority_encoder_2_out), .gs(INT_IR),
    .en_in(1'b1));  // open: en_out
  // Probe on ID_PC[11:0]
  // Probe on EX_PC[11:0]
  Multiplexer #(.select(2), .width(32), .disabled("Z"), .enable("false")) multiplexer_6 (
    .in1(32'h30ac), .in2(32'h3150), .in3(32'h31f4), .out(INT_PC), .sel(priority_encoder_2_out));  // open: in0
  and and_6 (and_6_out, INT_IR, INT_IE);
  Register #(.width(1), .trigger("falling"), .Select("low")) register_1 (
    .D(and_6_out), .Q(INT), .clk(CLK));  // open: en, clr
  // Probe on M_PC[11:0]
  D_Flip_Flop #(.trigger("high"), .Pre_Clr_Positions("LEGACY"), .NegatePresetClear("false"), .enable("true"), .NewFFLayout("false")) d_ff_8 (.Q(d_ff_8_q));  // open: clk, D, Qn, preset, en, reset
  // Probe on 13'he
  Multiplexer #(.select(1), .width(12), .disabled("Z"), .enable("false")) multiplexer_7 (
    .in0(ID_IR[31:20]), .in1({ID_IR[31:25], ID_IR[11:7]}), .out(multiplexer_7_out), .sel(\单周期硬布线控制器_1_s_type ));
  Register #(.width(2), .trigger("rising"), .Select("low")) register_2 (
    .D(priority_encoder_2_out), .Q(register_2_q), .clk(INT));  // open: en, clr
  // Probe on WB_PC[11:0]
  Comparator #(.width(13), .mode("twosComplement")) comparator_1 (
    .a(CNT_num), .b(13'he), .eq(comparator_1_eq), .lt(comparator_1_lt));  // open: gt
  Clock #(.highDuration(1), .lowDuration(1)) clock_1 (.out(clock_1_out));
  \单周期硬布线控制器  \u_单周期硬布线控制器_1  (
    .Funct({ID_IR[30], ID_IR[25], ID_IR[14:12]}), .OP(ID_IR[6:2]), .ALU_OP(\单周期硬布线控制器_1_alu_op ),
    .MemToReg(\单周期硬布线控制器_1_memtoreg ), .MemWrite(\单周期硬布线控制器_1_memwrite ), .ALU_SRC(\单周期硬布线控制器_1_alu_src ),
    .RegWrite(\单周期硬布线控制器_1_regwrite ), .ecall(ID_ecall), .S_type(\单周期硬布线控制器_1_s_type ), .Jalr(ID_JALR),
    .Beq(\单周期硬布线控制器_1_beq ), .JAL(ID_JAL), .Bne(\单周期硬布线控制器_1_bne ), .in_3(ID_IR[21]), .uret(ID_URET),
    .LBU(ID_LBU), .BGEU(\单周期硬布线控制器_1_bgeu ), .rs1_use(\单周期硬布线控制器_1_rs1_use ), .rs2_use(\单周期硬布线控制器_1_rs2_use ));  // open: CSRRSI, CSEECI
  Multiplexer #(.select(1), .width(5), .disabled("Z"), .enable("false")) multiplexer_8 (
    .in0(ID_IR[19:15]), .in1(5'b10001), .out(multiplexer_8_out), .sel(ID_ecall));
  Multiplexer #(.select(1), .width(5), .disabled("Z"), .enable("false")) multiplexer_9 (
    .in0(ID_IR[24:20]), .in1(5'b01010), .out(multiplexer_9_out), .sel(ID_ecall));
  assign bit_extender_1_out = {{20{multiplexer_7_out[11]}}, multiplexer_7_out};  // Bit_Extender bit_extender_1
  assign bit_extender_2_out = {{20{ID_IR[31]}}, {ID_IR[31], ID_IR[7], ID_IR[30:25], ID_IR[11:8]}};  // Bit_Extender bit_extender_2
  assign bit_extender_3_out = {{12{ID_IR[31]}}, {ID_IR[31], ID_IR[19:12], ID_IR[20], ID_IR[30:21]}};  // Bit_Extender bit_extender_3
  Decoder #(.select(2), .tristate("false"), .disabled("Z"), .enable("false")) decoder_1 (
    .out1(decoder_1_out1), .out2(decoder_1_out2), .out3(decoder_1_out3), .sel(register_2_q));  // open: out0
  and and_7 (IRC_RST, EX_URET, decoder_1_out3);
  and and_8 (IRB_RST, EX_URET, decoder_1_out2);
  and and_9 (IRA_RST, EX_URET, decoder_1_out1);
  Register #(.width(32), .trigger("rising"), .Select("low")) EPC (
    .D(\断点地址 ), .en(INT), .Q(\返回地址 ), .clk(CLK));  // open: clr
  or or_9 (\中断flush , INT, EX_URET);
  nand nand_1 (nand_1_out, d_ff_8_q, comparator_1_eq);
  Counter #(.width(13), .max('h1fff), .ongoal("stay"), .trigger("rising"), .behavior("old")) counter_1 (
    .count(comparator_1_lt), .Q(CNT_num), .clk(clock_1_out));  // open: load, D, carry, clr, preset
  assign CLK = nand_1_out ? clock_1_out : 1'bz;  // Controlled_Buffer controlled_buffer_1
  not not_2 (not_2_out, CLK);
  Regifile regifile_1 (
    .Din(RDin), .Clk(not_2_out), .R1(regifile_1_r1), .R2(regifile_1_r2), .WE(RegWrite), .W_num(WB_rd),
    .R1_num(multiplexer_8_out), .R2_num(multiplexer_9_out));
  Pull_Resistor #(.pull(1)) pull_resistor_1 (.node(CLK));
  not not_3 (not_3_out, halt);
  not not_4 (INT_IE, register_3_q);
  Register #(.width(1), .trigger("rising"), .Select("low")) register_3 (
    .D(1'b0), .en(EX_URET), .Q(register_3_q), .clk(CLK), .preset(INT));  // open: clr, cs
  or or_10 (or_10_out, \中断flush , \重定向处理逻辑_1_flush );
  ID_EX id_ex_1 (
    .Beq(\单周期硬布线控制器_1_beq ), .R1(regifile_1_r1), .Bgeu(\单周期硬布线控制器_1_bgeu ), .Bne(\单周期硬布线控制器_1_bne ),
    .R2(regifile_1_r2), .MemToReg(\单周期硬布线控制器_1_memtoreg ), .imm1(bit_extender_1_out),
    .MemWrite(\单周期硬布线控制器_1_memwrite ), .imm2(bit_extender_2_out), .RegWrite(\单周期硬布线控制器_1_regwrite ),
    .JAL(ID_JAL), .PC(ID_PC), .JALR(ID_JALR), .PC_4(ID_PC_4), .LBU(ID_LBU), .IR(ID_IR), .ecall(ID_ecall),
    .AluOP(\单周期硬布线控制器_1_alu_op ), .rd(ID_IR[11:7]), .AluSrcB(\单周期硬布线控制器_1_alu_src ), .Beq_2(id_ex_1_beq_2),
    .R1_2(EX_R1), .Bgeu_2(id_ex_1_bgeu_2), .Bne_2(id_ex_1_bne_2), .R2_2(EX_R2),
    .MemToReg_2(id_ex_1_memtoreg_2), .imm1_2(id_ex_1_imm1_2), .MemWrite_2(id_ex_1_memwrite_2),
    .imm2_2(id_ex_1_imm2_2), .RegWrite_2(EX_RegWrite), .JAL_2(EX_JAL), .PC_2(EX_PC), .JALR_2(EX_JALR),
    .PC_4_2(EX_PC_4), .LBU_2(EX_LBU), .IR_2(EX_IR), .ecall_2(EX_ecall), .AluOP_2(id_ex_1_aluop_2),
    .rd_2(EX_rd), .AluSrcB_2(id_ex_1_alusrcb_2), .reset(RST), .flush(or_10_out), .en(not_3_out), .clk(CLK),
    .imm3(bit_extender_3_out), .imm3_2(id_ex_1_imm3_2), .rs1forward(\重定向处理逻辑_1_rs1forward ),
    .rs1forward_2(EX_rs1forward), .rs2forward(\重定向处理逻辑_1_rs2forward ), .rs2forward_2(EX_rs2forward),
    .URET(ID_URET), .URET_2(EX_URET));  // open: PredictJump, Branch, PredictJump_2, Branch_2
  Counter #(.width(16), .max('hffff), .ongoal("wrap"), .trigger("rising"), .behavior("old")) counter_2 (
    .count(not_5_out), .Q(\总周期数 ), .clk(CLK), .clr(RST));  // open: load, D, carry, preset
  not not_5 (not_5_out, halt);
  and and_10 (and_10_out, not_5_out, or_11_out);
  or or_11 (or_11_out, EX_JAL, EX_JALR);
  Multiplexer #(.select(1), .width(32), .disabled("Z"), .enable("false")) multiplexer_10 (
    .in0(EX_realR2), .in1(id_ex_1_imm1_2), .out(multiplexer_10_out), .sel(id_ex_1_alusrcb_2));
  Shifter #(.width(32), .shift("ll")) shifter_1 (.in(id_ex_1_imm3_2), .\dist (5'b00001), .out(shifter_1_out));
  Shifter #(.width(32), .shift("ll")) shifter_2 (.in(id_ex_1_imm2_2), .\dist (5'b00001), .out(shifter_2_out));
  Counter #(.width(16), .max('hffff), .ongoal("wrap"), .trigger("rising"), .behavior("old")) counter_3 (
    .count(and_10_out), .Q(\无条件分支数 ), .clk(CLK), .clr(RST));  // open: load, D, carry, preset
  ALU alu_1 (
    .X(EX_realR1), .Y(multiplexer_10_out), .AluOP(id_ex_1_aluop_2), .Equal(alu_1_equal), .Result(ALU_result),
    .out_4(alu_1_out_4));  // open: Result_2, out_6
  Adder #(.width(32)) adder_2 (.a(shifter_1_out), .b(EX_PC), .out(J_PC));  // open: cin, cout
  Adder #(.width(32)) adder_3 (.a(shifter_2_out), .b(EX_PC), .out(B_PC));  // open: cin, cout
  and and_11 (and_11_out, not_5_out, EX_B);
  and and_12 (and_12_out, id_ex_1_beq_2, alu_1_equal);
  and and_13 (and_13_out, id_ex_1_bne_2, ~alu_1_equal);  // AND_Gate
  and and_14 (and_14_out, id_ex_1_bgeu_2, alu_1_out_4);
  // Probe on J_PC
  Counter #(.width(16), .max('hffff), .ongoal("wrap"), .trigger("rising"), .behavior("old")) counter_4 (
    .count(and_11_out), .Q(\条件分支成功数 ), .clk(CLK), .clr(RST));  // open: load, D, carry, preset
  or or_12 (EX_B, and_12_out, and_13_out, and_14_out);
  not not_6 (not_6_out, halt);
  and and_15 (and_15_out, not_5_out, or_13_out);
  EX_MEM ex_mem_1 (
    .MemToReg(id_ex_1_memtoreg_2), .ALU_result(ALU_result), .MemWrite(id_ex_1_memwrite_2),
    .WriteData(EX_realR2), .RegWrite(EX_RegWrite), .IR(EX_IR), .JAL(EX_JAL), .PC(EX_PC), .JALR(EX_JALR),
    .PC_4(EX_PC_4), .LBU(EX_LBU), .HALT(EX_HALT), .rd(EX_rd), .MemToReg_2(ex_mem_1_memtoreg_2),
    .ALU_result_2(MEM_ALU_result), .MemWrite_2(MemWrite), .WriteData_2(MDin),
    .RegWrite_2(ex_mem_1_regwrite_2), .IR_2(MEM_IR), .JAL_2(ex_mem_1_jal_2), .PC_2(M_PC),
    .JALR_2(ex_mem_1_jalr_2), .PC_4_2(MEM_PC_4), .LBU_2(ex_mem_1_lbu_2), .HALT_2(ex_mem_1_halt_2),
    .rd_2(MEM_rd), .reset(RST), .en(not_6_out), .clk(CLK));
  // Probe on EX_JAL
  Counter #(.width(16), .max('hffff), .ongoal("wrap"), .trigger("rising"), .behavior("old")) counter_5 (
    .count(and_15_out), .Q(\插入气泡数 ), .clk(CLK), .clr(RST));  // open: load, D, carry, preset
  or or_13 (or_13_out, BranchTaken, stall);
  // Probe on EX_realR1
  and and_16 (and_16_out, not_5_out, stall);
  Counter #(.width(16), .max('hffff), .ongoal("wrap"), .trigger("rising"), .behavior("old")) counter_6 (
    .count(and_16_out), .Q(\LoadUse次数 ), .clk(CLK), .clr(RST));  // open: load, D, carry, preset
  Comparator #(.width(32), .mode("unsigned")) comparator_2 (
    .a(EX_realR1), .b(32'ha), .eq(comparator_2_eq));  // open: gt, lt
  RAM #(.addrWidth(10), .dataWidth(32), .bus("separate"), .Select("high")) ram_1 (
    .addr(MEM_ALU_result[11:2]), .din(MDin), .data(ram_1_data), .str(MemWrite), .sel(1'b1), .clk(CLK),
    .ld(1'b1), .clr(RST));
  and and_17 (EX_HALT, comparator_2_eq, EX_ecall);
  and and_18 (and_18_out, ~comparator_2_eq, EX_ecall);  // AND_Gate
  // Probe on EX_realR2
  Multiplexer #(.select(2), .width(8), .disabled("Z"), .enable("false")) multiplexer_11 (
    .in0(ram_1_data[7:0]), .in1(ram_1_data[15:8]), .in2(ram_1_data[23:16]), .in3(ram_1_data[31:24]),
    .out(multiplexer_11_out), .sel(MEM_ALU_result[1:0]));
  Register #(.width(32), .trigger("rising"), .Select("low")) register_4 (
    .D(EX_realR2), .en(and_18_out), .Q(LedData), .clk(CLK), .clr(RST));
  assign bit_extender_4_out = {{24{1'b0}}, multiplexer_11_out};  // Bit_Extender bit_extender_4
  not not_7 (not_7_out, halt);
  MEM_WB mem_wb_1 (
    .MemToReg(ex_mem_1_memtoreg_2), .ALU_result(MEM_ALU_result), .RegWrite(ex_mem_1_regwrite_2),
    .ReadData(ram_1_data), .JAL(ex_mem_1_jal_2), .IR(MEM_IR), .JALR(ex_mem_1_jalr_2), .PC(M_PC),
    .HALT(ex_mem_1_halt_2), .PC_4(MEM_PC_4), .rd(MEM_rd), .MemToReg_2(mem_wb_1_memtoreg_2),
    .ALU_result_2(mem_wb_1_alu_result_2), .RegWrite_2(RegWrite), .ReadData_2(mem_wb_1_readdata_2),
    .JAL_2(mem_wb_1_jal_2), .IR_2(WB_IR), .JALR_2(mem_wb_1_jalr_2), .PC_2(WB_PC), .HALT_2(mem_wb_1_halt_2),
    .PC_4_2(WB_PC_4), .rd_2(WB_rd), .reset(RST), .en(not_7_out), .clk(CLK), .LBU(ex_mem_1_lbu_2),
    .LBU_2(mem_wb_1_lbu_2), .LBU_Data(bit_extender_4_out), .LBU_Data_2(mem_wb_1_lbu_data_2));
  or or_14 (or_14_out, mem_wb_1_jal_2, mem_wb_1_jalr_2);
  Priority_Encoder #(.select(2), .disabled("Z")) priority_encoder_3 (
    .in0(1'b1), .in1(mem_wb_1_memtoreg_2), .in2(mem_wb_1_lbu_2), .in3(or_14_out), .out(priority_encoder_3_out));  // open: gs, en_out, en_in
  Multiplexer #(.select(2), .width(32), .disabled("Z"), .enable("false")) multiplexer_12 (
    .in0(mem_wb_1_alu_result_2), .in1(mem_wb_1_readdata_2), .in2(mem_wb_1_lbu_data_2), .in3(WB_PC_4),
    .out(RDin), .sel(priority_encoder_3_out));
  D_Flip_Flop #(.trigger("rising"), .Pre_Clr_Positions("ABOVE_BELOW"), .NegatePresetClear("false"), .enable("true"), .NewFFLayout("true")) d_ff_9 (
    .clk(mem_wb_1_halt_2), .D(1'b1), .Q(halt), .en(1'b1), .reset(Go));  // open: Qn, preset
  // Probe on RDin
  // Probe on WB_PC_4
  Multiplexer #(.select(2), .width(32), .disabled("Z"), .enable("false")) multiplexer_13 (
    .in0(EX_R1), .in1(RDin), .in2(MEM_ALU_result), .out(EX_realR1), .sel(EX_rs1forward));  // open: in3
  Multiplexer #(.select(2), .width(32), .disabled("Z"), .enable("false")) multiplexer_14 (
    .in0(EX_R2), .in1(RDin), .in2(MEM_ALU_result), .out(EX_realR2), .sel(EX_rs2forward));  // open: in3
  // Probe on EX_rs1forward
  // Probe on EX_rs2forward

  // Other names for the same wires on the sheet: rs2[4:0] = ID_IR[24:20]; rs1[4:0] = ID_IR[19:15];
  //   MEM_PC[31:0] = M_PC; WB_RegWrite = RegWrite

  // Notes on the sheet:
  //   中断源
  //   时空图监测，可删除
  //   中断等待指示
  //   数码管输出
  //   指令存储器
  //   contents of rom_1 (hex, n*v repeats v):
  //   7d000113 100413 1f41993 41f9d993 433 c00913 800b13 140413 f47413 800293 100313 499993 89e9b3 1300533
  //   2200893 73 406282b3 fe0294e3 140413 f00f93 1f47433 1c41413 800293 100313 49d993 89e9b3 1300533
  //   2200893 73 406282b3 fe0294e3 1c45413 406b0b33 b0463 f95ff06f 2b3 fff2c293 1029293 fff2e293 500533
  //   2200893 73 f5dff06f 1112023 410113 a12023 410113 812023 410113 1312023 410113 1412023 410113 1512023
  //   410113 1612023 410113 100b13 300a13 100a93 1600433 441413 14469b3 1300533 2200893 73 fe0416e3
  //   415a0a33 fe0a10e3 ffc10113 12b03 ffc10113 12a83 ffc10113 12a03 ffc10113 12983 ffc10113 12403
  //   ffc10113 12503 ffc10113 12883 200073 1112023 410113 a12023 410113 812023 410113 1312023 410113
  //   1412023 410113 1512023 410113 1612023 410113 200b13 300a13 100a93 1600433 441413 14469b3 1300533
  //   2200893 73 fe0416e3 415a0a33 fe0a10e3 ffc10113 12b03 ffc10113 12a83 ffc10113 12a03 ffc10113 12983
  //   ffc10113 12403 ffc10113 12503 ffc10113 12883 200073 1112023 410113 a12023 410113 812023 410113
  //   1312023 410113 1412023 410113 1512023 410113 1612023 410113 300b13 300a13 100a93 1600433 441413
  //   14469b3 1300533 2200893 73 fe0416e3 415a0a33 fe0a10e3 ffc10113 12b03 ffc10113 12a83 ffc10113 12a03
  //   ffc10113 12983 ffc10113 12403 ffc10113 12503 ffc10113 12883 200073
  //   INT_IR为1说明有中断请求出现
  //   断点地址选择
  //   控制位
  //   指令字
  //   rd
  //   选择对应的中断程序地址
  //   流水调试日志用
  //   暂停节拍，不能为0
  //   rs1
  //   $a7
  //   rs2
  //   $a0
  //   B型
  //   J型
  //   戳工具置1进入计数暂停模式，ctrl+k时钟自动运行到对应节拍暂停
  //   ctrl+k关闭时钟连续运行，将控制位置零，进入单步调试模式调试
  //   中断识别
  //   可计数暂停的时钟源
  //   中断flush信号（需清空IF/ID和ID/EX）
  //   单极中断处理逻辑
  //   为方便自动评测，需要输出流水线各段保存的PC值，注意是PC不是PC+4，另外ID段寄存器写入信息，Mem段内存写入信息也要输出
  //   beq
  //   bne
  //   bgeu
  //   ALU_result
  //   WriteData
  //   ecall指令处理
  //   MemWrite
  //   即flush数
  //   这里设置为10是为了过头歌
  //   和任务书中的要求确实有出入
  //   MemToReg
  //   RegWrite
  //   JAL
  //   JALR
  //   ALU_result
  //   LBU_Data
  //   EX段重定向处理
  //   中止必须在这里进行
  //   否则第19（十进制）拍时报错
endmodule

module \BTB表  (
  input  CLK,
  input  EX_Branch,
  input  [31:0] EX_PC,
  input  EX_BranchTaken,
  input  [31:0] EX_BranchAddr,
  input  [31:0] PC,
  output PredictJump,
  output [31:0] JumpAddr
);

  wire and_1_out, and_2_out, and_3_out, and_4_out, and_5_out, and_6_out, and_7_out, and_8_out, and_25_out,
       comparator_1_eq, comparator_2_eq, comparator_3_eq, comparator_4_eq, comparator_5_eq, comparator_6_eq,
       comparator_7_eq, comparator_8_eq, comparator_9_eq, comparator_10_eq, comparator_11_eq,
       comparator_12_eq, comparator_13_eq, comparator_14_eq, comparator_15_eq, comparator_16_eq, full, L0,
       L1, L2, L3, L4, L5, L6, L7, miss, not_1_out, not_2_out, not_3_out, not_4_out, not_5_out, not_6_out,
       not_7_out, not_8_out, not_9_out, or_1_out, or_2_out, or_3_out, or_4_out, or_5_out, or_6_out, or_7_out,
       or_8_out, or_9_out, v0, v1, v2, v3, v4, v5, v6, v7, write0, write1, write2, write3, write4, write5,
       write6, write7, \行0 , \行1 , \行2 , \行3 , \行4 , \行5 , \行6 , \行7 ;
  wire [0:0] multiplexer_10_out;
  wire [1:0] multiplexer_1_out, multiplexer_2_out, multiplexer_3_out, multiplexer_4_out, multiplexer_5_out,
       multiplexer_6_out, multiplexer_7_out, multiplexer_8_out, multiplexer_9_out, multiplexer_12_out, next,
       predict0, predict1, predict2, predict3, predict4, predict5, predict6, predict7;
  wire [2:0] multiplexer_11_out, out, priority_encoder_1_out, priority_encoder_2_out, priority_encoder_3_out,
       \比较逻辑_输出最大值及其编号_1_对应编号 , \比较逻辑_输出最大值及其编号_2_对应编号 , \比较逻辑_输出最大值及其编号_3_对应编号 , \比较逻辑_输出最大值及其编号_4_对应编号 ,
       \比较逻辑_输出最大值及其编号_5_对应编号 , \比较逻辑_输出最大值及其编号_6_对应编号 ;
  wire [15:0] count0, count1, count2, count3, count4, count5, count6, count7, \比较逻辑_输出最大值及其编号_1_max ,
       \比较逻辑_输出最大值及其编号_2_max , \比较逻辑_输出最大值及其编号_3_max , \比较逻辑_输出最大值及其编号_4_max , \比较逻辑_输出最大值及其编号_5_max ,
       \比较逻辑_输出最大值及其编号_6_max ;
  wire [31:0] adder_1_out, addr0, addr1, addr2, addr3, addr4, addr5, addr6, addr7, multiplexer_13_out, tag0,
       tag1, tag2, tag3, tag4, tag5, tag6, tag7;

  Register #(.width(1), .trigger("rising"), .Select("low")) register_1 (
    .D(1'b1), .en(write0), .Q(v0), .clk(CLK));  // open: clr
  Register #(.width(1), .trigger("rising"), .Select("low")) register_2 (
    .D(1'b1), .en(write1), .Q(v1), .clk(CLK));  // open: clr
  Register #(.width(1), .trigger("rising"), .Select("low")) register_3 (
    .D(1'b1), .en(write2), .Q(v2), .clk(CLK));  // open: clr
  Register #(.width(1), .trigger("rising"), .Select("low")) register_4 (
    .D(1'b1), .en(write3), .Q(v3), .clk(CLK));  // open: clr
  Register #(.width(1), .trigger("rising"), .Select("low")) register_5 (
    .D(1'b1), .en(write4), .Q(v4), .clk(CLK));  // open: clr
  Register #(.width(1), .trigger("rising"), .Select("low")) register_6 (
    .D(1'b1), .en(write5), .Q(v5), .clk(CLK));  // open: clr
  Register #(.width(1), .trigger("rising"), .Select("low")) register_7 (
    .D(1'b1), .en(write6), .Q(v6), .clk(CLK));  // open: clr
  Register #(.width(1), .trigger("rising"), .Select("low")) register_8 (
    .D(1'b1), .en(write7), .Q(v7), .clk(CLK));  // open: clr
  Register #(.width(32), .trigger("rising"), .Select("low")) register_9 (
    .D(EX_PC), .en(write0), .Q(tag0), .clk(CLK));  // open: clr
  Register #(.width(32), .trigger("rising"), .Select("low")) register_10 (
    .D(EX_PC), .en(write1), .Q(tag1), .clk(CLK));  // open: clr
  Register #(.width(32), .trigger("rising"), .Select("low")) register_11 (
    .D(EX_PC), .en(write2), .Q(tag2), .clk(CLK));  // open: clr
  Register #(.width(32), .trigger("rising"), .Select("low")) register_12 (
    .D(EX_PC), .en(write3), .Q(tag3), .clk(CLK));  // open: clr
  Register #(.width(32), .trigger("rising"), .Select("low")) register_13 (
    .D(EX_PC), .en(write4), .Q(tag4), .clk(CLK));  // open: clr
  Register #(.width(32), .trigger("rising"), .Select("low")) register_14 (
    .D(EX_PC), .en(write5), .Q(tag5), .clk(CLK));  // open: clr
  Register #(.width(32), .trigger("rising"), .Select("low")) register_15 (
    .D(EX_PC), .en(write6), .Q(tag6), .clk(CLK));  // open: clr
  Register #(.width(32), .trigger("rising"), .Select("low")) register_16 (
    .D(EX_PC), .en(write7), .Q(tag7), .clk(CLK));  // open: clr
  Register #(.width(32), .trigger("rising"), .Select("low")) register_17 (
    .D(EX_BranchAddr), .en(write0), .Q(addr0), .clk(CLK));  // open: clr
  Register #(.width(32), .trigger("rising"), .Select("low")) register_18 (
    .D(EX_BranchAddr), .en(write1), .Q(addr1), .clk(CLK));  // open: clr
  Register #(.width(32), .trigger("rising"), .Select("low")) register_19 (
    .D(EX_BranchAddr), .en(write2), .Q(addr2), .clk(CLK));  // open: clr
  Register #(.width(32), .trigger("rising"), .Select("low")) register_20 (
    .D(EX_BranchAddr), .en(write3), .Q(addr3), .clk(CLK));  // open: clr
  Register #(.width(32), .trigger("rising"), .Select("low")) register_21 (
    .D(EX_BranchAddr), .en(write4), .Q(addr4), .clk(CLK));  // open: clr
  Register #(.width(32), .trigger("rising"), .Select("low")) register_22 (
    .D(EX_BranchAddr), .en(write5), .Q(addr5), .clk(CLK));  // open: clr
  Register #(.width(32), .trigger("rising"), .Select("low")) register_23 (
    .D(EX_BranchAddr), .en(write6), .Q(addr6), .clk(CLK));  // open: clr
  Register #(.width(32), .trigger("rising"), .Select("low")) register_24 (
    .D(EX_BranchAddr), .en(write7), .Q(addr7), .clk(CLK));  // open: clr
  Multiplexer #(.select(1), .width(2), .disabled("Z"), .enable("false")) multiplexer_1 (
    .in0(2'b01), .in1(2'b10), .out(multiplexer_1_out), .sel(EX_BranchTaken));
  Multiplexer #(.select(1), .width(2), .disabled("Z"), .enable("false")) multiplexer_2 (
    .in0(next), .in1(multiplexer_1_out), .out(multiplexer_2_out), .sel(write0));
  Multiplexer #(.select(1), .width(2), .disabled("Z"), .enable("false")) multiplexer_3 (
    .in0(next), .in1(multiplexer_1_out), .out(multiplexer_3_out), .sel(write1));
  Multiplexer #(.select(1), .width(2), .disabled("Z"), .enable("false")) multiplexer_4 (
    .in0(next), .in1(multiplexer_1_out), .out(multiplexer_4_out), .sel(write2));
  Multiplexer #(.select(1), .width(2), .disabled("Z"), .enable("false")) multiplexer_5 (
    .in0(next), .in1(multiplexer_1_out), .out(multiplexer_5_out), .sel(write3));
  Multiplexer #(.select(1), .width(2), .disabled("Z"), .enable("false")) multiplexer_6 (
    .in0(next), .in1(multiplexer_1_out), .out(multiplexer_6_out), .sel(write4));
  Multiplexer #(.select(1), .width(2), .disabled("Z"), .enable("false")) multiplexer_7 (
    .in0(next), .in1(multiplexer_1_out), .out(multiplexer_7_out), .sel(write5));
  Multiplexer #(.select(1), .width(2), .disabled("Z"), .enable("false")) multiplexer_8 (
    .in0(next), .in1(multiplexer_1_out), .out(multiplexer_8_out), .sel(write6));
  Multiplexer #(.select(1), .width(2), .disabled("Z"), .enable("false")) multiplexer_9 (
    .in0(next), .in1(multiplexer_1_out), .out(multiplexer_9_out), .sel(write7));
  and and_1 (and_1_out, \行0 , EX_Branch);
  and and_2 (and_2_out, \行1 , EX_Branch);
  and and_3 (and_3_out, \行2 , EX_Branch);
  and and_4 (and_4_out, \行3 , EX_Branch);
  and and_5 (and_5_out, \行4 , EX_Branch);
  and and_6 (and_6_out, \行5 , EX_Branch);
  and and_7 (and_7_out, \行6 , EX_Branch);
  and and_8 (and_8_out, \行7 , EX_Branch);
  Register #(.width(2), .trigger("rising"), .Select("low")) register_25 (
    .D(multiplexer_2_out), .en(and_1_out), .Q(predict0), .clk(CLK));  // open: clr
  Register #(.width(2), .trigger("rising"), .Select("low")) register_26 (
    .D(multiplexer_3_out), .en(and_2_out), .Q(predict1), .clk(CLK));  // open: clr
  Register #(.width(2), .trigger("rising"), .Select("low")) register_27 (
    .D(multiplexer_4_out), .en(and_3_out), .Q(predict2), .clk(CLK));  // open: clr
  Register #(.width(2), .trigger("rising"), .Select("low")) register_28 (
    .D(multiplexer_5_out), .en(and_4_out), .Q(predict3), .clk(CLK));  // open: clr
  Register #(.width(2), .trigger("rising"), .Select("low")) register_29 (
    .D(multiplexer_6_out), .en(and_5_out), .Q(predict4), .clk(CLK));  // open: clr
  Register #(.width(2), .trigger("rising"), .Select("low")) register_30 (
    .D(multiplexer_7_out), .en(and_6_out), .Q(predict5), .clk(CLK));  // open: clr
  Register #(.width(2), .trigger("rising"), .Select("low")) register_31 (
    .D(multiplexer_8_out), .en(and_7_out), .Q(predict6), .clk(CLK));  // open: clr
  Register #(.width(2), .trigger("rising"), .Select("low")) register_32 (
    .D(multiplexer_9_out), .en(and_8_out), .Q(predict7), .clk(CLK));  // open: clr
  \比较逻辑_输出最大值及其编号  \u_比较逻辑_输出最大值及其编号_1  (
    .A(count0), .B(count1), .\B编号 (3'b001), .\A编号 (3'b000), .MAX(\比较逻辑_输出最大值及其编号_1_max ),
    .\对应编号 (\比较逻辑_输出最大值及其编号_1_对应编号 ));
  \比较逻辑_输出最大值及其编号  \u_比较逻辑_输出最大值及其编号_2  (
    .A(count2), .B(count3), .\B编号 (3'b011), .\A编号 (3'b010), .MAX(\比较逻辑_输出最大值及其编号_2_max ),
    .\对应编号 (\比较逻辑_输出最大值及其编号_2_对应编号 ));
  \比较逻辑_输出最大值及其编号  \u_比较逻辑_输出最大值及其编号_3  (
    .A(count4), .B(count5), .\B编号 (3'b101), .\A编号 (3'b100), .MAX(\比较逻辑_输出最大值及其编号_3_max ),
    .\对应编号 (\比较逻辑_输出最大值及其编号_3_对应编号 ));
  \比较逻辑_输出最大值及其编号  \u_比较逻辑_输出最大值及其编号_4  (
    .A(count6), .B(count7), .\B编号 (3'b111), .\A编号 (3'b110), .MAX(\比较逻辑_输出最大值及其编号_4_max ),
    .\对应编号 (\比较逻辑_输出最大值及其编号_4_对应编号 ));
  Counter #(.width(16), .max('hffff), .ongoal("wrap"), .trigger("rising"), .behavior("new")) counter_1 (
    .load(or_1_out), .D({16{1'b0}}), .Q(count0), .clk(CLK));  // open: count, carry, clr, preset, down
  or or_1 (or_1_out, L0, write0);
  Counter #(.width(16), .max('hffff), .ongoal("wrap"), .trigger("rising"), .behavior("new")) counter_2 (
    .load(or_2_out), .D({16{1'b0}}), .Q(count1), .clk(CLK));  // open: count, carry, clr, preset, down
  or or_2 (or_2_out, L1, write1);
  Counter #(.width(16), .max('hffff), .ongoal("wrap"), .trigger("rising"), .behavior("new")) counter_3 (
    .load(or_3_out), .D({16{1'b0}}), .Q(count2), .clk(CLK));  // open: count, carry, clr, preset, down
  or or_3 (or_3_out, L2, write2);
  Counter #(.width(16), .max('hffff), .ongoal("wrap"), .trigger("rising"), .behavior("new")) counter_4 (
    .load(or_4_out), .D({16{1'b0}}), .Q(count3), .clk(CLK));  // open: count, carry, clr, preset, down
  or or_4 (or_4_out, L3, write3);
  Counter #(.width(16), .max('hffff), .ongoal("wrap"), .trigger("rising"), .behavior("new")) counter_5 (
    .load(or_5_out), .D({16{1'b0}}), .Q(count4), .clk(CLK));  // open: count, carry, clr, preset, down
  or or_5 (or_5_out, L4, write4);
  Counter #(.width(16), .max('hffff), .ongoal("wrap"), .trigger("rising"), .behavior("new")) counter_6 (
    .load(or_6_out), .D({16{1'b0}}), .Q(count5), .clk(CLK));  // open: count, carry, clr, preset, down
  or or_6 (or_6_out, L5, write5);
  Counter #(.width(16), .max('hffff), .ongoal("wrap"), .trigger("rising"), .behavior("new")) counter_7 (
    .load(or_7_out), .D({16{1'b0}}), .Q(count6), .clk(CLK));  // open: count, carry, clr, preset, down
  or or_7 (or_7_out, L6, write6);
  Counter #(.width(16), .max('hffff), .ongoal("wrap"), .trigger("rising"), .behavior("new")) counter_8 (
    .load(or_8_out), .D({16{1'b0}}), .Q(count7), .clk(CLK));  // open: count, carry, clr, preset, down
  or or_8 (or_8_out, L7, write7);
  \比较逻辑_输出最大值及其编号  \u_比较逻辑_输出最大值及其编号_5  (
    .A(\比较逻辑_输出最大值及其编号_1_max ), .B(\比较逻辑_输出最大值及其编号_2_max ), .\B编号 (\比较逻辑_输出最大值及其编号_2_对应编号 ),
    .\A编号 (\比较逻辑_输出最大值及其编号_1_对应编号 ), .MAX(\比较逻辑_输出最大值及其编号_5_max ), .\对应编号 (\比较逻辑_输出最大值及其编号_5_对应编号 ));
  \比较逻辑_输出最大值及其编号  \u_比较逻辑_输出最大值及其编号_6  (
    .A(\比较逻辑_输出最大值及其编号_3_max ), .B(\比较逻辑_输出最大值及其编号_4_max ), .\B编号 (\比较逻辑_输出最大值及其编号_4_对应编号 ),
    .\A编号 (\比较逻辑_输出最大值及其编号_3_对应编号 ), .MAX(\比较逻辑_输出最大值及其编号_6_max ), .\对应编号 (\比较逻辑_输出最大值及其编号_6_对应编号 ));
  \比较逻辑_输出最大值及其编号  \u_比较逻辑_输出最大值及其编号_7  (
    .A(\比较逻辑_输出最大值及其编号_5_max ), .B(\比较逻辑_输出最大值及其编号_6_max ), .\B编号 (\比较逻辑_输出最大值及其编号_6_对应编号 ),
    .\A编号 (\比较逻辑_输出最大值及其编号_5_对应编号 ), .\对应编号 (out));  // open: MAX
  Comparator #(.width(32), .mode("unsigned")) comparator_1 (.a(tag0), .b(PC), .eq(comparator_1_eq));  // open: gt, lt
  Comparator #(.width(32), .mode("unsigned")) comparator_2 (.a(tag1), .b(PC), .eq(comparator_2_eq));  // open: gt, lt
  Comparator #(.width(32), .mode("unsigned")) comparator_3 (.a(tag2), .b(PC), .eq(comparator_3_eq));  // open: gt, lt
  Comparator #(.width(32), .mode("unsigned")) comparator_4 (.a(tag3), .b(PC), .eq(comparator_4_eq));  // open: gt, lt
  Comparator #(.width(32), .mode("unsigned")) comparator_5 (.a(tag4), .b(PC), .eq(comparator_5_eq));  // open: gt, lt
  Comparator #(.width(32), .mode("unsigned")) comparator_6 (.a(tag5), .b(PC), .eq(comparator_6_eq));  // open: gt, lt
  Comparator #(.width(32), .mode("unsigned")) comparator_7 (.a(tag6), .b(PC), .eq(comparator_7_eq));  // open: gt, lt
  Comparator #(.width(32), .mode("unsigned")) comparator_8 (.a(tag7), .b(PC), .eq(comparator_8_eq));  // open: gt, lt
  and and_9 (L0, comparator_1_eq, v0);
  and and_10 (L1, comparator_2_eq, v1);
  and and_11 (L2, comparator_3_eq, v2);
  and and_12 (L3, comparator_4_eq, v3);
  and and_13 (L4, comparator_5_eq, v4);
  and and_14 (L5, comparator_6_eq, v5);
  and and_15 (L6, comparator_7_eq, v6);
  and and_16 (L7, comparator_8_eq, v7);
  Comparator #(.width(32), .mode("unsigned")) comparator_9 (.a(tag0), .b(EX_PC), .eq(comparator_9_eq));  // open: gt, lt
  Comparator #(.width(32), .mode("unsigned")) comparator_10 (
    .a(tag1), .b(EX_PC), .eq(comparator_10_eq));  // open: gt, lt
  Comparator #(.width(32), .mode("unsigned")) comparator_11 (
    .a(tag2), .b(EX_PC), .eq(comparator_11_eq));  // open: gt, lt
  Comparator #(.width(32), .mode("unsigned")) comparator_12 (
    .a(tag3), .b(EX_PC), .eq(comparator_12_eq));  // open: gt, lt
  Comparator #(.width(32), .mode("unsigned")) comparator_13 (
    .a(tag4), .b(EX_PC), .eq(comparator_13_eq));  // open: gt, lt
  Comparator #(.width(32), .mode("unsigned")) comparator_14 (
    .a(tag5), .b(EX_PC), .eq(comparator_14_eq));  // open: gt, lt
  Comparator #(.width(32), .mode("unsigned")) comparator_15 (
    .a(tag6), .b(EX_PC), .eq(comparator_15_eq));  // open: gt, lt
  Comparator #(.width(32), .mode("unsigned")) comparator_16 (
    .a(tag7), .b(EX_PC), .eq(comparator_16_eq));  // open: gt, lt
  and and_17 (\行0 , comparator_9_eq, v0);
  and and_18 (\行1 , comparator_10_eq, v1);
  and and_19 (\行2 , comparator_11_eq, v2);
  and and_20 (\行3 , comparator_12_eq, v3);
  and and_21 (\行4 , comparator_13_eq, v4);
  and and_22 (\行5 , comparator_14_eq, v5);
  and and_23 (\行6 , comparator_15_eq, v6);
  and and_24 (\行7 , comparator_16_eq, v7);
  Priority_Encoder #(.select(3), .disabled("Z")) priority_encoder_1 (
    .in0(L0), .in1(L1), .in2(L2), .in3(L3), .in4(L4), .in5(L5), .in6(L6), .in7(L7),
    .out(priority_encoder_1_out), .en_in(1'b1));  // open: gs, en_out
  Multiplexer #(.select(3), .width(2), .disabled("Z"), .enable("false")) multiplexer_10 (
    .in0(predict0), .in1(predict1), .in2(predict2), .in3(predict3), .in4(predict4), .in5(predict5),
    .in6(predict6), .in7(predict7), .out({PredictJump, multiplexer_10_out[0]}), .sel(priority_encoder_1_out));
  Pull_Resistor #(.pull(0)) pull_resistor_1 (.node(PredictJump));
  not not_1 (not_1_out, v0);
  not not_2 (not_2_out, v1);
  not not_3 (not_3_out, v2);
  not not_4 (not_4_out, v3);
  Priority_Encoder #(.select(3), .disabled("Z")) priority_encoder_2 (
    .in0(not_1_out), .in1(not_2_out), .in2(not_3_out), .in3(not_4_out), .in4(not_5_out), .in5(not_6_out),
    .in6(not_7_out), .in7(not_8_out), .out(priority_encoder_2_out), .en_out(full), .en_in(1'b1));  // open: gs
  not not_5 (not_5_out, v4);
  not not_6 (not_6_out, v5);
  not not_7 (not_7_out, v6);
  not not_8 (not_8_out, v7);
  or or_9 (or_9_out, \行0 , \行1 , \行2 , \行3 , \行4 , \行5 , \行6 , \行7 );
  Priority_Encoder #(.select(3), .disabled("Z")) priority_encoder_3 (
    .in0(\行0 ), .in1(\行1 ), .in2(\行2 ), .in3(\行3 ), .in4(\行4 ), .in5(\行5 ), .in6(\行6 ), .in7(\行7 ),
    .out(priority_encoder_3_out), .en_in(1'b1));  // open: gs, en_out
  Pull_Resistor #(.pull(0)) pull_resistor_2 (.node(priority_encoder_3_out));
  not not_9 (not_9_out, PredictJump);
  Multiplexer #(.select(1), .width(3), .disabled("Z"), .enable("false")) multiplexer_11 (
    .in0(priority_encoder_2_out), .in1(out), .out(multiplexer_11_out), .sel(full));
  not not_10 (miss, or_9_out);
  Multiplexer #(.select(3), .width(2), .disabled("Z"), .enable("false")) multiplexer_12 (
    .in0(predict0), .in1(predict1), .in2(predict2), .in3(predict3), .in4(predict4), .in5(predict5),
    .in6(predict6), .in7(predict7), .out(multiplexer_12_out), .sel(priority_encoder_3_out));
  Multiplexer #(.select(3), .width(32), .disabled("Z"), .enable("false")) multiplexer_13 (
    .in0(addr0), .in1(addr1), .in2(addr2), .in3(addr3), .in4(addr4), .in5(addr5), .in6(addr6), .in7(addr7),
    .out(multiplexer_13_out), .sel(priority_encoder_1_out));
  Multiplexer #(.select(1), .width(32), .disabled("Z"), .enable("false")) multiplexer_14 (
    .in0(multiplexer_13_out), .in1(adder_1_out), .out(JumpAddr), .sel(not_9_out));
  Demultiplexer #(.select(3), .width(1), .tristate("false"), .disabled("Z"), .enable("false")) demultiplexer_1 (
    .out0(write0), .out1(write1), .out2(write2), .out3(write3), .out4(write4), .out5(write5), .out6(write6),
    .out7(write7), .in(and_25_out), .sel(multiplexer_11_out));
  and and_25 (and_25_out, EX_Branch, miss);
  FSM fsm_1 (.x(multiplexer_12_out[1]), .y(multiplexer_12_out[0]), .j(EX_BranchTaken), .x1(next[1]), .y1(next[0]));
  Adder #(.width(32)) adder_1 (.a(PC), .b(32'h4), .out(adder_1_out));  // open: cin, cout

  // Notes on the sheet:
  //   全相联cache
  //   valid
  //   初次写入cache时，设置分支预测历史位的初值
  //   分支预测历史位
  //   计数，用于替换算法
  //   LRU计数淘汰
  //   IF阶段，全相联查找，输出PredictJump和JumpAddr
  //   EX阶段，查找成功则只需更新分支预测历史位，查找失败说明缺失，提供write信号
  //   cache满时根据替换算法求出out
  //   注：超过1位不能用电阻附0
endmodule

module FSM (
  input  x,
  input  y,
  input  j,
  output x1,
  output y1
);

  wire and_1_out, and_2_out, and_3_out, and_4_out, not_1_out, not_2_out, not_3_out, not_4_out, not_5_out;

  not not_1 (not_1_out, y);
  not not_2 (not_2_out, x);
  not not_3 (not_3_out, y);
  not not_4 (not_4_out, y);
  not not_5 (not_5_out, j);
  and and_1 (and_1_out, y, j);
  and and_2 (and_2_out, x, not_1_out);
  and and_3 (and_3_out, not_2_out, not_3_out, j);
  and and_4 (and_4_out, x, not_4_out, not_5_out);
  or or_1 (x1, and_1_out, and_2_out);
  or or_2 (y1, and_3_out, and_4_out);

  // Notes on the sheet:
  //   参考课本P277页状态转换图
endmodule

// max
module \比较逻辑_输出最大值及其编号  (
  input  [15:0] A,
  input  [15:0] B,
  input  [2:0] \B编号 ,
  input  [2:0] \A编号 ,
  output [15:0] MAX,
  output [2:0] \对应编号 
);

  wire comparator_1_eq, comparator_1_gt, or_1_out;

  Multiplexer #(.select(1), .width(3), .disabled("Z"), .enable("false")) multiplexer_1 (
    .in0(\B编号 ), .in1(\A编号 ), .out(\对应编号 ), .sel(or_1_out));
  Comparator #(.width(16), .mode("unsigned")) comparator_1 (
    .a(A), .b(B), .gt(comparator_1_gt), .eq(comparator_1_eq));  // open: lt
  Multiplexer #(.select(1), .width(16), .disabled("Z"), .enable("false")) multiplexer_2 (
    .in0(B), .in1(A), .out(MAX), .sel(or_1_out));
  or or_1 (or_1_out, comparator_1_gt, comparator_1_eq);
endmodule

module \重定向流水线_动态分支预测  (
  output RegWrite,
  output MemWrite,
  output [31:0] IF_PC,
  output [31:0] ID_PC,
  output [31:0] EX_PC,
  output [31:0] M_PC,
  output [31:0] WB_PC,
  output [31:0] RDin,
  output [31:0] MDin,
  output [31:0] LedData
);

  wire alu_1_equal, alu_1_out_4, and_2_out, and_3_out, and_4_out, and_5_out, and_6_out, and_8_out, and_9_out,
       and_10_out, and_11_out, BranchTaken, CLK, clock_1_out, comparator_1_eq, comparator_1_lt,
       comparator_2_eq, d_ff_1_q, EX_B, EX_Branch, EX_BranchTaken, EX_ecall, EX_HALT, EX_JAL, EX_JALR,
       EX_LBU, ex_mem_1_halt_2, ex_mem_1_jal_2, ex_mem_1_jalr_2, ex_mem_1_lbu_2, ex_mem_1_memtoreg_2,
       ex_mem_1_regwrite_2, EX_PredictJump, EX_RegWrite, Go, halt, ID_Branch, ID_ecall, id_ex_1_alusrcb_2,
       id_ex_1_beq_2, id_ex_1_bgeu_2, id_ex_1_bne_2, id_ex_1_memtoreg_2, id_ex_1_memwrite_2, ID_JAL, ID_JALR,
       ID_LBU, ID_PredictJump, IF_PredictJump, IR1, IR2, IR3, mem_wb_1_halt_2, mem_wb_1_jal_2,
       mem_wb_1_jalr_2, mem_wb_1_lbu_2, mem_wb_1_memtoreg_2, nand_1_out, not_1_out, not_2_out, not_3_out,
       not_4_out, not_5_out, or_3_out, or_5_out, or_6_out, PC_EN, PredictErr, RST, stall, W1, W2, W3,
       \单周期硬布线控制器_1_alu_src , \单周期硬布线控制器_1_beq , \单周期硬布线控制器_1_bgeu , \单周期硬布线控制器_1_bne ,
       \单周期硬布线控制器_1_memtoreg , \单周期硬布线控制器_1_memwrite , \单周期硬布线控制器_1_regwrite , \单周期硬布线控制器_1_rs1_use ,
       \单周期硬布线控制器_1_rs2_use , \单周期硬布线控制器_1_s_type , \重定向处理逻辑_1_flush ;
  wire [1:0] EX_rs1forward, EX_rs2forward, priority_encoder_1_out, \重定向处理逻辑_1_rs1forward ,
       \重定向处理逻辑_1_rs2forward ;
  wire [3:0] id_ex_1_aluop_2, \单周期硬布线控制器_1_alu_op ;
  wire [4:0] EX_rd, MEM_rd, multiplexer_5_out, multiplexer_6_out, WB_rd;
  wire [7:0] multiplexer_10_out;
  wire [11:0] multiplexer_4_out;
  wire [12:0] CNT_num;
  wire [15:0] \LoadUse次数 , \总周期数 , \插入气泡数 , \无条件分支数 , \条件分支成功数 ;
  wire [31:0] ALU_result, B_PC, bit_extender_1_out, bit_extender_2_out, bit_extender_3_out,
       bit_extender_4_out, EX_BranchAddr, EX_IR, EX_PC_4, EX_R1, EX_R2, EX_realR1, EX_realR2, id_ex_1_imm1_2,
       id_ex_1_imm2_2, id_ex_1_imm3_2, ID_IR, ID_PC_4, IF_IR, IF_PC_4, J_PC, JumpAddr, MEM_ALU_result,
       MEM_IR, MEM_PC_4, mem_wb_1_alu_result_2, mem_wb_1_lbu_data_2, mem_wb_1_readdata_2, multiplexer_1_out,
       multiplexer_2_out, multiplexer_3_out, multiplexer_7_out, multiplexer_9_out, ram_1_data, regifile_1_r1,
       regifile_1_r2, shifter_1_out, shifter_2_out, WB_IR, WB_PC_4;

  Button \u_总复位  (.out(RST));
  Button _1 (.out(IR1));
  Button _2 (.out(IR2));
  Button _3 (.out(IR3));
  // Probe on \总周期数 
  // Probe on \总周期数 
  Button \u_继续运行  (.out(Go));
  LED #(.active("true")) led_1 (.in(W1));
  LED #(.active("true")) led_2 (.in(W2));
  LED #(.active("true")) led_3 (.in(W3));
  Multiplexer #(.select(1), .width(32), .disabled("Z"), .enable("false")) multiplexer_1 (
    .in0(IF_PC_4), .in1(JumpAddr), .out(multiplexer_1_out), .sel(IF_PredictJump));
  Multiplexer #(.select(1), .width(32), .disabled("Z"), .enable("false")) multiplexer_2 (
    .in0(EX_PC_4), .in1(EX_BranchAddr), .out(multiplexer_2_out), .sel(EX_BranchTaken));
  Hex_Digit_Display hex_digit_display_1 (.value(LedData[31:28]));  // open: dp
  // Probe on IF_PC[19:0]
  // RiscV_Probe riscv_probe_1: pin names not known; wires that end beside it: IF_IR
  Multiplexer #(.select(1), .width(32), .disabled("Z"), .enable("false")) multiplexer_3 (
    .in0(multiplexer_1_out), .in1(multiplexer_2_out), .out(multiplexer_3_out), .sel(PredictErr));
  Hex_Digit_Display hex_digit_display_2 (.value(LedData[23:20]));  // open: dp
  Hex_Digit_Display hex_digit_display_3 (.value(LedData[27:24]));  // open: dp
  // Probe on ID_PC[19:0]
  // RiscV_Probe riscv_probe_2: pin names not known; wires that end beside it: ID_IR
  \重定向处理逻辑  \u_重定向处理逻辑_1  (
    .rs1_rs(ID_IR[19:15]), .rs2_rt(ID_IR[24:20]), .rs1_used(\单周期硬布线控制器_1_rs1_use ), .EX_rd(EX_rd),
    .EX_MemToReg(id_ex_1_memtoreg_2), .rs2_used(\单周期硬布线控制器_1_rs2_use ), .MEM_rd(MEM_rd),
    .BranchTaken(PredictErr), .rs1forward(\重定向处理逻辑_1_rs1forward ), .rs2forward(\重定向处理逻辑_1_rs2forward ),
    .stall(stall), .flush(\重定向处理逻辑_1_flush ), .ecall(ID_ecall), .EX_RegWrite(EX_RegWrite),
    .MEM_RegWrite(ex_mem_1_regwrite_2));
  and and_1 (PC_EN, ~halt, ~stall);  // AND_Gate
  Register #(.width(32), .trigger("rising"), .Select("low")) PC (
    .D(multiplexer_3_out), .en(PC_EN), .Q(IF_PC), .clk(CLK), .clr(RST));
  Hex_Digit_Display hex_digit_display_4 (.value(LedData[15:12]));  // open: dp
  Hex_Digit_Display hex_digit_display_5 (.value(LedData[19:16]));  // open: dp
  Hex_Digit_Display hex_digit_display_6 (.value(LedData[11:8]));  // open: dp
  Hex_Digit_Display hex_digit_display_7 (.value(LedData[7:4]));  // open: dp
  // Probe on EX_PC[19:0]
  // RiscV_Probe riscv_probe_3: pin names not known; wires that end beside it: EX_IR
  xor xor_1 (PredictErr, EX_BranchTaken, EX_PredictJump);
  or or_1 (EX_BranchTaken, EX_B, EX_JALR, EX_JAL);
  \BTB表  \btb表_1  (
    .CLK(CLK), .EX_Branch(EX_Branch), .EX_PC(EX_PC), .EX_BranchTaken(EX_BranchTaken),
    .EX_BranchAddr(EX_BranchAddr), .PC(IF_PC), .PredictJump(IF_PredictJump), .JumpAddr(JumpAddr));
  Hex_Digit_Display hex_digit_display_8 (.value(LedData[3:0]));  // open: dp
  ROM #(.addrWidth(10), .dataWidth(32), .Select("high")) rom_1 (.addr(IF_PC[11:2]), .data(IF_IR));
  Adder #(.width(32)) adder_1 (.a(IF_PC), .b(32'h4), .out(IF_PC_4));  // open: cin, cout
  and and_2 (and_2_out, ~halt, ~stall);  // AND_Gate
  // Probe on \总周期数 
  // Probe on M_PC[19:0]
  // RiscV_Probe riscv_probe_4: pin names not known; wires that end beside it: MEM_IR
  // Probe on EX_BranchAddr
  IF_ID if_id_1 (
    .IR(IF_IR), .PC_4(IF_PC_4), .PredictJump(IF_PredictJump), .IR_2(ID_IR), .PC_4_2(ID_PC_4),
    .PredictJump_2(ID_PredictJump), .reset(RST), .BranchTaken(PredictErr), .en(and_2_out), .clk(CLK),
    .PC(IF_PC), .PC_2(ID_PC));
  // Probe on \总周期数 
  // Probe on \无条件分支数 
  // Probe on \条件分支成功数 
  // Probe on \插入气泡数 
  // Probe on \LoadUse次数 
  or or_2 (ID_Branch, \单周期硬布线控制器_1_bne , \单周期硬布线控制器_1_bgeu , \单周期硬布线控制器_1_beq , ID_JALR, ID_JAL);
  // Probe on IF_PC[11:0]
  // Probe on WB_PC[19:0]
  // RiscV_Probe riscv_probe_5: pin names not known; wires that end beside it: WB_IR
  Multiplexer #(.select(1), .width(12), .disabled("Z"), .enable("false")) multiplexer_4 (
    .in0(ID_IR[31:20]), .in1({ID_IR[31:25], ID_IR[11:7]}), .out(multiplexer_4_out), .sel(\单周期硬布线控制器_1_s_type ));
  // Probe on EX_PC[11:0]
  // Probe on ID_PC[11:0]
  \单周期硬布线控制器  \u_单周期硬布线控制器_1  (
    .Funct({ID_IR[30], ID_IR[25], ID_IR[14:12]}), .OP(ID_IR[6:2]), .ALU_OP(\单周期硬布线控制器_1_alu_op ),
    .MemToReg(\单周期硬布线控制器_1_memtoreg ), .MemWrite(\单周期硬布线控制器_1_memwrite ), .ALU_SRC(\单周期硬布线控制器_1_alu_src ),
    .RegWrite(\单周期硬布线控制器_1_regwrite ), .ecall(ID_ecall), .S_type(\单周期硬布线控制器_1_s_type ), .Jalr(ID_JALR),
    .Beq(\单周期硬布线控制器_1_beq ), .JAL(ID_JAL), .Bne(\单周期硬布线控制器_1_bne ), .in_3(ID_IR[21]), .LBU(ID_LBU),
    .BGEU(\单周期硬布线控制器_1_bgeu ), .rs1_use(\单周期硬布线控制器_1_rs1_use ), .rs2_use(\单周期硬布线控制器_1_rs2_use ));  // open: uret, CSRRSI, CSEECI
  Multiplexer #(.select(1), .width(5), .disabled("Z"), .enable("false")) multiplexer_5 (
    .in0(ID_IR[19:15]), .in1(5'b10001), .out(multiplexer_5_out), .sel(ID_ecall));
  Multiplexer #(.select(1), .width(5), .disabled("Z"), .enable("false")) multiplexer_6 (
    .in0(ID_IR[24:20]), .in1(5'b01010), .out(multiplexer_6_out), .sel(ID_ecall));
  assign bit_extender_1_out = {{20{multiplexer_4_out[11]}}, multiplexer_4_out};  // Bit_Extender bit_extender_1
  assign bit_extender_2_out = {{20{ID_IR[31]}}, {ID_IR[31], ID_IR[7], ID_IR[30:25], ID_IR[11:8]}};  // Bit_Extender bit_extender_2
  assign bit_extender_3_out = {{12{ID_IR[31]}}, {ID_IR[31], ID_IR[19:12], ID_IR[20], ID_IR[30:21]}};  // Bit_Extender bit_extender_3
  Multiplexer #(.select(1), .width(32), .disabled("Z"), .enable("false")) multiplexer_7 (
    .in0(B_PC), .in1(J_PC), .out(multiplexer_7_out), .sel(EX_JAL));
  // Probe on M_PC[11:0]
  D_Flip_Flop #(.trigger("high"), .Pre_Clr_Positions("LEGACY"), .NegatePresetClear("false"), .enable("true"), .NewFFLayout("false")) d_ff_1 (.Q(d_ff_1_q));  // open: clk, D, Qn, preset, en, reset
  // Probe on 13'h57
  // Probe on WB_PC[11:0]
  Comparator #(.width(13), .mode("twosComplement")) comparator_1 (
    .a(CNT_num), .b(13'h57), .eq(comparator_1_eq), .lt(comparator_1_lt));  // open: gt
  Clock #(.highDuration(1), .lowDuration(1)) clock_1 (.out(clock_1_out));
  not not_1 (not_1_out, CLK);
  Regifile regifile_1 (
    .Din(RDin), .Clk(not_1_out), .R1(regifile_1_r1), .R2(regifile_1_r2), .WE(RegWrite), .W_num(WB_rd),
    .R1_num(multiplexer_5_out), .R2_num(multiplexer_6_out));
  Multiplexer #(.select(1), .width(32), .disabled("Z"), .enable("false")) multiplexer_8 (
    .in0(multiplexer_7_out), .in1(ALU_result), .out(EX_BranchAddr), .sel(EX_JALR));
  nand nand_1 (nand_1_out, d_ff_1_q, comparator_1_eq);
  Counter #(.width(13), .max('h1fff), .ongoal("stay"), .trigger("rising"), .behavior("old")) counter_1 (
    .count(comparator_1_lt), .Q(CNT_num), .clk(clock_1_out));  // open: load, D, carry, clr, preset
  not not_2 (not_2_out, halt);
  assign CLK = nand_1_out ? clock_1_out : 1'bz;  // Controlled_Buffer controlled_buffer_1
  ID_EX id_ex_1 (
    .Beq(\单周期硬布线控制器_1_beq ), .R1(regifile_1_r1), .Bgeu(\单周期硬布线控制器_1_bgeu ), .Bne(\单周期硬布线控制器_1_bne ),
    .R2(regifile_1_r2), .MemToReg(\单周期硬布线控制器_1_memtoreg ), .imm1(bit_extender_1_out),
    .MemWrite(\单周期硬布线控制器_1_memwrite ), .imm2(bit_extender_2_out), .RegWrite(\单周期硬布线控制器_1_regwrite ),
    .JAL(ID_JAL), .PC(ID_PC), .JALR(ID_JALR), .PC_4(ID_PC_4), .LBU(ID_LBU), .IR(ID_IR), .ecall(ID_ecall),
    .AluOP(\单周期硬布线控制器_1_alu_op ), .PredictJump(ID_PredictJump), .rd(ID_IR[11:7]),
    .AluSrcB(\单周期硬布线控制器_1_alu_src ), .Branch(ID_Branch), .Beq_2(id_ex_1_beq_2), .R1_2(EX_R1),
    .Bgeu_2(id_ex_1_bgeu_2), .Bne_2(id_ex_1_bne_2), .R2_2(EX_R2), .MemToReg_2(id_ex_1_memtoreg_2),
    .imm1_2(id_ex_1_imm1_2), .MemWrite_2(id_ex_1_memwrite_2), .imm2_2(id_ex_1_imm2_2),
    .RegWrite_2(EX_RegWrite), .JAL_2(EX_JAL), .PC_2(EX_PC), .JALR_2(EX_JALR), .PC_4_2(EX_PC_4),
    .LBU_2(EX_LBU), .IR_2(EX_IR), .ecall_2(EX_ecall), .AluOP_2(id_ex_1_aluop_2),
    .PredictJump_2(EX_PredictJump), .rd_2(EX_rd), .AluSrcB_2(id_ex_1_alusrcb_2), .Branch_2(EX_Branch),
    .reset(RST), .flush(\重定向处理逻辑_1_flush ), .en(not_2_out), .clk(CLK), .imm3(bit_extender_3_out),
    .imm3_2(id_ex_1_imm3_2), .rs1forward(\重定向处理逻辑_1_rs1forward ), .rs1forward_2(EX_rs1forward),
    .rs2forward(\重定向处理逻辑_1_rs2forward ), .rs2forward_2(EX_rs2forward));  // open: URET, URET_2
  Pull_Resistor #(.pull(1)) pull_resistor_1 (.node(CLK));
  Multiplexer #(.select(1), .width(32), .disabled("Z"), .enable("false")) multiplexer_9 (
    .in0(EX_realR2), .in1(id_ex_1_imm1_2), .out(multiplexer_9_out), .sel(id_ex_1_alusrcb_2));
  Shifter #(.width(32), .shift("ll")) shifter_1 (.in(id_ex_1_imm3_2), .\dist (5'b00001), .out(shifter_1_out));
  Shifter #(.width(32), .shift("ll")) shifter_2 (.in(id_ex_1_imm2_2), .\dist (5'b00001), .out(shifter_2_out));
  // Probe on EX_realR1
  Counter #(.width(16), .max('hffff), .ongoal("wrap"), .trigger("rising"), .behavior("old")) counter_2 (
    .count(not_3_out), .Q(\总周期数 ), .clk(CLK), .clr(RST));  // open: load, D, carry, preset
  not not_3 (not_3_out, halt);
  ALU alu_1 (
    .X(EX_realR1), .Y(multiplexer_9_out), .AluOP(id_ex_1_aluop_2), .Equal(alu_1_equal), .Result(ALU_result),
    .out_4(alu_1_out_4));  // open: Result_2, out_6
  Adder #(.width(32)) adder_2 (.a(shifter_1_out), .b(EX_PC), .out(J_PC));  // open: cin, cout
  Adder #(.width(32)) adder_3 (.a(shifter_2_out), .b(EX_PC), .out(B_PC));  // open: cin, cout
  and and_3 (and_3_out, not_3_out, or_3_out);
  or or_3 (or_3_out, EX_JAL, EX_JALR);
  and and_4 (and_4_out, id_ex_1_beq_2, alu_1_equal);
  and and_5 (and_5_out, id_ex_1_bne_2, ~alu_1_equal);  // AND_Gate
  and and_6 (and_6_out, id_ex_1_bgeu_2, alu_1_out_4);
  // Probe on J_PC
  Comparator #(.width(32), .mode("unsigned")) comparator_2 (
    .a(EX_realR1), .b(32'ha), .eq(comparator_2_eq));  // open: gt, lt
  Counter #(.width(16), .max('hffff), .ongoal("wrap"), .trigger("rising"), .behavior("old")) counter_3 (
    .count(and_3_out), .Q(\无条件分支数 ), .clk(CLK), .clr(RST));  // open: load, D, carry, preset
  or or_4 (EX_B, and_4_out, and_5_out, and_6_out);
  not not_4 (not_4_out, halt);
  and and_7 (EX_HALT, comparator_2_eq, EX_ecall);
  and and_8 (and_8_out, ~comparator_2_eq, EX_ecall);  // AND_Gate
  // Probe on EX_realR2
  and and_9 (and_9_out, not_3_out, EX_B);
  EX_MEM ex_mem_1 (
    .MemToReg(id_ex_1_memtoreg_2), .ALU_result(ALU_result), .MemWrite(id_ex_1_memwrite_2),
    .WriteData(EX_realR2), .RegWrite(EX_RegWrite), .IR(EX_IR), .JAL(EX_JAL), .PC(EX_PC), .JALR(EX_JALR),
    .PC_4(EX_PC_4), .LBU(EX_LBU), .HALT(EX_HALT), .rd(EX_rd), .MemToReg_2(ex_mem_1_memtoreg_2),
    .ALU_result_2(MEM_ALU_result), .MemWrite_2(MemWrite), .WriteData_2(MDin),
    .RegWrite_2(ex_mem_1_regwrite_2), .IR_2(MEM_IR), .JAL_2(ex_mem_1_jal_2), .PC_2(M_PC),
    .JALR_2(ex_mem_1_jalr_2), .PC_4_2(MEM_PC_4), .LBU_2(ex_mem_1_lbu_2), .HALT_2(ex_mem_1_halt_2),
    .rd_2(MEM_rd), .reset(RST), .en(not_4_out), .clk(CLK));
  // Probe on EX_JAL
  Register #(.width(32), .trigger("rising"), .Select("low")) register_1 (
    .D(EX_realR2), .en(and_8_out), .Q(LedData), .clk(CLK), .clr(RST));
  Counter #(.width(16), .max('hffff), .ongoal("wrap"), .trigger("rising"), .behavior("old")) counter_4 (
    .count(and_9_out), .Q(\条件分支成功数 ), .clk(CLK), .clr(RST));  // open: load, D, carry, preset
  and and_10 (and_10_out, not_3_out, or_5_out);
  Counter #(.width(16), .max('hffff), .ongoal("wrap"), .trigger("rising"), .behavior("old")) counter_5 (
    .count(and_10_out), .Q(\插入气泡数 ), .clk(CLK), .clr(RST));  // open: load, D, carry, preset
  or or_5 (or_5_out, BranchTaken, stall);
  and and_11 (and_11_out, not_3_out, stall);
  RAM #(.addrWidth(10), .dataWidth(32), .bus("separate"), .Select("high")) ram_1 (
    .addr(MEM_ALU_result[11:2]), .din(MDin), .data(ram_1_data), .str(MemWrite), .sel(1'b1), .clk(CLK),
    .ld(1'b1), .clr(RST));
  Counter #(.width(16), .max('hffff), .ongoal("wrap"), .trigger("rising"), .behavior("old")) counter_6 (
    .count(and_11_out), .Q(\LoadUse次数 ), .clk(CLK), .clr(RST));  // open: load, D, carry, preset
  Multiplexer #(.select(2), .width(8), .disabled("Z"), .enable("false")) multiplexer_10 (
    .in0(ram_1_data[7:0]), .in1(ram_1_data[15:8]), .in2(ram_1_data[23:16]), .in3(ram_1_data[31:24]),
    .out(multiplexer_10_out), .sel(MEM_ALU_result[1:0]));
  Multiplexer #(.select(2), .width(32), .disabled("Z"), .enable("false")) multiplexer_11 (
    .in0(EX_R1), .in1(RDin), .in2(MEM_ALU_result), .out(EX_realR1), .sel(EX_rs1forward));  // open: in3
  Multiplexer #(.select(2), .width(32), .disabled("Z"), .enable("false")) multiplexer_12 (
    .in0(EX_R2), .in1(RDin), .in2(MEM_ALU_result), .out(EX_realR2), .sel(EX_rs2forward));  // open: in3
  assign bit_extender_4_out = {{24{1'b0}}, multiplexer_10_out};  // Bit_Extender bit_extender_4
  not not_5 (not_5_out, halt);
  // Probe on EX_rs1forward
  // Probe on EX_rs2forward
  MEM_WB mem_wb_1 (
    .MemToReg(ex_mem_1_memtoreg_2), .ALU_result(MEM_ALU_result), .RegWrite(ex_mem_1_regwrite_2),
    .ReadData(ram_1_data), .JAL(ex_mem_1_jal_2), .IR(MEM_IR), .JALR(ex_mem_1_jalr_2), .PC(M_PC),
    .HALT(ex_mem_1_halt_2), .PC_4(MEM_PC_4), .rd(MEM_rd), .MemToReg_2(mem_wb_1_memtoreg_2),
    .ALU_result_2(mem_wb_1_alu_result_2), .RegWrite_2(RegWrite), .ReadData_2(mem_wb_1_readdata_2),
    .JAL_2(mem_wb_1_jal_2), .IR_2(WB_IR), .JALR_2(mem_wb_1_jalr_2), .PC_2(WB_PC), .HALT_2(mem_wb_1_halt_2),
    .PC_4_2(WB_PC_4), .rd_2(WB_rd), .reset(RST), .en(not_5_out), .clk(CLK), .LBU(ex_mem_1_lbu_2),
    .LBU_2(mem_wb_1_lbu_2), .LBU_Data(bit_extender_4_out), .LBU_Data_2(mem_wb_1_lbu_data_2));
  or or_6 (or_6_out, mem_wb_1_jal_2, mem_wb_1_jalr_2);
  Priority_Encoder #(.select(2), .disabled("Z")) priority_encoder_1 (
    .in0(1'b1), .in1(mem_wb_1_memtoreg_2), .in2(mem_wb_1_lbu_2), .in3(or_6_out), .out(priority_encoder_1_out));  // open: gs, en_out, en_in
  Multiplexer #(.select(2), .width(32), .disabled("Z"), .enable("false")) multiplexer_13 (
    .in0(mem_wb_1_alu_result_2), .in1(mem_wb_1_readdata_2), .in2(mem_wb_1_lbu_data_2), .in3(WB_PC_4),
    .out(RDin), .sel(priority_encoder_1_out));
  D_Flip_Flop #(.trigger("rising"), .Pre_Clr_Positions("ABOVE_BELOW"), .NegatePresetClear("false"), .enable("true"), .NewFFLayout("true")) d_ff_2 (
    .clk(mem_wb_1_halt_2), .D(1'b1), .Q(halt), .en(1'b1), .reset(Go));  // open: Qn, preset
  // Probe on RDin
  // Probe on WB_PC_4

  // Other names for the same wires on the sheet: rs2[4:0] = ID_IR[24:20]; rs1[4:0] = ID_IR[19:15];
  //   MEM_PC[31:0] = M_PC; WB_RegWrite = RegWrite

  // Notes on the sheet:
  //   中断源
  //   时空图监测，可删除
  //   中断等待指示
  //   数码管输出
  //   指令存储器
  //   注意这里较之前的重定向流水线有个小改动
  //   ID/EX的输入BranchTaken位不再是原来单纯的EX.BranchTaken，而是与EX.PredictJump异或后得到的PredictErr
  //   contents of rom_1 (hex, n*v repeats v):
  //   100493 100006f 100493 200913 300993 100006f 100493 200913 300993 100006f 100493 200913 300993
  //   100006f 100493 200913 300993 3d8000ef 100413 100493 1f49493 900533 2200893 73 24d493 48463 fedff06f
  //   900533 2200893 73 100493 249493 900533 2200893 73 48463 fedff06f 100493 1f49493 900533 2200893 73
  //   4034d493 900533 2200893 73 4044d493 900533 2200893 73 4044d493 900533 2200893 73 4044d493 900533
  //   2200893 73 4044d493 900533 2200893 73 4044d493 900533 2200893 73 4044d493 900533 2200893 73 4044d493
  //   900533 2200893 73 100413 1f41993 41f9d993 433 c00913 300b13 140413 f47413 800293 100313 499993
  //   89e9b3 1300533 2200893 73 406282b3 fe0294e3 140413 f00f93 1f47433 1c41413 800293 100313 49d993
  //   89e9b3 1300533 2200893 73 406282b3 fe0294e3 1c45413 406b0b33 b0463 f95ff06f 2b3 fff2c293 829293
  //   ff2e293 500533 2200893 73 fff00413 493 84a023 140413 448493 84a023 140413 448493 84a023 140413
  //   448493 84a023 140413 448493 84a023 140413 448493 84a023 140413 448493 84a023 140413 448493 84a023
  //   140413 448493 84a023 140413 448493 84a023 140413 448493 84a023 140413 448493 84a023 140413 448493
  //   84a023 140413 448493 84a023 140413 448493 84a023 140413 448493 84a023 140413 448493 140413 433
  //   3c00493 42983 4aa03 149a2b3 28663 134a023 1442023 ffc48493 fe9412e3 800533 2200893 73 440413 3c00493
  //   fc9416e3 a00893 73 100293 300313 800493 849493 7648493 900533 2200893 73 800e13 5494b3 6494b3 900533
  //   2200893 73 fffe0e13 fe0e14e3 a00893 73 100293 300313 800493 849493 7648493 1449493 900533 2200893 73
  //   800e13 4054d4b3 4064d4b3 900533 2200893 73 fffe0e13 fe0e14e3 a00893 73 313 1000e13 8400493 849493
  //   8348493 400913 891913 490913 849493 8248493 849493 8148493 891913 490913 891913 490913 932023
  //   12484b3 430313 fffe0e13 fe0e18e3 2000e13 313 34483 900533 2200893 73 130313 fffe0e13 fe0e14e3 a00893
  //   73 f00493 100913 409909b3 900533 2200893 73 fff48493 ff29f6e3 a00893 73 413 140413 800533 2200893 73
  //   240413 800533 2200893 73 340413 800533 2200893 73 440413 800533 2200893 73 540413 800533 2200893 73
  //   640413 800533 2200893 73 740413 800533 2200893 73 840413 800533 2200893 2200893 73 8067
  //   指令字
  //   rd
  //   rs1
  //   $a7
  //   rs2
  //   $a0
  //   B型
  //   J型
  //   控制位
  //   Beq
  //   Bgeu
  //   Bne
  //   分支预测：EX.BranchAddr的计算
  //   流水调试日志用
  //   暂停节拍，不能为0
  //   MemToReg
  //   MemWrite
  //   ALUSrcB
  //   RegWrite
  //   戳工具置1进入计数暂停模式，ctrl+k时钟自动运行到对应节拍暂停
  //   ctrl+k关闭时钟连续运行，将控制位置零，进入单步调试模式调试
  //   可计数暂停的时钟源
  //   ecall指令处理
  //   beq
  //   bne
  //   bgeu
  //   这里设置为10是为了过头歌
  //   和任务书中的要求确实有出入
  //   为方便自动评测，需要输出流水线各段保存的PC值，注意是PC不是PC+4，另外ID段寄存器写入信息，Mem段内存写入信息也要输出
  //   ALU_result
  //   WriteData
  //   MemWrite
  //   EX段重定向处理
  //   即flush数
  //   MemToReg
  //   RegWrite
  //   JAL
  //   JALR
  //   ALU_result
  //   LBU_Data
  //   中止必须在这里进行
  //   否则第19（十进制）拍时报错
endmodule

module Backend_graphics_memory (
  input  \写使能 ,
  input  [9:0] Addr,
  input  CLK,
  input  RST,
  input  [31:0] Data,
  output [31:0] \行1 ,
  output [31:0] \行9 ,
  output [31:0] \行17 ,
  output [31:0] \行25 ,
  output [31:0] \行2 ,
  output [31:0] \行10 ,
  output [31:0] \行18 ,
  output [31:0] \行26 ,
  output [31:0] \行3 ,
  output [31:0] \行11 ,
  output [31:0] \行19 ,
  output [31:0] \行27 ,
  output [31:0] \行4 ,
  output [31:0] \行12 ,
  output [31:0] \行20 ,
  output [31:0] \行28 ,
  output [31:0] \行5 ,
  output [31:0] \行13 ,
  output [31:0] \行21 ,
  output [31:0] \行29 ,
  output [31:0] \行6 ,
  output [31:0] \行14 ,
  output [31:0] \行22 ,
  output [31:0] \行30 ,
  output [31:0] \行7 ,
  output [31:0] \行15 ,
  output [31:0] \行23 ,
  output [31:0] \行31 ,
  output [31:0] \行8 ,
  output [31:0] \行16 ,
  output [31:0] \行24 ,
  output [31:0] \行32 
);

  wire and_1_out, and_2_out, and_3_out, and_4_out, and_5_out, and_6_out, and_7_out, and_8_out, and_9_out,
       and_10_out, and_11_out, and_12_out, and_13_out, and_14_out, and_15_out, and_16_out, and_17_out,
       and_18_out, and_19_out, and_20_out, and_21_out, and_22_out, and_23_out, and_24_out, and_25_out,
       and_26_out, and_27_out, and_28_out, and_29_out, and_30_out, and_31_out, and_32_out, \行1_t , \行2_t ,
       \行3_t , \行4_t , \行5_t , \行6_t , \行7_t , \行8_t , \行9_t , \行10_t , \行11_t , \行12_t , \行13_t , \行14_t ,
       \行15_t , \行16_t , \行17_t , \行18_t , \行19_t , \行20_t , \行21_t , \行22_t , \行23_t , \行24_t , \行25_t ,
       \行26_t , \行27_t , \行28_t , \行29_t , \行30_t , \行31_t , \行32_t ;

  and and_1 (and_1_out, \写使能 , \行1_t );
  and and_2 (and_2_out, \写使能 , \行2_t );
  and and_3 (and_3_out, \写使能 , \行3_t );
  and and_4 (and_4_out, \写使能 , \行4_t );
  and and_5 (and_5_out, \写使能 , \行5_t );
  and and_6 (and_6_out, \写使能 , \行6_t );
  and and_7 (and_7_out, \写使能 , \行7_t );
  and and_8 (and_8_out, \写使能 , \行8_t );
  Register #(.width(32), .trigger("rising"), .Select("low")) register_1 (
    .D(Data), .en(and_1_out), .Q(\行1 ), .clk(CLK), .clr(RST));
  Register #(.width(32), .trigger("rising"), .Select("low")) register_2 (
    .D(Data), .en(and_2_out), .Q(\行2 ), .clk(CLK), .clr(RST));
  Register #(.width(32), .trigger("rising"), .Select("low")) register_3 (
    .D(Data), .en(and_3_out), .Q(\行3 ), .clk(CLK), .clr(RST));
  Register #(.width(32), .trigger("rising"), .Select("low")) register_4 (
    .D(Data), .en(and_4_out), .Q(\行4 ), .clk(CLK), .clr(RST));
  Register #(.width(32), .trigger("rising"), .Select("low")) register_5 (
    .D(Data), .en(and_5_out), .Q(\行5 ), .clk(CLK), .clr(RST));
  Register #(.width(32), .trigger("rising"), .Select("low")) register_6 (
    .D(Data), .en(and_6_out), .Q(\行6 ), .clk(CLK), .clr(RST));
  Register #(.width(32), .trigger("rising"), .Select("low")) register_7 (
    .D(Data), .en(and_7_out), .Q(\行7 ), .clk(CLK), .clr(RST));
  Register #(.width(32), .trigger("rising"), .Select("low")) register_8 (
    .D(Data), .en(and_8_out), .Q(\行8 ), .clk(CLK), .clr(RST));
  and and_9 (and_9_out, \写使能 , \行9_t );
  and and_10 (and_10_out, \写使能 , \行10_t );
  and and_11 (and_11_out, \写使能 , \行11_t );
  and and_12 (and_12_out, \写使能 , \行12_t );
  and and_13 (and_13_out, \写使能 , \行13_t );
  and and_14 (and_14_out, \写使能 , \行14_t );
  and and_15 (and_15_out, \写使能 , \行15_t );
  and and_16 (and_16_out, \写使能 , \行16_t );
  Register #(.width(32), .trigger("rising"), .Select("low")) register_9 (
    .D(Data), .en(and_9_out), .Q(\行9 ), .clk(CLK), .clr(RST));
  Register #(.width(32), .trigger("rising"), .Select("low")) register_10 (
    .D(Data), .en(and_10_out), .Q(\行10 ), .clk(CLK), .clr(RST));
  Register #(.width(32), .trigger("rising"), .Select("low")) register_11 (
    .D(Data), .en(and_11_out), .Q(\行11 ), .clk(CLK), .clr(RST));
  Register #(.width(32), .trigger("rising"), .Select("low")) register_12 (
    .D(Data), .en(and_12_out), .Q(\行12 ), .clk(CLK), .clr(RST));
  Register #(.width(32), .trigger("rising"), .Select("low")) register_13 (
    .D(Data), .en(and_13_out), .Q(\行13 ), .clk(CLK), .clr(RST));
  Register #(.width(32), .trigger("rising"), .Select("low")) register_14 (
    .D(Data), .en(and_14_out), .Q(\行14 ), .clk(CLK), .clr(RST));
  Register #(.width(32), .trigger("rising"), .Select("low")) register_15 (
    .D(Data), .en(and_15_out), .Q(\行15 ), .clk(CLK), .clr(RST));
  Register #(.width(32), .trigger("rising"), .Select("low")) register_16 (
    .D(Data), .en(and_16_out), .Q(\行16 ), .clk(CLK), .clr(RST));
  and and_17 (and_17_out, \写使能 , \行17_t );
  and and_18 (and_18_out, \写使能 , \行18_t );
  and and_19 (and_19_out, \写使能 , \行19_t );
  and and_20 (and_20_out, \写使能 , \行20_t );
  and and_21 (and_21_out, \写使能 , \行21_t );
  and and_22 (and_22_out, \写使能 , \行22_t );
  and and_23 (and_23_out, \写使能 , \行23_t );
  and and_24 (and_24_out, \写使能 , \行24_t );
  Register #(.width(32), .trigger("rising"), .Select("low")) register_17 (
    .D(Data), .en(and_17_out), .Q(\行17 ), .clk(CLK), .clr(RST));
  Register #(.width(32), .trigger("rising"), .Select("low")) register_18 (
    .D(Data), .en(and_18_out), .Q(\行18 ), .clk(CLK), .clr(RST));
  Register #(.width(32), .trigger("rising"), .Select("low")) register_19 (
    .D(Data), .en(and_19_out), .Q(\行19 ), .clk(CLK), .clr(RST));
  Register #(.width(32), .trigger("rising"), .Select("low")) register_20 (
    .D(Data), .en(and_20_out), .Q(\行20 ), .clk(CLK), .clr(RST));
  Register #(.width(32), .trigger("rising"), .Select("low")) register_21 (
    .D(Data), .en(and_21_out), .Q(\行21 ), .clk(CLK), .clr(RST));
  Register #(.width(32), .trigger("rising"), .Select("low")) register_22 (
    .D(Data), .en(and_22_out), .Q(\行22 ), .clk(CLK), .clr(RST));
  Register #(.width(32), .trigger("rising"), .Select("low")) register_23 (
    .D(Data), .en(and_23_out), .Q(\行23 ), .clk(CLK), .clr(RST));
  Register #(.width(32), .trigger("rising"), .Select("low")) register_24 (
    .D(Data), .en(and_24_out), .Q(\行24 ), .clk(CLK), .clr(RST));
  and and_25 (and_25_out, \写使能 , \行25_t );
  and and_26 (and_26_out, \写使能 , \行26_t );
  and and_27 (and_27_out, \写使能 , \行27_t );
  and and_28 (and_28_out, \写使能 , \行28_t );
  and and_29 (and_29_out, \写使能 , \行29_t );
  and and_30 (and_30_out, \写使能 , \行30_t );
  and and_31 (and_31_out, \写使能 , \行31_t );
  and and_32 (and_32_out, \写使能 , \行32_t );
  Register #(.width(32), .trigger("rising"), .Select("low")) register_25 (
    .D(Data), .en(and_25_out), .Q(\行25 ), .clk(CLK), .clr(RST));
  Register #(.width(32), .trigger("rising"), .Select("low")) register_26 (
    .D(Data), .en(and_26_out), .Q(\行26 ), .clk(CLK), .clr(RST));
  Register #(.width(32), .trigger("rising"), .Select("low")) register_27 (
    .D(Data), .en(and_27_out), .Q(\行27 ), .clk(CLK), .clr(RST));
  Register #(.width(32), .trigger("rising"), .Select("low")) register_28 (
    .D(Data), .en(and_28_out), .Q(\行28 ), .clk(CLK), .clr(RST));
  Register #(.width(32), .trigger("rising"), .Select("low")) register_29 (
    .D(Data), .en(and_29_out), .Q(\行29 ), .clk(CLK), .clr(RST));
  Register #(.width(32), .trigger("rising"), .Select("low")) register_30 (
    .D(Data), .en(and_30_out), .Q(\行30 ), .clk(CLK), .clr(RST));
  Register #(.width(32), .trigger("rising"), .Select("low")) register_31 (
    .D(Data), .en(and_31_out), .Q(\行31 ), .clk(CLK), .clr(RST));
  Register #(.width(32), .trigger("rising"), .Select("low")) register_32 (
    .D(Data), .en(and_32_out), .Q(\行32 ), .clk(CLK), .clr(RST));
  Demultiplexer #(.select(5), .width(1), .tristate("false"), .disabled("Z"), .enable("false")) demultiplexer_1 (
    .out0(\行1_t ), .out1(\行2_t ), .out2(\行3_t ), .out3(\行4_t ), .out4(\行5_t ), .out5(\行6_t ), .out6(\行7_t ),
    .out7(\行8_t ), .out8(\行9_t ), .out9(\行10_t ), .out10(\行11_t ), .out11(\行12_t ), .out12(\行13_t ),
    .out13(\行14_t ), .out14(\行15_t ), .out15(\行16_t ), .out16(\行17_t ), .out17(\行18_t ), .out18(\行19_t ),
    .out19(\行20_t ), .out20(\行21_t ), .out21(\行22_t ), .out22(\行23_t ), .out23(\行24_t ), .out24(\行25_t ),
    .out25(\行26_t ), .out26(\行27_t ), .out27(\行28_t ), .out28(\行29_t ), .out29(\行30_t ), .out30(\行31_t ),
    .out31(\行32_t ), .in(1'b1), .sel(Addr[4:0]));
endmodule

module button_ctrl (
  input  CLK,
  input  \_1号中断 ,
  input  [2:0] target,
  input  Clear_IR,
  input  \_2号中断 ,
  input  \_3号中断 ,
  input  \_4号中断 ,
  input  \_5号中断 ,
  input  \_6号中断 ,
  input  RST,
  output \_1号中断等待指示灯 ,
  output \_2号中断等待指示灯 ,
  output \_3号中断等待指示灯 ,
  output \_4号中断等待指示灯 ,
  output IR,
  output \_5号中断等待指示灯 ,
  output [2:0] \中断号 ,
  output \_6号中断等待指示灯 
);

  wire and_1_out, and_2_out, and_3_out, and_4_out, and_5_out, and_6_out, comparator_1_eq, comparator_2_eq,
       comparator_3_eq, comparator_4_eq, comparator_5_eq, comparator_6_eq, d_ff_1_q, d_ff_2_q, d_ff_3_q,
       d_ff_4_q, d_ff_5_q, d_ff_6_q, I1, I2, I3, I4, I5, I6, or_7_out, or_8_out, or_9_out, or_10_out,
       or_11_out, or_12_out, pull_resistor_1_node, pull_resistor_2_node, pull_resistor_3_node,
       pull_resistor_4_node, pull_resistor_5_node, pull_resistor_6_node;

  D_Flip_Flop #(.trigger("rising"), .Pre_Clr_Positions("LEGACY"), .NegatePresetClear("false"), .enable("true"), .NewFFLayout("false")) d_ff_1 (
    .clk(\_1号中断 ), .D(1'b1), .Q(d_ff_1_q), .reset(I1));  // open: Qn, preset, en
  or or_1 (\_1号中断等待指示灯 , I1, d_ff_1_q);
  D_Flip_Flop #(.trigger("rising"), .Pre_Clr_Positions("LEGACY"), .NegatePresetClear("false"), .enable("true"), .NewFFLayout("false")) d_ff_2 (
    .clk(\_2号中断 ), .D(1'b1), .Q(d_ff_2_q), .reset(I2));  // open: Qn, preset, en
  or or_2 (\_2号中断等待指示灯 , I2, d_ff_2_q);
  D_Flip_Flop #(.trigger("rising"), .Pre_Clr_Positions("LEGACY"), .NegatePresetClear("false"), .enable("true"), .NewFFLayout("false")) d_ff_3 (
    .clk(\_3号中断 ), .D(1'b1), .Q(d_ff_3_q), .reset(I3));  // open: Qn, preset, en
  or or_3 (\_3号中断等待指示灯 , I3, d_ff_3_q);
  D_Flip_Flop #(.trigger("rising"), .Pre_Clr_Positions("LEGACY"), .NegatePresetClear("false"), .enable("true"), .NewFFLayout("false")) d_ff_4 (
    .clk(\_4号中断 ), .D(1'b1), .Q(d_ff_4_q), .reset(I4));  // open: Qn, preset, en
  or or_4 (\_4号中断等待指示灯 , I4, d_ff_4_q);
  D_Flip_Flop #(.trigger("rising"), .Pre_Clr_Positions("LEGACY"), .NegatePresetClear("false"), .enable("true"), .NewFFLayout("false")) d_ff_5 (
    .clk(\_5号中断 ), .D(1'b1), .Q(d_ff_5_q), .reset(I5));  // open: Qn, preset, en
  or or_5 (\_5号中断等待指示灯 , I5, d_ff_5_q);
  D_Flip_Flop #(.trigger("rising"), .Pre_Clr_Positions("LEGACY"), .NegatePresetClear("false"), .enable("true"), .NewFFLayout("false")) d_ff_6 (
    .clk(\_6号中断 ), .D(1'b1), .Q(d_ff_6_q), .reset(I6));  // open: Qn, preset, en
  or or_6 (\_6号中断等待指示灯 , I6, d_ff_6_q);
  or or_7 (or_7_out, d_ff_1_q, I1);
  and and_1 (and_1_out, or_7_out, ~pull_resistor_1_node);  // AND_Gate
  or or_8 (or_8_out, d_ff_2_q, I2);
  and and_2 (and_2_out, or_8_out, ~pull_resistor_2_node);  // AND_Gate
  or or_9 (or_9_out, d_ff_3_q, I3);
  and and_3 (and_3_out, or_9_out, ~pull_resistor_3_node);  // AND_Gate
  or or_10 (or_10_out, d_ff_4_q, I4);
  and and_4 (and_4_out, or_10_out, ~pull_resistor_4_node);  // AND_Gate
  or or_11 (or_11_out, d_ff_5_q, I5);
  and and_5 (and_5_out, or_11_out, ~pull_resistor_5_node);  // AND_Gate
  or or_12 (or_12_out, d_ff_6_q, I6);
  and and_6 (and_6_out, or_12_out, ~pull_resistor_6_node);  // AND_Gate
  D_Flip_Flop #(.trigger("rising"), .Pre_Clr_Positions("LEGACY"), .NegatePresetClear("false"), .enable("true"), .NewFFLayout("false")) IR1 (
    .clk(CLK), .D(and_1_out), .Q(I1), .reset(RST));  // open: Qn, preset, en
  D_Flip_Flop #(.trigger("rising"), .Pre_Clr_Positions("LEGACY"), .NegatePresetClear("false"), .enable("true"), .NewFFLayout("false")) IR2 (
    .clk(CLK), .D(and_2_out), .Q(I2), .reset(RST));  // open: Qn, preset, en
  D_Flip_Flop #(.trigger("rising"), .Pre_Clr_Positions("LEGACY"), .NegatePresetClear("false"), .enable("true"), .NewFFLayout("false")) IR3 (
    .clk(CLK), .D(and_3_out), .Q(I3), .reset(RST));  // open: Qn, preset, en
  D_Flip_Flop #(.trigger("rising"), .Pre_Clr_Positions("LEGACY"), .NegatePresetClear("false"), .enable("true"), .NewFFLayout("false")) IR4 (
    .clk(CLK), .D(and_4_out), .Q(I4), .reset(RST));  // open: Qn, preset, en
  D_Flip_Flop #(.trigger("rising"), .Pre_Clr_Positions("LEGACY"), .NegatePresetClear("false"), .enable("true"), .NewFFLayout("false")) IR5 (
    .clk(CLK), .D(and_5_out), .Q(I5), .reset(RST));  // open: Qn, preset, en
  D_Flip_Flop #(.trigger("rising"), .Pre_Clr_Positions("LEGACY"), .NegatePresetClear("false"), .enable("true"), .NewFFLayout("false")) IR6 (
    .clk(CLK), .D(and_6_out), .Q(I6), .reset(RST));  // open: Qn, preset, en
  Pull_Resistor #(.pull(0)) pull_resistor_1 (.node(pull_resistor_1_node));
  Pull_Resistor #(.pull(0)) pull_resistor_2 (.node(pull_resistor_2_node));
  Pull_Resistor #(.pull(0)) pull_resistor_3 (.node(pull_resistor_3_node));
  Pull_Resistor #(.pull(0)) pull_resistor_4 (.node(pull_resistor_4_node));
  Pull_Resistor #(.pull(0)) pull_resistor_5 (.node(pull_resistor_5_node));
  Pull_Resistor #(.pull(0)) pull_resistor_6 (.node(pull_resistor_6_node));
  Comparator #(.width(3), .mode("unsigned")) comparator_1 (
    .a(target), .b(3'b001), .eq(comparator_1_eq));  // open: gt, lt
  Comparator #(.width(3), .mode("unsigned")) comparator_2 (
    .a(target), .b(3'b010), .eq(comparator_2_eq));  // open: gt, lt
  Comparator #(.width(3), .mode("unsigned")) comparator_3 (
    .a(target), .b(3'b011), .eq(comparator_3_eq));  // open: gt, lt
  Comparator #(.width(3), .mode("unsigned")) comparator_4 (
    .a(target), .b(3'b100), .eq(comparator_4_eq));  // open: gt, lt
  Comparator #(.width(3), .mode("unsigned")) comparator_5 (
    .a(target), .b(3'b101), .eq(comparator_5_eq));  // open: gt, lt
  Comparator #(.width(3), .mode("unsigned")) comparator_6 (
    .a(target), .b(3'b110), .eq(comparator_6_eq));  // open: gt, lt
  assign pull_resistor_1_node = comparator_1_eq ? Clear_IR : 1'bz;  // Controlled_Buffer controlled_buffer_1
  assign pull_resistor_2_node = comparator_2_eq ? Clear_IR : 1'bz;  // Controlled_Buffer controlled_buffer_2
  assign pull_resistor_3_node = comparator_3_eq ? Clear_IR : 1'bz;  // Controlled_Buffer controlled_buffer_3
  assign pull_resistor_4_node = comparator_4_eq ? Clear_IR : 1'bz;  // Controlled_Buffer controlled_buffer_4
  assign pull_resistor_5_node = comparator_5_eq ? Clear_IR : 1'bz;  // Controlled_Buffer controlled_buffer_5
  assign pull_resistor_6_node = comparator_6_eq ? Clear_IR : 1'bz;  // Controlled_Buffer controlled_buffer_6
  or or_13 (IR, I1, I2, I3, I4, I5, I6);
  Priority_Encoder #(.select(3), .disabled("Z")) priority_encoder_1 (
    .in0(1'b1), .in1(I1), .in2(I2), .in3(I3), .in4(I4), .in5(I5), .in6(I6), .out(\中断号 ), .en_in(1'b1));  // open: in7, gs, en_out

  // Notes on the sheet:
  //   Reset 
  //   Reset 
  //   Reset 
endmodule

module Interactive_circuit (
);

  wire clock_1_out, down, left, level1_out, level2_out, level3_out, right, RST_out, up;
  wire [31:0] \core_1_行1 , \core_1_行2 , \core_1_行3 , \core_1_行4 , \core_1_行5 , \core_1_行6 , \core_1_行7 ,
       \core_1_行8 , \core_1_行9 , \core_1_行10 , \core_1_行11 , \core_1_行12 , \core_1_行13 , \core_1_行14 ,
       \core_1_行15 , \core_1_行16 , \core_1_行17 , \core_1_行18 , \core_1_行19 , \core_1_行20 , \core_1_行21 ,
       \core_1_行22 , \core_1_行23 , \core_1_行24 , \core_1_行25 , \core_1_行26 , \core_1_行27 , \core_1_行28 ,
       \core_1_行29 , \core_1_行30 , \core_1_行31 , \core_1_行32 ;

  Button \u_左  (.out(left));
  Button level1 (.out(level1_out));
  Button level2 (.out(level2_out));
  Button level3 (.out(level3_out));
  Button \u_上  (.out(up));
  Button \u_下  (.out(down));
  Button \u_右  (.out(right));
  Clock #(.highDuration(1), .lowDuration(1)) clock_1 (.out(clock_1_out));
  core core_1 (
    .in_1(clock_1_out), .IR1(level1_out), .RST(RST_out), .IR2(left), .IR3(right), .IR4(up), .IR5(down),
    .IR6(level2_out), .IR7(level3_out), .\行1 (\core_1_行1 ), .\行2 (\core_1_行2 ), .\行3 (\core_1_行3 ),
    .\行4 (\core_1_行4 ), .\行5 (\core_1_行5 ), .\行6 (\core_1_行6 ), .\行7 (\core_1_行7 ), .\行8 (\core_1_行8 ),
    .\行9 (\core_1_行9 ), .\行10 (\core_1_行10 ), .\行11 (\core_1_行11 ), .\行12 (\core_1_行12 ),
    .\行13 (\core_1_行13 ), .\行14 (\core_1_行14 ), .\行15 (\core_1_行15 ), .\行16 (\core_1_行16 ),
    .\行17 (\core_1_行17 ), .\行18 (\core_1_行18 ), .\行19 (\core_1_行19 ), .\行20 (\core_1_行20 ),
    .\行21 (\core_1_行21 ), .\行22 (\core_1_行22 ), .\行23 (\core_1_行23 ), .\行24 (\core_1_行24 ),
    .\行25 (\core_1_行25 ), .\行26 (\core_1_行26 ), .\行27 (\core_1_行27 ), .\行28 (\core_1_行28 ),
    .\行29 (\core_1_行29 ), .\行30 (\core_1_行30 ), .\行31 (\core_1_行31 ), .\行32 (\core_1_行32 ));  // open: success, out_28
  Button RST (.out(RST_out));
  DotMatrix #(.inputtype("column"), .matrixcols(32), .matrixrows(32), .persist(0), .dotshape("square")) dotmatrix_1 (
    .col0(\core_1_行1 ), .col1(\core_1_行2 ), .col2(\core_1_行3 ), .col3(\core_1_行4 ), .col4(\core_1_行5 ),
    .col5(\core_1_行6 ), .col6(\core_1_行7 ), .col7(\core_1_行8 ), .col8(\core_1_行9 ), .col9(\core_1_行10 ),
    .col10(\core_1_行11 ), .col11(\core_1_行12 ), .col12(\core_1_行13 ), .col13(\core_1_行14 ),
    .col14(\core_1_行15 ), .col15(\core_1_行16 ), .col16(\core_1_行17 ), .col17(\core_1_行18 ),
    .col18(\core_1_行19 ), .col19(\core_1_行20 ), .col20(\core_1_行21 ), .col21(\core_1_行22 ),
    .col22(\core_1_行23 ), .col23(\core_1_行24 ), .col24(\core_1_行25 ), .col25(\core_1_行26 ),
    .col26(\core_1_行27 ), .col27(\core_1_行28 ), .col28(\core_1_行29 ), .col29(\core_1_行30 ),
    .col30(\core_1_行31 ), .col31(\core_1_行32 ));
endmodule
module core (
  input  in_1,
  input  IR1,
  input  RST,
  input  IR2,
  input  IR3,
  input  IR4,
  input  IR5,
  input  IR6,
  input  IR7,
  output [31:0] \行1 ,
  output [31:0] \行2 ,
  output [31:0] \行3 ,
  output [31:0] \行4 ,
  output [31:0] \行5 ,
  output [31:0] \行6 ,
  output [31:0] \行7 ,
  output [31:0] \行8 ,
  output [31:0] \行9 ,
  output [31:0] \行10 ,
  output [31:0] \行11 ,
  output [31:0] \行12 ,
  output [31:0] \行13 ,
  output [31:0] \行14 ,
  output [31:0] \行15 ,
  output [31:0] \行16 ,
  output [31:0] \行17 ,
  output [31:0] \行18 ,
  output [2:0] out_28,
  output [31:0] \行19 ,
  output [31:0] \行20 ,
  output [31:0] \行21 ,
  output [31:0] \行22 ,
  output [31:0] \行23 ,
  output [31:0] \行24 ,
  output success,
  output [31:0] \行25 ,
  output [31:0] \行26 ,
  output [31:0] \行27 ,
  output [31:0] \行28 ,
  output [31:0] \行29 ,
  output [31:0] \行30 ,
  output [31:0] \行31 ,
  output [31:0] \行32 
);

  wire _1_out, _2_out, _3_out, alu_1_equal, alu_1_out_4, and_1_out, and_2_out, and_3_out, and_4_out,
       and_5_out, and_6_out, and_7_out, and_8_out, and_17_out, and_18_out, and_19_out, and_20_out,
       and_21_out, Beq, Bgeu, Bne, \B型 , clock_1_out, comparator_1_eq, comparator_2_eq, comparator_2_lt,
       comparator_3_lt, controlled_buffer_1_out, CSRRCI, CSRRSI, d_ff_1_q, d_ff_2_q, d_ff_3_q, d_ff_4_q,
       d_ff_5_q, d_ff_6_q, d_ff_7_q, d_ff_9_q, d_ff_10_q, d_ff_11_q, d_ff_12_q, d_ff_13_q, d_ff_14_q,
       d_ff_15_q, d_ff_16_q, decoder_1_out1, decoder_1_out2, decoder_1_out3, decoder_1_out4, decoder_1_out5,
       decoder_1_out6, decoder_1_out7, ecall, Go, INT, INT_IE, INT_IR, IRA_RST, IRB_RST, IRC_RST, IRD_RST,
       IRE_RST, IRF_RST, IRG_RST, JAL, JALR, LBU, MemToReg, MemWrite, nand_1_out, not_1_out, not_2_out,
       not_3_out, or_1_out, or_2_out, or_3_out, or_4_out, or_5_out, or_6_out, or_7_out, or_8_out, or_9_out,
       or_10_out, or_11_out, or_12_out, or_13_out, or_14_out, or_16_out, pull_resistor_1_node, register_4_q,
       RegWrite, URET, W1, W2, W3, \单周期硬布线控制器_1_alu_src , \单周期硬布线控制器_1_s_type ;
  wire [1:0] priority_encoder_1_out, priority_encoder_3_out;
  wire [2:0] register_2_q;
  wire [3:0] \单周期硬布线控制器_1_alu_op ;
  wire [4:0] multiplexer_5_out, multiplexer_6_out;
  wire [7:0] multiplexer_9_out;
  wire [9:0] ADDR;
  wire [11:0] multiplexer_7_out;
  wire [12:0] CNT_num;
  wire [15:0] \总周期数 ;
  wire [31:0] adder_1_out, adder_2_out, adder_3_out, ALU_result, and_9_out, bit_extender_1_out,
       bit_extender_2_out, bit_extender_3_out, bit_extender_4_out, INT_PC, IR, LedData, MDin,
       multiplexer_2_out, multiplexer_3_out, multiplexer_8_out, PC, R1, ram_1_data, RDin, shifter_1_out,
       shifter_2_out, \断点地址 , \返回地址 ;

  Button \u_继续运行  (.out(Go));
  Button _1 (.out(_1_out));
  Button _2 (.out(_2_out));
  Button _3 (.out(_3_out));
  LED #(.active("true")) led_1 (.in(W1));
  LED #(.active("true")) led_2 (.in(W2));
  LED #(.active("true")) led_3 (.in(W3));
  LED #(.active("true")) led_4 (.in(or_1_out));
  LED #(.active("true")) led_5 (.in(or_2_out));
  LED #(.active("true")) led_6 (.in(or_3_out));
  LED #(.active("true")) led_7 (.in(or_4_out));
  LED #(.active("true")) led_8 (.in(or_5_out));
  LED #(.active("true")) led_9 (.in(or_6_out));
  LED #(.active("true")) led_10 (.in(or_7_out));
  Hex_Digit_Display hex_digit_display_1 (.value(LedData[31:28]));  // open: dp
  Comparator #(.width(32), .mode("unsigned")) comparator_1 (.a(R1), .b(32'ha), .eq(comparator_1_eq));  // open: gt, lt
  // Probe on \返回地址 
  // Probe on \断点地址 
  or or_1 (or_1_out, d_ff_9_q, d_ff_1_q);
  or or_2 (or_2_out, d_ff_10_q, d_ff_2_q);
  or or_3 (or_3_out, d_ff_11_q, d_ff_3_q);
  or or_4 (or_4_out, d_ff_12_q, d_ff_4_q);
  or or_5 (or_5_out, d_ff_13_q, d_ff_5_q);
  or or_6 (or_6_out, d_ff_14_q, d_ff_6_q);
  or or_7 (or_7_out, d_ff_15_q, d_ff_7_q);
  Hex_Digit_Display hex_digit_display_2 (.value(LedData[23:20]));  // open: dp
  Hex_Digit_Display hex_digit_display_3 (.value(LedData[27:24]));  // open: dp
  and and_1 (and_1_out, ~comparator_1_eq, ecall);  // AND_Gate
  D_Flip_Flop #(.trigger("rising"), .Pre_Clr_Positions("LEGACY"), .NegatePresetClear("false"), .enable("true"), .NewFFLayout("false")) d_ff_1 (
    .clk(IR1), .D(1'b1), .Q(d_ff_1_q), .reset(d_ff_9_q));  // open: Qn, preset, en
  D_Flip_Flop #(.trigger("rising"), .Pre_Clr_Positions("LEGACY"), .NegatePresetClear("false"), .enable("true"), .NewFFLayout("false")) d_ff_2 (
    .clk(IR2), .D(1'b1), .Q(d_ff_2_q), .reset(d_ff_10_q));  // open: Qn, preset, en
  D_Flip_Flop #(.trigger("rising"), .Pre_Clr_Positions("LEGACY"), .NegatePresetClear("false"), .enable("true"), .NewFFLayout("false")) d_ff_3 (
    .clk(IR3), .D(1'b1), .Q(d_ff_3_q), .reset(d_ff_11_q));  // open: Qn, preset, en
  D_Flip_Flop #(.trigger("rising"), .Pre_Clr_Positions("LEGACY"), .NegatePresetClear("false"), .enable("true"), .NewFFLayout("false")) d_ff_4 (
    .clk(IR4), .D(1'b1), .Q(d_ff_4_q), .reset(d_ff_12_q));  // open: Qn, preset, en
  D_Flip_Flop #(.trigger("rising"), .Pre_Clr_Positions("LEGACY"), .NegatePresetClear("false"), .enable("true"), .NewFFLayout("false")) d_ff_5 (
    .clk(IR5), .D(1'b1), .Q(d_ff_5_q), .reset(d_ff_13_q));  // open: Qn, preset, en
  D_Flip_Flop #(.trigger("rising"), .Pre_Clr_Positions("LEGACY"), .NegatePresetClear("false"), .enable("true"), .NewFFLayout("false")) d_ff_6 (
    .clk(IR6), .D(1'b1), .Q(d_ff_6_q), .reset(d_ff_14_q));  // open: Qn, preset, en
  D_Flip_Flop #(.trigger("rising"), .Pre_Clr_Positions("LEGACY"), .NegatePresetClear("false"), .enable("true"), .NewFFLayout("false")) d_ff_7 (
    .clk(IR7), .D(1'b1), .Q(d_ff_7_q), .reset(d_ff_15_q));  // open: Qn, preset, en
  Hex_Digit_Display hex_digit_display_4 (.value(LedData[19:16]));  // open: dp
  Hex_Digit_Display hex_digit_display_5 (.value(LedData[15:12]));  // open: dp
  D_Flip_Flop #(.trigger("rising"), .Pre_Clr_Positions("ABOVE_BELOW"), .NegatePresetClear("false"), .enable("true"), .NewFFLayout("true")) d_ff_8 (
    .clk(comparator_1_eq), .D(1'b1), .en(ecall), .reset(Go));  // open: Q, Qn, preset
  Register #(.width(32), .trigger("rising"), .Select("low")) register_1 (
    .D(MDin), .en(and_1_out), .Q(LedData), .clk(in_1));  // open: clr
  // Probe on PC
  or or_8 (or_8_out, d_ff_1_q, d_ff_9_q);
  or or_9 (or_9_out, d_ff_2_q, d_ff_10_q);
  or or_10 (or_10_out, d_ff_3_q, d_ff_11_q);
  or or_11 (or_11_out, d_ff_4_q, d_ff_12_q);
  or or_12 (or_12_out, d_ff_5_q, d_ff_13_q);
  or or_13 (or_13_out, d_ff_6_q, d_ff_14_q);
  or or_14 (or_14_out, d_ff_7_q, d_ff_15_q);
  Hex_Digit_Display hex_digit_display_6 (.value(LedData[11:8]));  // open: dp
  Hex_Digit_Display hex_digit_display_7 (.value(LedData[7:4]));  // open: dp
  // Probe on \总周期数 
  and and_2 (and_2_out, or_8_out, ~IRA_RST);  // AND_Gate
  and and_3 (and_3_out, or_9_out, ~IRB_RST);  // AND_Gate
  and and_4 (and_4_out, or_10_out, ~IRC_RST);  // AND_Gate
  and and_5 (and_5_out, or_11_out, ~IRD_RST);  // AND_Gate
  and and_6 (and_6_out, or_12_out, ~IRE_RST);  // AND_Gate
  and and_7 (and_7_out, or_13_out, ~IRF_RST);  // AND_Gate
  and and_8 (and_8_out, or_14_out, ~IRG_RST);  // AND_Gate
  Hex_Digit_Display hex_digit_display_8 (.value(LedData[3:0]));  // open: dp
  Priority_Encoder #(.select(2), .disabled("Z")) priority_encoder_1 (
    .in0(1'b1), .in1(\B型 ), .in2(JAL), .in3(JALR), .out(priority_encoder_1_out));  // open: gs, en_out, en_in
  Multiplexer #(.select(2), .width(32), .disabled("Z"), .enable("false")) multiplexer_1 (
    .in0(adder_1_out), .in1(adder_2_out), .in2(adder_3_out), .in3(and_9_out), .out(\断点地址 ),
    .sel(priority_encoder_1_out));
  assign and_9_out = 32'hfffffffe & {ALU_result[31:12], ADDR, ALU_result[1:0]};  // AND_Gate and_9, 32 bits wide
  D_Flip_Flop #(.trigger("rising"), .Pre_Clr_Positions("LEGACY"), .NegatePresetClear("false"), .enable("true"), .NewFFLayout("false")) d_ff_9 (
    .clk(in_1), .D(and_2_out), .Q(d_ff_9_q));  // open: Qn, preset, en, reset
  D_Flip_Flop #(.trigger("rising"), .Pre_Clr_Positions("LEGACY"), .NegatePresetClear("false"), .enable("true"), .NewFFLayout("false")) d_ff_10 (
    .clk(in_1), .D(and_3_out), .Q(d_ff_10_q));  // open: Qn, preset, en, reset
  D_Flip_Flop #(.trigger("rising"), .Pre_Clr_Positions("LEGACY"), .NegatePresetClear("false"), .enable("true"), .NewFFLayout("false")) d_ff_11 (
    .clk(in_1), .D(and_4_out), .Q(d_ff_11_q));  // open: Qn, preset, en, reset
  D_Flip_Flop #(.trigger("rising"), .Pre_Clr_Positions("LEGACY"), .NegatePresetClear("false"), .enable("true"), .NewFFLayout("false")) d_ff_12 (
    .clk(in_1), .D(and_5_out), .Q(d_ff_12_q));  // open: Qn, preset, en, reset
  D_Flip_Flop #(.trigger("rising"), .Pre_Clr_Positions("LEGACY"), .NegatePresetClear("false"), .enable("true"), .NewFFLayout("false")) d_ff_13 (
    .clk(in_1), .D(and_6_out), .Q(d_ff_13_q));  // open: Qn, preset, en, reset
  D_Flip_Flop #(.trigger("rising"), .Pre_Clr_Positions("LEGACY"), .NegatePresetClear("false"), .enable("true"), .NewFFLayout("false")) d_ff_14 (
    .clk(in_1), .D(and_7_out), .Q(d_ff_14_q));  // open: Qn, preset, en, reset
  D_Flip_Flop #(.trigger("rising"), .Pre_Clr_Positions("LEGACY"), .NegatePresetClear("false"), .enable("true"), .NewFFLayout("false")) d_ff_15 (
    .clk(in_1), .D(and_8_out), .Q(d_ff_15_q));  // open: Qn, preset, en, reset
  Multiplexer #(.select(1), .width(32), .disabled("Z"), .enable("false")) multiplexer_2 (
    .in0(\返回地址 ), .in1(multiplexer_3_out), .out(multiplexer_2_out), .sel(not_1_out));
  Multiplexer #(.select(1), .width(32), .disabled("Z"), .enable("false")) multiplexer_3 (
    .in0(\断点地址 ), .in1(INT_PC), .out(multiplexer_3_out), .sel(INT));
  not not_1 (not_1_out, URET);
  not not_2 (not_2_out, 1'b0);
  Counter #(.width(16), .max('hffff), .ongoal("wrap"), .trigger("rising"), .behavior("new")) counter_1 (
    .count(not_2_out), .Q(\总周期数 ), .clk(in_1));  // open: load, D, carry, clr, preset, down
  Priority_Encoder #(.select(3), .disabled("Z")) priority_encoder_2 (
    .in0(1'b0), .in1(d_ff_9_q), .in2(d_ff_10_q), .in3(d_ff_11_q), .in4(d_ff_12_q), .in5(d_ff_13_q),
    .in6(d_ff_14_q), .in7(d_ff_15_q), .out(out_28), .gs(INT_IR), .en_in(1'b1));  // open: en_out
  Register #(.width(32), .trigger("rising"), .Select("low")) u_PC (
    .D(multiplexer_2_out), .en(not_3_out), .Q(PC), .clk(in_1), .clr(RST));
  not not_3 (not_3_out, 1'b0);
  Register #(.width(3), .trigger("rising"), .Select("low")) register_2 (
    .D(out_28), .Q(register_2_q), .clk(INT));  // open: en, clr
  // RiscV_Probe riscv_probe_1: pin names not known; wires that end beside it: IR
  Decoder #(.select(3), .tristate("false"), .disabled("Z"), .enable("false")) decoder_1 (
    .out1(decoder_1_out1), .out2(decoder_1_out2), .out3(decoder_1_out3), .out4(decoder_1_out4),
    .out5(decoder_1_out5), .out6(decoder_1_out6), .out7(decoder_1_out7), .sel(register_2_q));  // open: out0
  and and_10 (IRC_RST, URET, decoder_1_out3);
  and and_11 (IRB_RST, URET, decoder_1_out2);
  and and_12 (IRA_RST, URET, decoder_1_out1);
  Multiplexer #(.select(3), .width(32), .disabled("Z"), .enable("false")) multiplexer_4 (
    .in1(32'h400420), .in2(32'h400d34), .in3(32'h400d8c), .in4(32'h400de8), .in5(32'h400e3c),
    .in6(32'h400594), .in7(32'h400930), .out(INT_PC), .sel(out_28));  // open: in0
  ROM #(.addrWidth(10), .dataWidth(32), .Select("high")) rom_1 (.addr(PC[11:2]), .data(IR));
  and and_13 (IRE_RST, URET, decoder_1_out5);
  and and_14 (IRD_RST, URET, decoder_1_out4);
  and and_15 (IRF_RST, URET, decoder_1_out6);
  and and_16 (IRG_RST, URET, decoder_1_out7);
  \单周期硬布线控制器  \u_单周期硬布线控制器_1  (
    .Funct({IR[30], IR[25], IR[14:12]}), .OP(IR[6:2]), .ALU_OP(\单周期硬布线控制器_1_alu_op ), .MemToReg(MemToReg),
    .MemWrite(MemWrite), .ALU_SRC(\单周期硬布线控制器_1_alu_src ), .RegWrite(RegWrite), .ecall(ecall),
    .S_type(\单周期硬布线控制器_1_s_type ), .Jalr(JALR), .Beq(Beq), .JAL(JAL), .Bne(Bne), .in_3(IR[21]), .uret(URET),
    .LBU(LBU), .BGEU(Bgeu), .CSRRSI(CSRRSI), .CSEECI(CSRRCI));  // open: rs1_use, rs2_use
  Multiplexer #(.select(1), .width(5), .disabled("Z"), .enable("false")) multiplexer_5 (
    .in0(IR[19:15]), .in1(5'b10001), .out(multiplexer_5_out), .sel(ecall));
  Multiplexer #(.select(1), .width(5), .disabled("Z"), .enable("false")) multiplexer_6 (
    .in0(IR[24:20]), .in1(5'b01010), .out(multiplexer_6_out), .sel(ecall));
  Multiplexer #(.select(1), .width(12), .disabled("Z"), .enable("false")) multiplexer_7 (
    .in0(IR[31:20]), .in1({IR[31:25], IR[11:7]}), .out(multiplexer_7_out), .sel(\单周期硬布线控制器_1_s_type ));
  assign bit_extender_1_out = {{20{IR[31]}}, {IR[31], IR[7], IR[30:25], IR[11:8]}};  // Bit_Extender bit_extender_1
  assign bit_extender_2_out = {{12{IR[31]}}, {IR[31], IR[19:12], IR[20], IR[30:21]}};  // Bit_Extender bit_extender_2
  assign bit_extender_3_out = {{20{multiplexer_7_out[11]}}, multiplexer_7_out};  // Bit_Extender bit_extender_3
  Shifter #(.width(32), .shift("ll")) shifter_1 (.in(bit_extender_1_out), .\dist (5'b00001), .out(shifter_1_out));
  Shifter #(.width(32), .shift("ll")) shifter_2 (.in(bit_extender_2_out), .\dist (5'b00001), .out(shifter_2_out));
  and and_17 (and_17_out, INT_IR, INT_IE);
  Regifile regifile_1 (
    .Din(RDin), .Clk(in_1), .R1(R1), .R2(MDin), .WE(RegWrite), .W_num(IR[11:7]), .R1_num(multiplexer_5_out),
    .R2_num(multiplexer_6_out));
  Adder #(.width(32)) adder_1 (.a(PC), .b(32'h4), .out(adder_1_out));  // open: cin, cout
  Adder #(.width(32)) adder_2 (.a(shifter_1_out), .b(PC), .out(adder_2_out));  // open: cin, cout
  Adder #(.width(32)) adder_3 (.a(shifter_2_out), .b(PC), .out(adder_3_out));  // open: cin, cout
  Register #(.width(1), .trigger("falling"), .Select("low")) register_3 (
    .D(and_17_out), .Q(INT), .clk(in_1));  // open: en, clr
  Multiplexer #(.select(1), .width(32), .disabled("Z"), .enable("false")) multiplexer_8 (
    .in0(MDin), .in1(bit_extender_3_out), .out(multiplexer_8_out), .sel(\单周期硬布线控制器_1_alu_src ));
  Register #(.width(32), .trigger("rising"), .Select("low")) EPC (
    .D(\断点地址 ), .en(INT), .Q(\返回地址 ), .clk(in_1));  // open: clr
  D_Flip_Flop #(.trigger("high"), .Pre_Clr_Positions("LEGACY"), .NegatePresetClear("false"), .enable("true"), .NewFFLayout("false")) d_ff_16 (.Q(d_ff_16_q));  // open: clk, D, Qn, preset, en, reset
  // Probe on 13'hbc
  ALU alu_1 (
    .X(R1), .Y(multiplexer_8_out), .AluOP(\单周期硬布线控制器_1_alu_op ), .Equal(alu_1_equal),
    .Result({ALU_result[31:12], ADDR, ALU_result[1:0]}), .out_4(alu_1_out_4));  // open: Result_2, out_6
  Comparator #(.width(13), .mode("twosComplement")) comparator_2 (
    .a(CNT_num), .b(13'hbc), .eq(comparator_2_eq), .lt(comparator_2_lt));  // open: gt
  Clock #(.highDuration(1), .lowDuration(1)) clock_1 (.out(clock_1_out));
  and and_18 (and_18_out, Beq, alu_1_equal);
  and and_19 (and_19_out, Bne, ~alu_1_equal);  // AND_Gate
  and and_20 (and_20_out, Bgeu, alu_1_out_4);
  \单周期_单级中断  \u_单周期_单级中断_1  ();  // open: IR1, IR2, IR3, RegWrite, MemWrite, PC, IR, RDin, MDin, LedData
  Counter #(.width(13), .max('h1fff), .ongoal("stay"), .trigger("rising"), .behavior("old")) counter_2 (
    .count(comparator_2_lt), .Q(CNT_num), .clk(clock_1_out));  // open: load, D, carry, clr, preset
  or or_15 (\B型 , and_18_out, and_19_out, and_20_out);
  Register #(.width(1), .trigger("falling"), .Select("low")) register_4 (
    .D(1'b0), .en(URET), .Q(register_4_q), .clk(in_1), .preset(INT));  // open: clr, cs
  not not_4 (INT_IE, register_4_q);
  nand nand_1 (nand_1_out, d_ff_16_q, comparator_2_eq);
  RAM #(.addrWidth(10), .dataWidth(32), .bus("separate"), .Select("high")) ram_1 (
    .addr(ADDR), .din(MDin), .data(ram_1_data), .str(MemWrite), .sel(1'b1), .clk(in_1), .ld(1'b1), .clr(RST));
  assign controlled_buffer_1_out = nand_1_out ? clock_1_out : 1'bz;  // Controlled_Buffer controlled_buffer_1
  Pull_Resistor #(.pull(1)) pull_resistor_1 (.node(pull_resistor_1_node));
  Multiplexer #(.select(2), .width(8), .disabled("Z"), .enable("false")) multiplexer_9 (
    .in0(ram_1_data[7:0]), .in1(ram_1_data[15:8]), .in2(ram_1_data[23:16]), .in3(ram_1_data[31:24]),
    .out(multiplexer_9_out), .sel(ALU_result[1:0]));
  Priority_Encoder #(.select(2), .disabled("Z")) priority_encoder_3 (
    .in0(1'b1), .in1(MemToReg), .in2(LBU), .in3(or_16_out), .out(priority_encoder_3_out));  // open: gs, en_out, en_in
  assign bit_extender_4_out = {{24{1'b0}}, multiplexer_9_out};  // Bit_Extender bit_extender_4
  or or_16 (or_16_out, JAL, JALR);
  Multiplexer #(.select(2), .width(32), .disabled("Z"), .enable("false")) multiplexer_10 (
    .in0({ALU_result[31:12], ADDR, ALU_result[1:0]}), .in1(ram_1_data), .in2(bit_extender_4_out),
    .in3(adder_1_out), .out(RDin), .sel(priority_encoder_3_out));
  Comparator #(.width(10), .mode("unsigned")) comparator_3 (
    .a(ADDR), .b(10'h20), .lt(comparator_3_lt));  // open: gt, eq
  and and_21 (and_21_out, MemWrite, comparator_3_lt);
  Backend_graphics_memory backend_graphics_memory_1 (
    .\写使能 (and_21_out), .Addr(ADDR), .CLK(in_1), .Data(MDin), .\行1 (\行1 ), .\行9 (\行9 ), .\行17 (\行17 ),
    .\行25 (\行25 ), .\行2 (\行2 ), .\行10 (\行10 ), .\行18 (\行18 ), .\行26 (\行26 ), .\行3 (\行3 ), .\行11 (\行11 ),
    .\行19 (\行19 ), .\行27 (\行27 ), .\行4 (\行4 ), .\行12 (\行12 ), .\行20 (\行20 ), .\行28 (\行28 ), .\行5 (\行5 ),
    .\行13 (\行13 ), .\行21 (\行21 ), .\行29 (\行29 ), .\行6 (\行6 ), .\行14 (\行14 ), .\行22 (\行22 ), .\行30 (\行30 ),
    .\行7 (\行7 ), .\行15 (\行15 ), .\行23 (\行23 ), .\行31 (\行31 ), .\行8 (\行8 ), .\行16 (\行16 ), .\行24 (\行24 ),
    .\行32 (\行32 ), .RST(RST));

  // Other names for the same wires on the sheet: ALU_result[11:2] = ADDR; CLK = in_1

  // Notes on the sheet:
  //   中断源
  //   中断等待指示
  //   总复位信号应将除ROM以外所有存储组件全部清零
  //   这里设置为10是为了过头歌
  //   和任务书中的要求确实有出入
  //   数码管输出
  //   数码管输出应该用寄存器锁存，否则显示数据只能一闪而过
  //   指令探针
  //   指令存储器
  //   此寄存器必须为上升沿触发，在INT到来时即刻完成中断识别
  //   指令字
  //   contents of rom_1 (hex, n*v repeats v):
  //   913 ff06293 829293 ff2e293 829293 ff2e293 829293 ff2e293 502023 8006293 829293 202e293 829293 2e293
  //   829293 12e293 502223 bf06293 829293 af2e293 829293 802e293 829293 12e293 502423 bf06293 829293
  //   a82e293 829293 802e293 829293 1d2e293 502623 b006293 829293 282e293 829293 9f2e293 829293 d2e293
  //   502823 bf06293 829293 202e293 829293 112e293 829293 152e293 502a23 b006293 829293 2f2e293 829293
  //   912e293 829293 212e293 502c23 bf06293 829293 a02e293 829293 802e293 829293 12e293 502e23 bf06293
  //   829293 a02e293 829293 9f2e293 829293 12e293 2502023 8006293 829293 202e293 829293 42e293 829293
  //   7d2e293 2502223 bf06293 829293 a82e293 829293 842e293 829293 52e293 2502423 bf06293 829293 af2e293
  //   829293 9f2e293 829293 52e293 2502623 b206293 829293 282e293 829293 802e293 829293 12e293 2502823
  //   b206293 829293 202e293 829293 1f2e293 829293 7d2e293 2502a23 bf06293 829293 af2e293 829293 912e293
  //   829293 552e293 2502c23 bf06293 829293 a82e293 829293 9f2e293 829293 452e293 2502e23 8006293 829293
  //   282e293 829293 802e293 829293 12e293 4502023 b306293 829293 a02e293 829293 1f2e293 829293 792e293
  //   4502223 b306293 829293 af2e293 829293 912e293 829293 52e293 4502423 b506293 829293 a22e293 829293
  //   1f2e293 829293 792e293 4502623 b506293 829293 ad2e293 829293 802e293 829293 12e293 4502823 b906293
  //   829293 a02e293 829293 1d2e293 829293 7d2e293 4502a23 b906293 829293 a02e293 829293 152e293 829293
  //   552e293 4502c23 8006293 829293 282e293 829293 172e293 829293 452e293 4502e23 bf06293 829293 af2e293
  //   829293 802e293 829293 12e293 6502023 bf06293 829293 a82e293 829293 1f2e293 829293 7d2e293 6502223
  //   b506293 829293 a02e293 829293 152e293 829293 52e293 6502423 b506293 829293 af2e293 829293 912e293
  //   829293 52e293 6502623 b506293 829293 a82e293 829293 802e293 829293 12e293 6502823 b106293 829293
  //   af2e293 829293 802e293 829293 12e293 6502a23 8006293 829293 202e293 829293 2e293 829293 12e293
  //   6502c23 ff06293 829293 ff2e293 829293 ff2e293 829293 ff2e293 6502e23 100913 5*13 fe9ff0ef 16090863
  //   413 493 6293 c29293 22e293 829293 12e293 502023 6293 c29293 22e293 829293 ff2e293 502223 6293 c29293
  //   22e293 829293 802e293 502423 502623 502823 502a23 502c23 502e23 2502023 2502223 2502423 2502623
  //   706293 829293 ff2e293 829293 fe2e293 829293 802e293 2502823 4006293 c29293 2e293 829293 802e293
  //   2502a23 506293 829293 ff2e293 829293 ff2e293 829293 802e293 2502c23 5006293 c29293 2e293 829293
  //   2e293 2502e23 4502023 4502223 4502423 4502623 4502823 4502a23 4502c23 4502e23 6502023 6502223
  //   6502423 6502623 6502823 fd06293 829293 2e293 829293 2e293 829293 2e293 6502a23 1006293 c29293 2e293
  //   829293 2e293 6502c23 7f006293 c29293 2e293 829293 2e293 6502e23 100913 200073 38090c63 413 493
  //   2006293 c29293 2e293 829293 12e293 502023 7e06293 829293 ff2e293 829293 ff2e293 829293 ba2e293
  //   502223 806293 c29293 2e293 829293 6e2e293 502423 7e06293 829293 ff2e293 829293 ff2e293 829293 2e293
  //   502623 42406293 c29293 2e293 829293 7f2e293 502823 5f06293 829293 5f2e293 829293 ff2e293 829293
  //   402e293 502a23 50506293 c29293 2e293 829293 5e2e293 502c23 57506293 c29293 7ff2e293 829293 522e293
  //   502e23 52506293 c29293 102e293 829293 22e293 2502023 56f06293 c29293 7d72e293 829293 fe2e293 2502223
  //   52006293 c29293 4502e293 829293 2e293 2502423 57f06293 c29293 7572e293 829293 ff2e293 2502623
  //   50006293 c29293 5402e293 829293 2e293 2502823 57706293 c29293 57f2e293 829293 fe2e293 2502a23
  //   55506293 c29293 4002e293 829293 2e293 2502c23 15506293 c29293 7ff2e293 829293 fe2e293 2502e23
  //   f406293 829293 102e293 829293 2e293 829293 2e293 4502023 1506293 829293 ff2e293 829293 af2e293
  //   829293 ff2e293 4502223 d406293 829293 2e293 829293 a82e293 829293 2e293 4502423 d706293 829293
  //   ff2e293 829293 ab2e293 829293 fd2e293 4502623 8006293 829293 2e293 829293 aa2e293 829293 12e293
  //   4502823 bf06293 829293 fe2e293 829293 ab2e293 829293 fd2e293 4502a23 a006293 829293 2e293 829293
  //   a02e293 829293 152e293 4502c23 bf06293 829293 ff2e293 829293 af2e293 829293 d52e293 4502e23 a806293
  //   829293 2e293 829293 2d2e293 829293 552e293 6502023 8306293 829293 ef2e293 829293 e12e293 829293
  //   552e293 65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
  //   JAL
  //   JALR
  //   URET
  //   LBU
  //   $a7
  //   $a0
  //   I型（上）/sw（下）
  //   B型指令立即数
  //   J型指令立即数
  //   注意JALR是I型指令
  //   为方便自动评测，需要输出PC，IR，寄存器堆写如数据RDin
  //   Beq
  //   Bgeu
  //   Bne
  //   MemToReg
  //   MemWrite
  //   AluOP
  //   AluSrcB
  //   RegWrite
  //   S_Type
  //   RAM写使能MemWrite、RAM写入数据MDin等信号
  //   AluSrcB为1代表是lw/sw/立即数指令
  //   控制位
  //   暂停节拍，不能为0
  //   戳工具置1进入计数暂停模式，ctrl+k时钟自动运行到对应节拍暂停
  //   ctrl+k关闭时钟连续运行，将控制位置零，进入单步调试模式调试
  //   只有sw指令会往存储器存数据
  //   数据存储器
  //   可计数暂停的时钟源
  //   LBU无符号加载字节指令
endmodule
